// Logisim project lab3(改).circ as structural Verilog: 17 circuits, main circuit CNTR4U
module CNTR4U (
  input  CLK,
  input  LD,
  input  D0,
  input  CLR,
  input  D1,
  input  D2,
  input  D3,
  input  ENP,
  input  ENT,
  output Q0,
  output Q1,
  output Q2,
  output Q3,
  output RCO
);

  wire and_1_out, and_2_out, and_3_out, and_4_out, and_5_out, and_6_out, and_8_out, and_9_out, and_10_out,
       and_11_out, and_12_out, and_13_out, and_14_out, and_15_out, buffer_1_out, d_ff_1_qn, d_ff_2_qn,
       d_ff_3_qn, d_ff_4_qn, not_1_out, not_2_out, or_1_out, or_2_out, or_3_out, or_4_out, xor_1_out,
       xor_2_out, xor_3_out, xor_4_out;

  buf buffer_1 (buffer_1_out, CLR);
  not not_1 (not_1_out, CLK);
  and and_1 (and_1_out, LD, ~buffer_1_out);  // AND_Gate
  and and_2 (and_2_out, ~and_1_out, ~buffer_1_out);  // AND_Gate
  and and_3 (and_3_out, ENP, ENT);
  and and_4 (and_4_out, ~d_ff_1_qn, and_3_out);  // AND_Gate
  and and_5 (and_5_out, ~d_ff_1_qn, ~d_ff_2_qn, and_3_out);  // AND_Gate
  and and_6 (and_6_out, ~d_ff_1_qn, ~d_ff_2_qn, ~d_ff_3_qn, and_3_out);  // AND_Gate
  not not_2 (not_2_out, and_3_out);
  xor xor_1 (xor_1_out, and_3_out, ~d_ff_1_qn);  // XOR_Gate
  xor xor_2 (xor_2_out, and_4_out, ~d_ff_2_qn);  // XOR_Gate
  xor xor_3 (xor_3_out, and_5_out, ~d_ff_3_qn);  // XOR_Gate
  xor xor_4 (xor_4_out, and_6_out, ~d_ff_4_qn);  // XOR_Gate
  and and_7 (RCO, ~d_ff_1_qn, ~d_ff_2_qn, ~d_ff_3_qn, ~d_ff_4_qn, ~not_2_out);  // AND_Gate
  and and_8 (and_8_out, and_1_out, D0);
  and and_9 (and_9_out, and_2_out, xor_1_out);
  and and_10 (and_10_out, and_1_out, D1);
  and and_11 (and_11_out, and_2_out, xor_2_out);
  and and_12 (and_12_out, and_1_out, D2);
  and and_13 (and_13_out, and_2_out, xor_3_out);
  and and_14 (and_14_out, and_1_out, D3);
  and and_15 (and_15_out, and_2_out, xor_4_out);
  or or_1 (or_1_out, and_8_out, and_9_out);
  or or_2 (or_2_out, and_10_out, and_11_out);
  or or_3 (or_3_out, and_12_out, and_13_out);
  or or_4 (or_4_out, and_14_out, and_15_out);
  D_Flip_Flop d_ff_1 (.clk(not_1_out), .D(or_1_out), .Q(Q0), .Qn(d_ff_1_qn));  // open: preset, reset
  D_Flip_Flop d_ff_2 (.clk(not_1_out), .D(or_2_out), .Q(Q1), .Qn(d_ff_2_qn));  // open: preset, reset
  D_Flip_Flop d_ff_3 (.clk(not_1_out), .D(or_3_out), .Q(Q2), .Qn(d_ff_3_qn));  // open: preset, reset
  D_Flip_Flop d_ff_4 (.clk(not_1_out), .D(or_4_out), .Q(Q3), .Qn(d_ff_4_qn));  // open: preset, reset

  // Notes on the sheet:
  //   4位二进制同步计数器
endmodule

module SHRG4U (
  input  CLK,
  input  CLR,
  input  RIN,
  input  D3,
  input  D2,
  input  D1,
  input  S1,
  input  S0,
  input  D0,
  input  LIN,
  output Q3,
  output Q2,
  output Q1,
  output Q0
);

  wire _00_2_out, _00_3_out, _00_4_out, _00_out, _01_2_out, _01_3_out, _01_4_out, _01_out, _10_2_out,
       _10_3_out, _10_4_out, _10_out, _11_2_out, _11_3_out, _11_4_out, _11_out, not_1_out, not_2_out,
       not_3_out, not_4_out, not_5_out, not_6_out, not_7_out, or_1_out, or_2_out, or_3_out, or_4_out;

  not not_1 (not_1_out, CLK);
  not not_2 (not_2_out, CLR);
  not not_3 (not_3_out, S1);
  not not_4 (not_4_out, S0);
  not not_5 (not_5_out, not_2_out);
  not not_6 (not_6_out, not_3_out);
  not not_7 (not_7_out, not_4_out);
  and _10 (_10_out, ~not_3_out, RIN, ~not_7_out);  // AND_Gate
  and _00 (_00_out, ~not_6_out, Q3, ~not_7_out);  // AND_Gate
  and _11 (_11_out, ~not_3_out, D3, ~not_4_out);  // AND_Gate
  and _01 (_01_out, ~not_6_out, Q2, ~not_4_out);  // AND_Gate
  and _10_2 (_10_2_out, ~not_3_out, Q3, ~not_7_out);  // AND_Gate
  and _00_2 (_00_2_out, ~not_6_out, Q2, ~not_7_out);  // AND_Gate
  and _11_2 (_11_2_out, ~not_3_out, D2, ~not_4_out);  // AND_Gate
  and _01_2 (_01_2_out, ~not_6_out, Q1, ~not_4_out);  // AND_Gate
  and _10_3 (_10_3_out, ~not_3_out, Q2, ~not_7_out);  // AND_Gate
  and _00_3 (_00_3_out, ~not_6_out, Q1, ~not_7_out);  // AND_Gate
  and _11_3 (_11_3_out, ~not_3_out, D1, ~not_4_out);  // AND_Gate
  and _01_3 (_01_3_out, ~not_6_out, Q0, ~not_4_out);  // AND_Gate
  and _10_4 (_10_4_out, ~not_3_out, Q1, ~not_7_out);  // AND_Gate
  and _00_4 (_00_4_out, ~not_6_out, Q0, ~not_7_out);  // AND_Gate
  and _11_4 (_11_4_out, ~not_3_out, D0, ~not_4_out);  // AND_Gate
  and _01_4 (_01_4_out, ~not_6_out, LIN, ~not_4_out);  // AND_Gate
  or or_1 (or_1_out, _10_out, _00_out, _11_out, _01_out);
  or or_2 (or_2_out, _10_2_out, _00_2_out, _11_2_out, _01_2_out);
  or or_3 (or_3_out, _10_3_out, _00_3_out, _11_3_out, _01_3_out);
  or or_4 (or_4_out, _10_4_out, _00_4_out, _11_4_out, _01_4_out);
  D_Flip_Flop #(.trigger("falling"), .NegatePresetClear("true")) d_ff_1 (
    .clk(not_1_out), .D(or_1_out), .Q(Q3), .reset(not_5_out));  // open: Qn, preset
  D_Flip_Flop #(.trigger("falling"), .NegatePresetClear("true")) d_ff_2 (
    .clk(not_1_out), .D(or_2_out), .Q(Q2), .reset(not_5_out));  // open: Qn, preset
  D_Flip_Flop #(.trigger("falling"), .NegatePresetClear("true")) d_ff_3 (
    .clk(not_1_out), .D(or_3_out), .Q(Q1), .reset(not_5_out));  // open: Qn, preset
  D_Flip_Flop #(.trigger("falling"), .NegatePresetClear("true")) d_ff_4 (
    .clk(not_1_out), .D(or_4_out), .Q(Q0), .reset(not_5_out));  // open: Qn, preset
endmodule

module \随机序列  (
  input  CLR,
  input  S1,
  input  S0
);

  wire CLK_out, xor_1_out;
  wire [3:0] shrg4u_1_q0;

  xor xor_1 (xor_1_out, shrg4u_1_q0[1], shrg4u_1_q0[0]);
  Clock CLK (.out(CLK_out));
  SHRG4U shrg4u_1 (
    .D0(1'b0), .S1(S1), .S0(S0), .Q0(shrg4u_1_q0[0]), .CLK(CLK_out), .CLR(CLR), .RIN(xor_1_out),
    .Q3(shrg4u_1_q0[3]), .D3(1'b1), .Q2(shrg4u_1_q0[2]), .D2(1'b0), .Q1(shrg4u_1_q0[1]), .D1(1'b0));  // open: LIN
  Hex_Digit_Display hex_digit_display_1 (.value(shrg4u_1_q0));  // open: dp
  // Digital_Oscilloscope #(.nState(20)) 数字示波器: pin names not known; wires that end beside it: CLK_out, shrg4u_1_q0[3], shrg4u_1_q0[2], shrg4u_1_q0[1], shrg4u_1_q0[0]

  // Notes on the sheet:
  //   CLK
  //   QD
  //   QC
  //   QB
  //   QA
endmodule

module regfiles (
  input  [4:0] R1_num,
  input  [4:0] R2_num,
  input  [31:0] Din,
  input  [4:0] Write_Reg_num,
  input  Write_Enable,
  input  Clock,
  output [31:0] Reg1Out,
  output [31:0] Reg2Out
);

  wire _0_out, _1_out, _2_out, _3_out, _4_out, _5_out, _6_out, _7_out, _8_out, _9_out, _10_out, _11_out,
       _12_out, _13_out, _14_out, _15_out, _16_out, _17_out, _18_out, _19_out, _20_out, _21_out, _22_out,
       _23_out, _24_out, _25_out, _26_out, _27_out, _28_out, _29_out, _30_out, _31_out, undriven, undriven_2,
       undriven_3, undriven_4;
  wire [31:0] D0, D1, D2, D3, D4, D5, D6, D7, D8, D9, D10, D11, D12, D13, D14, D16, D17, D18, D19, D20, D21,
       D22, D23, D24, D25, D26, D27, D28, D29, D30, D31, dec;

  Decoder #(.select(5), .enable("false")) decoder_1 (
    .out0(dec[0]), .out1(dec[1]), .out2(dec[2]), .out3(dec[3]), .out4(dec[4]), .out5(dec[5]), .out6(dec[6]),
    .out7(dec[7]), .out8(dec[8]), .out9(dec[9]), .out10(dec[10]), .out11(dec[11]), .out12(dec[12]),
    .out13(dec[13]), .out14(dec[14]), .out15(dec[15]), .out16(dec[16]), .out17(dec[17]), .out18(dec[18]),
    .out19(dec[19]), .out20(dec[20]), .out21(dec[21]), .out22(dec[22]), .out23(dec[23]), .out24(dec[24]),
    .out25(dec[25]), .out26(dec[26]), .out27(dec[27]), .out28(dec[28]), .out29(dec[29]), .out30(dec[30]),
    .out31(dec[31]), .sel(Write_Reg_num));
  // Probe on Write_Reg_num
  and _0 (_0_out, dec[0], Write_Enable);
  and _1 (_1_out, dec[1], Write_Enable);
  and _2 (_2_out, dec[2], Write_Enable);
  and _3 (_3_out, dec[3], Write_Enable);
  and _4 (_4_out, dec[4], Write_Enable);
  and _5 (_5_out, dec[5], Write_Enable);
  and _6 (_6_out, dec[6], Write_Enable);
  and _7 (_7_out, dec[7], Write_Enable);
  and _8 (_8_out, dec[8], Write_Enable);
  and _9 (_9_out, dec[9], Write_Enable);
  and _10 (_10_out, dec[10], Write_Enable);
  and _11 (_11_out, dec[11], Write_Enable);
  and _12 (_12_out, dec[12], Write_Enable);
  and _13 (_13_out, dec[13], Write_Enable);
  and _14 (_14_out, dec[14], Write_Enable);
  and _15 (_15_out, dec[15], Write_Enable);
  Register #(.width(32), .Select("low")) register_1 (.D(Din), .en(_0_out), .Q(D0), .clk(Clock));  // open: clr
  Register #(.width(32), .Select("low")) register_2 (.D(Din), .en(_1_out), .Q(D1), .clk(Clock));  // open: clr
  Register #(.width(32), .Select("low")) register_3 (.D(Din), .en(_2_out), .Q(D2), .clk(Clock));  // open: clr
  Register #(.width(32), .Select("low")) register_4 (.D(Din), .en(_3_out), .Q(D3), .clk(Clock), .clr(undriven));
  Register #(.width(32), .Select("low")) register_5 (.D(Din), .en(_4_out), .Q(D4), .clk(Clock));  // open: clr
  Register #(.width(32), .Select("low")) register_6 (.D(Din), .en(_5_out), .Q(D5), .clk(Clock));  // open: clr
  Register #(.width(32), .Select("low")) register_7 (.D(Din), .en(_6_out), .Q(D6), .clk(Clock));  // open: clr
  Register #(.width(32), .Select("low")) register_8 (.D(Din), .en(_7_out), .Q(D7), .clk(Clock));  // open: clr
  Register #(.width(32), .Select("low")) register_9 (.D(Din), .en(_8_out), .Q(D8), .clk(Clock));  // open: clr
  Register #(.width(32), .Select("low")) register_10 (.D(Din), .en(_9_out), .Q(D9), .clk(Clock));  // open: clr
  Register #(.width(32), .Select("low")) register_11 (.D(Din), .en(_10_out), .Q(D10), .clk(Clock));  // open: clr
  Register #(.width(32), .Select("low")) register_12 (.D(Din), .en(_11_out), .Q(D11), .clk(Clock), .clr(undriven_2));
  Register #(.width(32), .Select("low")) register_13 (.D(Din), .en(_12_out), .Q(D12), .clk(Clock));  // open: clr
  Register #(.width(32), .Select("low")) register_14 (.D(Din), .en(_13_out), .Q(D13), .clk(Clock));  // open: clr
  Register #(.width(32), .Select("low")) register_15 (.D(Din), .en(_14_out), .Q(D14), .clk(Clock));  // open: clr
  Register #(.width(32), .Select("low")) register_16 (.D(Din), .en(_15_out), .Q(D14), .clk(Clock));  // open: clr
  and _16 (_16_out, dec[16], Write_Enable);
  and _17 (_17_out, dec[17], Write_Enable);
  and _18 (_18_out, dec[18], Write_Enable);
  and _19 (_19_out, dec[19], Write_Enable);
  and _20 (_20_out, dec[20], Write_Enable);
  and _21 (_21_out, dec[21], Write_Enable);
  and _22 (_22_out, dec[22], Write_Enable);
  and _23 (_23_out, dec[23], Write_Enable);
  and _24 (_24_out, dec[24], Write_Enable);
  and _25 (_25_out, dec[25], Write_Enable);
  and _26 (_26_out, dec[26], Write_Enable);
  and _27 (_27_out, dec[27], Write_Enable);
  and _28 (_28_out, dec[28], Write_Enable);
  and _29 (_29_out, dec[29], Write_Enable);
  and _30 (_30_out, dec[30], Write_Enable);
  and _31 (_31_out, dec[31], Write_Enable);
  Register #(.width(32), .Select("low")) register_17 (.D(Din), .en(_16_out), .Q(D16), .clk(Clock));  // open: clr
  Register #(.width(32), .Select("low")) register_18 (.D(Din), .en(_17_out), .Q(D17), .clk(Clock));  // open: clr
  Register #(.width(32), .Select("low")) register_19 (.D(Din), .en(_18_out), .Q(D18), .clk(Clock));  // open: clr
  Register #(.width(32), .Select("low")) register_20 (.D(Din), .en(_19_out), .Q(D19), .clk(Clock), .clr(undriven_3));
  Register #(.width(32), .Select("low")) register_21 (.D(Din), .en(_20_out), .Q(D20), .clk(Clock));  // open: clr
  Register #(.width(32), .Select("low")) register_22 (.D(Din), .en(_21_out), .Q(D21), .clk(Clock));  // open: clr
  Register #(.width(32), .Select("low")) register_23 (.D(Din), .en(_22_out), .Q(D22), .clk(Clock));  // open: clr
  Register #(.width(32), .Select("low")) register_24 (.D(Din), .en(_23_out), .Q(D23), .clk(Clock));  // open: clr
  Register #(.width(32), .Select("low")) register_25 (.D(Din), .en(_24_out), .Q(D24), .clk(Clock));  // open: clr
  Register #(.width(32), .Select("low")) register_26 (.D(Din), .en(_25_out), .Q(D25), .clk(Clock));  // open: clr
  Register #(.width(32), .Select("low")) register_27 (.D(Din), .en(_26_out), .Q(D26), .clk(Clock));  // open: clr
  Register #(.width(32), .Select("low")) register_28 (.D(Din), .en(_27_out), .Q(D27), .clk(Clock), .clr(undriven_4));
  Register #(.width(32), .Select("low")) register_29 (.D(Din), .en(_28_out), .Q(D28), .clk(Clock));  // open: clr
  Register #(.width(32), .Select("low")) register_30 (.D(Din), .en(_29_out), .Q(D29), .clk(Clock));  // open: clr
  Register #(.width(32), .Select("low")) register_31 (.D(Din), .en(_30_out), .Q(D30), .clk(Clock));  // open: clr
  Register #(.width(32), .Select("low")) register_32 (.D(Din), .en(_31_out), .Q(D31), .clk(Clock));  // open: clr
  Multiplexer #(.select(5), .width(32), .enable("false")) multiplexer_1 (
    .in0(D0), .in1(D1), .in2(D2), .in3(D3), .in4(D4), .in5(D5), .in6(D6), .in7(D7), .in8(D8), .in9(D9),
    .in10(D10), .in11(D11), .in12(D12), .in13(D13), .in14(D14), .in15(D14), .in16(D16), .in17(D17),
    .in18(D18), .in19(D19), .in20(D20), .in21(D21), .in22(D22), .in23(D23), .in24(D24), .in25(D25),
    .in26(D26), .in27(D27), .in28(D28), .in29(D29), .in30(D30), .in31(D31), .out(Reg1Out), .sel(R1_num));
  Multiplexer #(.select(5), .width(32), .enable("false")) multiplexer_2 (
    .in0(D0), .in1(D1), .in2(D2), .in3(D3), .in4(D4), .in5(D5), .in6(D6), .in7(D7), .in8(D8), .in9(D9),
    .in10(D10), .in11(D11), .in12(D12), .in13(D13), .in14(D14), .in15(D14), .in16(D16), .in17(D17),
    .in18(D18), .in19(D19), .in20(D20), .in21(D21), .in22(D22), .in23(D23), .in24(D24), .in25(D25),
    .in26(D26), .in27(D27), .in28(D28), .in29(D29), .in30(D30), .in31(D31), .out(Reg2Out), .sel(R2_num));

  // Other names for the same wires on the sheet: CLK = Clock; D15[31:0] = D14; RA[4:0] = R1_num; RB[4:0] = R2_num;
  //   RDA[31:0] = Reg1Out; RDB[31:0] = Reg2Out; RW[4:0] = Write_Reg_num; WE = Write_Enable

  // Notes on the sheet:
  //   输入引脚
  //   电路功能：实现寄存器堆功能，实现0-31号寄存器。写使能有效且时钟边沿有效后写入数据，随时读出双口数据
  //   输出引脚
endmodule

module \数字时钟  (
  input  \设置初值 ,
  input  [3:0] \时高位 ,
  input  [3:0] \时低位 ,
  input  [3:0] \分高位 ,
  input  [3:0] \分低位 ,
  input  [3:0] \秒高位 ,
  input  [3:0] \秒低位 ,
  input  [3:0] \闹钟时高位 ,
  input  [3:0] \闹钟时低位 ,
  input  [3:0] \闹钟分高位 ,
  input  [3:0] \闹钟分低位 ,
  input  [3:0] \闹钟秒高位 ,
  input  [3:0] \闹钟秒低位 
);

  wire and_1_out, and_2_out, and_3_out, and_4_out, and_5_out, and_6_out, and_7_out, buzzer_2_p2, CLK,
       comparator_1_eq, comparator_2_eq, comparator_3_eq, comparator_4_eq, comparator_5_eq, comparator_6_eq,
       LED, not_1_out, or_1_out;
  wire [3:0] H0, H1, M0, M1, S0, S1;

  Clock \u_时钟  (.out(CLK));
  not not_1 (not_1_out, CLK);
  CNTR4U cntr4u_1 (
    .LD(\设置初值 ), .D0(\秒低位 [0]), .Q0(S0[0]), .CLK(CLK), .D1(\秒低位 [1]), .D2(\秒低位 [2]), .D3(\秒低位 [3]),
    .ENP(1'b1), .ENT(1'b1), .Q1(S0[1]), .Q2(S0[2]), .Q3(S0[3]), .CLR(and_1_out));  // open: RCO
  and and_1 (and_1_out, S0[3], S0[0]);
  CNTR4U cntr4u_2 (
    .LD(\设置初值 ), .D0(\时高位 [0]), .Q0(H1[0]), .CLK(CLK), .D1(\时高位 [1]), .D2(\时高位 [2]), .D3(\时高位 [3]),
    .ENP(or_1_out), .ENT(or_1_out), .Q1(H1[1]), .Q2(H1[2]), .Q3(H1[3]), .CLR(and_2_out));  // open: RCO
  and and_2 (and_2_out, H1[1], or_1_out);
  D_Flip_Flop d_ff_1 (.clk(not_1_out), .D(and_2_out), .Q(LED));  // open: Qn, preset, reset
  Hex_Digit_Display hex_digit_display_1 (.value(H1));  // open: dp
  Hex_Digit_Display hex_digit_display_2 (.value(H0), .dp(1'b1));
  and and_3 (and_3_out, S1[2], S1[0], and_1_out);
  CNTR4U cntr4u_3 (
    .LD(\设置初值 ), .D0(\时低位 [0]), .Q0(H0[0]), .CLK(CLK), .D1(\时低位 [1]), .D2(\时低位 [2]), .D3(\时低位 [3]),
    .ENP(and_7_out), .ENT(and_7_out), .Q1(H0[1]), .Q2(H0[2]), .Q3(H0[3]), .CLR(or_1_out));  // open: RCO
  and and_4 (and_4_out, H0[3], H0[0], and_7_out);
  or or_1 (or_1_out, and_4_out, and_5_out);
  and and_5 (and_5_out, H0[0], H0[1], and_7_out, H1[1]);
  Hex_Digit_Display hex_digit_display_3 (.value(M1));  // open: dp
  Hex_Digit_Display hex_digit_display_4 (.value(M0), .dp(1'b1));
  CNTR4U cntr4u_4 (
    .LD(\设置初值 ), .D0(\秒高位 [0]), .Q0(S1[0]), .CLK(CLK), .D1(\秒高位 [1]), .D2(\秒高位 [2]), .D3(\秒高位 [3]),
    .ENP(1'b1), .ENT(and_1_out), .Q1(S1[1]), .Q2(S1[2]), .Q3(S1[3]), .CLR(and_3_out));  // open: RCO
  Hex_Digit_Display hex_digit_display_5 (.value(S0), .dp(1'b1));
  Hex_Digit_Display hex_digit_display_6 (.value(S1));  // open: dp
  LED \u_整点点亮  (.in(LED));
  // Buzzer buzzer_1: pin names not known; wires that end beside it: 14'h1000, LED, 7'b0110000
  CNTR4U cntr4u_5 (
    .LD(\设置初值 ), .D0(\分低位 [0]), .Q0(M0[0]), .CLK(CLK), .D1(\分低位 [1]), .D2(\分低位 [2]), .D3(\分低位 [3]),
    .ENP(and_3_out), .ENT(and_3_out), .Q1(M0[1]), .Q2(M0[2]), .Q3(M0[3]), .CLR(and_6_out));  // open: RCO
  and and_6 (and_6_out, M0[3], M0[0], and_3_out);
  CNTR4U cntr4u_6 (
    .LD(\设置初值 ), .D0(\分高位 [0]), .Q0(M1[0]), .CLK(CLK), .D1(\分高位 [1]), .D2(\分高位 [2]), .D3(\分高位 [3]),
    .ENP(and_6_out), .ENT(and_6_out), .Q1(M1[1]), .Q2(M1[2]), .Q3(M1[3]), .CLR(and_7_out));  // open: RCO
  and and_7 (and_7_out, M1[2], M1[0], and_6_out);
  Comparator #(.width(4), .mode("unsigned")) comparator_1 (.a(\闹钟时高位 ), .b(H1), .eq(comparator_1_eq));  // open: gt, lt
  Comparator #(.width(4), .mode("unsigned")) comparator_2 (.a(\闹钟时低位 ), .b(H0), .eq(comparator_2_eq));  // open: gt, lt
  Comparator #(.width(4), .mode("unsigned")) comparator_3 (.a(\闹钟分高位 ), .b(M1), .eq(comparator_3_eq));  // open: gt, lt
  Comparator #(.width(4), .mode("unsigned")) comparator_4 (.a(\闹钟分低位 ), .b(M0), .eq(comparator_4_eq));  // open: gt, lt
  Comparator #(.width(4), .mode("unsigned")) comparator_5 (.a(\闹钟秒高位 ), .b(S1), .eq(comparator_5_eq));  // open: gt, lt
  Comparator #(.width(4), .mode("unsigned")) comparator_6 (.a(\闹钟秒低位 ), .b(S0), .eq(comparator_6_eq));  // open: gt, lt
  // Buzzer buzzer_2: pin names not known; wires that end beside it: 14'h1000, buzzer_2_p2, 7'b0110000
  and and_8 (buzzer_2_p2, comparator_1_eq, comparator_2_eq, comparator_3_eq, comparator_4_eq, comparator_5_eq, comparator_6_eq);

  // Other names for the same wires on the sheet: LD = \设置初值 ; 蜂鸣使能 = LED

  // Notes on the sheet:
  //   输入信号
  //   初始时间
  //   BCD码
  //   数字时钟
  //   频率
  //   蜂鸣器
  //   音量
  //   频率
  //   音量
  //   蜂鸣器
endmodule

module \_4位无符号数乘法器  (
  input  [3:0] X,
  input  [3:0] Y,
  output [7:0] \乘积 
);

  wire \_4位加法器_cout , LOAD, not_1_out, not_2_out, RST, STOP, \时钟_out ;
  wire [3:0] \_4位加法器_f , cntr4u_1_q0, multiplexer_1_out, multiplexer_2_out, \n8位移位器_1_dataout ,
       \n8位移位器_1_dataout_2 ;

  Button \u_复位  (.out(RST));
  Clock \u_时钟  (.out(\时钟_out ));
  not not_1 (not_1_out, STOP);
  Hex_Digit_Display hex_digit_display_1 (.value(X));  // open: dp
  Multiplexer #(.width(4), .enable("false")) multiplexer_1 (
    .in0(4'b0000), .in1(X), .out(multiplexer_1_out), .sel(\乘积 [0]));
  \_4位加法器  \_4位加法器  (
    .X(\乘积 [7:4]), .F(\_4位加法器_f ), .Y(multiplexer_1_out), .Cout(\_4位加法器_cout ), .Cin(1'b0));  // open: CF_进_借位
  Hex_Digit_Display hex_digit_display_2 (.value(Y));  // open: dp
  // Probe on \乘积 [7:4]
  Register #(.width(4), .Select("low")) register_1 (
    .D(\n8位移位器_1_dataout_2 ), .en(not_1_out), .Q(\乘积 [7:4]), .clk(\时钟_out ), .clr(RST));
  Register #(.width(4), .Select("low")) u_Y (
    .D(multiplexer_2_out), .en(not_1_out), .Q(\乘积 [3:0]), .clk(\时钟_out ), .clr(RST));
  \_8位移位器  \u_8位移位器_1  (
    .DataIn({\_4位加法器_f , \乘积 [3:0]}), .shamt(3'b001), .DataOut({\n8位移位器_1_dataout_2 , \n8位移位器_1_dataout }),
    .L_R(1'b0), .A_L(1'b0), .IN(\_4位加法器_cout ));
  Hex_Digit_Display hex_digit_display_3 (.value(\乘积 [7:4]));  // open: dp
  // Probe on \乘积 [3:0]
  not not_2 (not_2_out, \时钟_out );
  Multiplexer #(.width(4), .enable("false")) multiplexer_2 (
    .in0(\n8位移位器_1_dataout ), .in1(Y), .out(multiplexer_2_out), .sel(LOAD));
  Hex_Digit_Display hex_digit_display_4 (.value(\乘积 [3:0]));  // open: dp
  CNTR4U cntr4u_1 (
    .LD(1'b0), .D0(1'b0), .Q0(cntr4u_1_q0[0]), .CLK(not_2_out), .D1(1'b0), .D2(1'b0), .D3(1'b0), .ENP(1'b1),
    .ENT(1'b1), .Q1(cntr4u_1_q0[1]), .Q2(cntr4u_1_q0[2]), .Q3(cntr4u_1_q0[3]), .CLR(RST));  // open: RCO
  // Probe on cntr4u_1_q0
  // Probe on X
  // Probe on Y
  // Probe on \乘积 
  Comparator #(.width(4), .mode("unsigned")) comparator_1 (.a(cntr4u_1_q0), .b(4'b0000), .eq(LOAD));  // open: gt, lt
  Comparator #(.width(4), .mode("unsigned")) comparator_2 (.a(cntr4u_1_q0), .b(4'b0100), .gt(STOP));  // open: eq, lt

  // Other names for the same wires on the sheet: Z[7:0] = \乘积 

  // Notes on the sheet:
  //   输入引脚区
  //   X
  //   4位无符号数一位乘法器
  //   P
  //   =
  //   输出引脚区
  //   ×
  //   =
endmodule

module \_60进制计数器  (
);

  wire and_1_out, and_2_out, clock_1_out;
  wire [3:0] cntr4u_1_q0, cntr4u_2_q0;

  Clock clock_1 (.out(clock_1_out));
  and and_1 (and_1_out, cntr4u_2_q0[2], and_2_out, cntr4u_2_q0[0]);
  and and_2 (and_2_out, cntr4u_1_q0[3], cntr4u_1_q0[0]);
  CNTR4U cntr4u_1 (
    .LD(1'b0), .D0(1'b0), .Q0(cntr4u_1_q0[0]), .CLK(clock_1_out), .D1(1'b0), .D2(1'b0), .D3(1'b0),
    .ENP(1'b1), .ENT(1'b1), .Q1(cntr4u_1_q0[1]), .Q2(cntr4u_1_q0[2]), .Q3(cntr4u_1_q0[3]), .CLR(and_2_out));  // open: RCO
  CNTR4U cntr4u_2 (
    .LD(1'b0), .D0(1'b0), .Q0(cntr4u_2_q0[0]), .CLK(clock_1_out), .D1(1'b0), .D2(1'b0), .D3(1'b0),
    .ENP(and_2_out), .ENT(and_2_out), .Q1(cntr4u_2_q0[1]), .Q2(cntr4u_2_q0[2]), .Q3(cntr4u_2_q0[3]),
    .CLR(and_1_out));  // open: RCO
  Hex_Digit_Display hex_digit_display_1 (.value(cntr4u_2_q0));  // open: dp
  Hex_Digit_Display hex_digit_display_2 (.value(cntr4u_1_q0));  // open: dp

  // Notes on the sheet:
  //   60进制计数器_分解计数
endmodule

module \_8位移位器  (
  input  [7:0] DataIn,
  input  [2:0] shamt,
  input  IN,
  input  L_R,
  input  A_L,
  output [7:0] DataOut
);

  wire [7:0] multiplexer_2_out, multiplexer_3_out;
  wire [7:7] multiplexer_1_out;

  Multiplexer #(.enable("false")) multiplexer_1 (.in0(IN), .in1(DataIn[7]), .out(multiplexer_1_out[7]), .sel(A_L));
  Multiplexer #(.select(2), .width(8), .enable("false")) multiplexer_2 (
    .in0(DataIn), .in1({multiplexer_1_out[7], DataIn[7:1]}), .in2(DataIn), .in3({DataIn[6:0], IN}),
    .out(multiplexer_2_out), .sel({L_R, shamt[0]}));
  Multiplexer #(.select(2), .width(8), .enable("false")) multiplexer_3 (
    .in0(multiplexer_2_out), .in1({{2{multiplexer_1_out[7]}}, multiplexer_2_out[7:2]}),
    .in2(multiplexer_2_out), .in3({multiplexer_2_out[5:0], {2{IN}}}), .out(multiplexer_3_out),
    .sel({L_R, shamt[1]}));
  Multiplexer #(.select(2), .width(8), .enable("false")) multiplexer_4 (
    .in0(multiplexer_3_out), .in1({{4{multiplexer_1_out[7]}}, multiplexer_3_out[7:4]}),
    .in2(multiplexer_3_out), .in3({multiplexer_3_out[3:0], {4{IN}}}), .out(DataOut), .sel({L_R, shamt[2]}));

  // Other names for the same wires on the sheet: Din[7:0] = DataIn; Input = IN; Left_Right = L_R; Arth_Logic = A_L;
  //   Dout[7:0] = DataOut

  // Notes on the sheet:
  //   输入信号
  //   L/R=0：右移；=1：左移
  //   右移
  //   左移
  //   A/L=0：逻辑右移；=1：算术右移
  //   8位桶形移位器
  //   输出信号
endmodule

module \_4位加法器  (
  input  [3:0] X,
  input  [3:0] Y,
  input  Cin,
  output [3:0] F,
  output Cout,
  output \CF_进_借位 
);

  wire nor_1_out, xor_2_out, \全加器_1_cout , \全加器_2_cout , \全加器_3_cout ;
  wire [3:0] multiplexer_1_out, not_1_out;

  assign not_1_out = ~Y;  // NOT_Gate not_1, 4 bits wide
  Multiplexer #(.width(4), .enable("false")) multiplexer_1 (
    .in0(Y), .in1(not_1_out), .out(multiplexer_1_out), .sel(Cin));
  Hex_Digit_Display hex_digit_display_1 (.value(X));  // open: dp
  Hex_Digit_Display hex_digit_display_2 (.value(Y));  // open: dp
  \全加器  \u_全加器_1  (.A(X[0]), .B(multiplexer_1_out[0]), .Cin(Cin), .F(F[0]), .Cout(\全加器_1_cout ));
  \全加器  \u_全加器_2  (.A(X[1]), .B(multiplexer_1_out[1]), .Cin(\全加器_1_cout ), .F(F[1]), .Cout(\全加器_2_cout ));
  \全加器  \u_全加器_3  (.A(X[2]), .B(multiplexer_1_out[2]), .Cin(\全加器_2_cout ), .F(F[2]), .Cout(\全加器_3_cout ));
  \全加器  \u_全加器_4  (.A(X[3]), .B(multiplexer_1_out[3]), .Cin(\全加器_3_cout ), .F(F[3]), .Cout(Cout));
  Hex_Digit_Display hex_digit_display_3 (.value(F));  // open: dp
  xor xor_1 (\CF_进_借位 , Cout, Cin);
  xor xor_2 (xor_2_out, \全加器_3_cout , Cout);
  nor nor_1 (nor_1_out, F[0], F[1], F[2], F[3]);

  // Other names for the same wires on the sheet: 操作数x[3:0] = X; 操作数y[3:0] = Y; 运算结果[3:0] = F

  // Notes on the sheet:
  //   输入
  //   输出
  //   =
endmodule

module \全加器  (
  input  A,
  input  B,
  input  Cin,
  output F,
  output Cout
);

  wire and_1_out, and_2_out, and_3_out;

  and and_1 (and_1_out, A, B);
  and and_2 (and_2_out, A, Cin);
  and and_3 (and_3_out, Cin, B);
  xor xor_1 (F, A, B, Cin);
  or or_1 (Cout, and_1_out, and_2_out, and_3_out);

  // Notes on the sheet:
  //   全加器
endmodule

module \寄存器堆读写  (
  input  [4:0] R2_num,
  input  [4:0] R1_num,
  input  [4:0] Write_Reg_num,
  input  [31:0] Din,
  input  Write_Enable,
  output [31:0] Reg1Out,
  output [31:0] Reg2Out
);

  wire clock_1_out;

  Clock clock_1 (.out(clock_1_out));
  regfiles \u_寄存器堆  (
    .R1_num(R1_num), .R2_num(R2_num), .Din(Din), .Write_Reg_num(Write_Reg_num), .Write_Enable(Write_Enable),
    .Clock(clock_1_out), .Reg1Out(Reg1Out), .Reg2Out(Reg2Out));
endmodule

module \数字电路_闹钟  (
  input  \设置初值 ,
  input  [3:0] \时高位 ,
  input  [3:0] \时低位 ,
  input  [3:0] \分高位 ,
  input  [3:0] \分低位 ,
  input  [3:0] \秒高位 ,
  input  [3:0] \秒低位 
);

  wire and_1_out, and_2_out, and_3_out, and_4_out, and_5_out, and_6_out, and_7_out, CLK, LED, not_1_out,
       or_1_out;
  wire [3:0] H0, H1, M0, M1, S0, S1;

  Clock \u_时钟  (.out(CLK));
  not not_1 (not_1_out, CLK);
  CNTR4U cntr4u_1 (
    .LD(\设置初值 ), .D0(\秒低位 [0]), .Q0(S0[0]), .CLK(CLK), .D1(\秒低位 [1]), .D2(\秒低位 [2]), .D3(\秒低位 [3]),
    .ENP(1'b1), .ENT(1'b1), .Q1(S0[1]), .Q2(S0[2]), .Q3(S0[3]), .CLR(and_1_out));  // open: RCO
  and and_1 (and_1_out, S0[3], S0[0]);
  CNTR4U cntr4u_2 (
    .LD(\设置初值 ), .D0(\时高位 [0]), .Q0(H1[0]), .CLK(CLK), .D1(\时高位 [1]), .D2(\时高位 [2]), .D3(\时高位 [3]),
    .ENP(or_1_out), .ENT(or_1_out), .Q1(H1[1]), .Q2(H1[2]), .Q3(H1[3]), .CLR(and_2_out));  // open: RCO
  and and_2 (and_2_out, H1[1], or_1_out);
  D_Flip_Flop d_ff_1 (.clk(not_1_out), .D(and_2_out), .Q(LED));  // open: Qn, preset, reset
  Hex_Digit_Display hex_digit_display_1 (.value(H0), .dp(1'b1));
  Hex_Digit_Display hex_digit_display_2 (.value(H1));  // open: dp
  and and_3 (and_3_out, S1[2], S1[0], and_1_out);
  CNTR4U cntr4u_3 (
    .LD(\设置初值 ), .D0(\时低位 [0]), .Q0(H0[0]), .CLK(CLK), .D1(\时低位 [1]), .D2(\时低位 [2]), .D3(\时低位 [3]),
    .ENP(and_7_out), .ENT(and_7_out), .Q1(H0[1]), .Q2(H0[2]), .Q3(H0[3]), .CLR(or_1_out));  // open: RCO
  and and_4 (and_4_out, H0[3], H0[0], and_7_out);
  or or_1 (or_1_out, and_4_out, and_5_out);
  and and_5 (and_5_out, H0[0], H0[1], and_7_out, H1[1]);
  Hex_Digit_Display hex_digit_display_3 (.value(M0), .dp(1'b1));
  Hex_Digit_Display hex_digit_display_4 (.value(M1));  // open: dp
  CNTR4U cntr4u_4 (
    .LD(\设置初值 ), .D0(\秒高位 [0]), .Q0(S1[0]), .CLK(CLK), .D1(\秒高位 [1]), .D2(\秒高位 [2]), .D3(\秒高位 [3]),
    .ENP(1'b1), .ENT(and_1_out), .Q1(S1[1]), .Q2(S1[2]), .Q3(S1[3]), .CLR(and_3_out));  // open: RCO
  Hex_Digit_Display hex_digit_display_5 (.value(S1));  // open: dp
  Hex_Digit_Display hex_digit_display_6 (.value(S0), .dp(1'b1));
  LED \u_整点点亮  (.in(LED));
  // Buzzer buzzer_1: pin names not known; wires that end beside it: 14'h1000, LED, 7'b0110000
  CNTR4U cntr4u_5 (
    .LD(\设置初值 ), .D0(\分低位 [0]), .Q0(M0[0]), .CLK(CLK), .D1(\分低位 [1]), .D2(\分低位 [2]), .D3(\分低位 [3]),
    .ENP(and_3_out), .ENT(and_3_out), .Q1(M0[1]), .Q2(M0[2]), .Q3(M0[3]), .CLR(and_6_out));  // open: RCO
  and and_6 (and_6_out, M0[3], M0[0], and_3_out);
  CNTR4U cntr4u_6 (
    .LD(\设置初值 ), .D0(\分高位 [0]), .Q0(M1[0]), .CLK(CLK), .D1(\分高位 [1]), .D2(\分高位 [2]), .D3(\分高位 [3]),
    .ENP(and_6_out), .ENT(and_6_out), .Q1(M1[1]), .Q2(M1[2]), .Q3(M1[3]), .CLR(and_7_out));  // open: RCO
  and and_7 (and_7_out, M1[2], M1[0], and_6_out);
  Comparator #(.width(16), .mode("unsigned")) comparator_1 ();  // open: a, b, gt, eq, lt
  Comparator #(.width(16), .mode("unsigned")) comparator_2 ();  // open: a, b, gt, eq, lt
  Comparator #(.width(16), .mode("unsigned")) comparator_3 ();  // open: a, b, gt, eq, lt
  Comparator #(.width(16), .mode("unsigned")) comparator_4 ();  // open: a, b, gt, eq, lt
  Comparator #(.width(16), .mode("unsigned")) comparator_5 ();  // open: a, b, gt, eq, lt
  Comparator #(.width(16), .mode("unsigned")) comparator_6 ();  // open: a, b, gt, eq, lt

  // Other names for the same wires on the sheet: LD = \设置初值 ; 蜂鸣使能 = LED

  // Notes on the sheet:
  //   输入信号
  //   初始时间
  //   BCD码
  //   数字时钟
  //   频率
  //   蜂鸣器
  //   音量
endmodule

module \Booth乘法器  (
  input  [3:0] X,
  input  [3:0] Y,
  output [7:0] \乘积 
);

  wire \_4位加法器_cout , CLOCK, comparator_1_eq, LOAD, not_1_out, not_2_out, not_3_out, RST, STOP;
  wire [0:0] Y_1_q;
  wire [3:0] \_4位加法器_f , cntr4u_2_1_q0, multiplexer_1_out, multiplexer_2_out, \n8位移位器_1_dataout ,
       \n8位移位器_1_dataout_2 ;

  Button \u_复位  (.out(RST));
  Clock \u_时钟  (.out(CLOCK));
  Hex_Digit_Display hex_digit_display_1 (.value(X));  // open: dp
  not not_1 (not_1_out, STOP);
  Comparator #(.width(2), .mode("unsigned")) comparator_1 (
    .a(2'b10), .b({\乘积 [0], Y_1_q[0]}), .eq(comparator_1_eq));  // open: gt, lt
  Multiplexer #(.select(2), .width(4), .enable("false")) multiplexer_1 (
    .in0(4'b0000), .in1(X), .in2(X), .in3(4'b0000), .out(multiplexer_1_out), .sel({\乘积 [0], Y_1_q[0]}));
  not not_2 (not_2_out, STOP);
  // Probe on \_4位加法器_f 
  // Probe on multiplexer_1_out
  Register #(.width(1), .Select("low")) Y_1 (.D(\乘积 [0]), .en(not_2_out), .Q(Y_1_q[0]), .clk(CLOCK), .clr(RST));
  Hex_Digit_Display hex_digit_display_2 (.value(Y));  // open: dp
  \_4位加法器  \_4位加法器  (
    .X(\乘积 [7:4]), .F(\_4位加法器_f ), .Y(multiplexer_1_out), .Cout(\_4位加法器_cout ), .Cin(comparator_1_eq));  // open: CF_进_借位
  // Probe on \乘积 [7:4]
  Register #(.width(4), .Select("low")) register_1 (
    .D(\n8位移位器_1_dataout_2 ), .en(not_1_out), .Q(\乘积 [7:4]), .clk(CLOCK), .clr(RST));
  Hex_Digit_Display hex_digit_display_3 (.value(\乘积 [7:4]));  // open: dp
  Register #(.width(4), .Select("low")) u_Y (
    .D(multiplexer_2_out), .en(not_1_out), .Q(\乘积 [3:0]), .clk(CLOCK), .clr(RST));
  not not_3 (not_3_out, CLOCK);
  \_8位移位器  \u_8位移位器_1  (
    .DataIn({\_4位加法器_f , \乘积 [3:0]}), .shamt(3'b001), .DataOut({\n8位移位器_1_dataout_2 , \n8位移位器_1_dataout }),
    .L_R(1'b0), .A_L(1'b1), .IN(\_4位加法器_cout ));
  Hex_Digit_Display hex_digit_display_4 (.value(\乘积 [3:0]));  // open: dp
  // Probe on \乘积 [3:0]
  Multiplexer #(.width(4), .enable("false")) multiplexer_2 (
    .in0(\n8位移位器_1_dataout ), .in1(Y), .out(multiplexer_2_out), .sel(LOAD));
  CNTR4U_2 cntr4u_2_1 (
    .CLK(not_3_out), .LD(1'b0), .CLR(RST), .D0(1'b0), .D1(1'b0), .D2(1'b0), .D3(1'b0), .ENP(1'b1),
    .ENT(1'b1), .Q0(cntr4u_2_1_q0[0]), .Q1(cntr4u_2_1_q0[1]), .Q2(cntr4u_2_1_q0[2]), .Q3(cntr4u_2_1_q0[3]));  // open: RCO
  // Probe on cntr4u_2_1_q0
  // Probe on X
  // Probe on Y
  // Probe on \乘积 
  Comparator #(.width(4), .mode("unsigned")) comparator_2 (.a(cntr4u_2_1_q0), .b(4'b0001), .eq(LOAD));  // open: gt, lt
  Comparator #(.width(4), .mode("unsigned")) comparator_3 (.a(cntr4u_2_1_q0), .b(4'b0101), .gt(STOP));  // open: eq, lt

  // Other names for the same wires on the sheet: Z[7:0] = \乘积 

  // Notes on the sheet:
  //   输入引脚区
  //   X
  //   4位无符号数一位乘法器
  //   =
  //   P
  //   输出引脚区
  //   ×
  //   =
endmodule

// CNTR
module CNTR4U_2 (
  input  CLK,
  input  LD,
  input  CLR,
  input  D0,
  input  D1,
  input  D2,
  input  D3,
  input  ENP,
  input  ENT,
  output Q0,
  output Q1,
  output Q2,
  output Q3,
  output RCO
);

  wire and_1_out, and_2_out, and_3_out, and_4_out, and_5_out, and_6_out, and_8_out, and_9_out, and_10_out,
       and_11_out, and_12_out, and_13_out, and_14_out, and_15_out, buffer_1_out, d_ff_1_qn, d_ff_2_qn,
       d_ff_3_qn, d_ff_4_qn, not_1_out, not_2_out, or_1_out, or_2_out, or_3_out, or_4_out, xor_1_out,
       xor_2_out, xor_3_out, xor_4_out;

  buf buffer_1 (buffer_1_out, CLR);
  not not_1 (not_1_out, CLK);
  and and_1 (and_1_out, ENP, ENT);
  and and_2 (and_2_out, LD, ~buffer_1_out);  // AND_Gate
  and and_3 (and_3_out, ~and_2_out, ~buffer_1_out);  // AND_Gate
  not not_2 (not_2_out, and_1_out);
  xor xor_1 (xor_1_out, and_1_out, ~d_ff_1_qn);  // XOR_Gate
  and and_4 (and_4_out, ~d_ff_1_qn, and_1_out);  // AND_Gate
  xor xor_2 (xor_2_out, and_4_out, ~d_ff_2_qn);  // XOR_Gate
  and and_5 (and_5_out, ~d_ff_1_qn, ~d_ff_2_qn, and_1_out);  // AND_Gate
  xor xor_3 (xor_3_out, and_5_out, ~d_ff_3_qn);  // XOR_Gate
  and and_6 (and_6_out, ~d_ff_1_qn, ~d_ff_2_qn, ~d_ff_3_qn, and_1_out);  // AND_Gate
  xor xor_4 (xor_4_out, and_6_out, ~d_ff_4_qn);  // XOR_Gate
  and and_7 (RCO, ~d_ff_1_qn, ~d_ff_2_qn, ~d_ff_3_qn, ~d_ff_4_qn, ~not_2_out);  // AND_Gate
  and and_8 (and_8_out, and_2_out, D0);
  and and_9 (and_9_out, and_3_out, xor_1_out);
  and and_10 (and_10_out, and_2_out, D1);
  and and_11 (and_11_out, and_3_out, xor_2_out);
  and and_12 (and_12_out, and_2_out, D2);
  and and_13 (and_13_out, and_3_out, xor_3_out);
  and and_14 (and_14_out, and_2_out, D3);
  and and_15 (and_15_out, and_3_out, xor_4_out);
  or or_1 (or_1_out, and_8_out, and_9_out);
  or or_2 (or_2_out, and_10_out, and_11_out);
  or or_3 (or_3_out, and_12_out, and_13_out);
  or or_4 (or_4_out, and_14_out, and_15_out);
  D_Flip_Flop #(.trigger("falling")) d_ff_1 (
    .clk(not_1_out), .D(or_1_out), .Q(Q0), .Qn(d_ff_1_qn), .reset(CLR));  // open: preset
  D_Flip_Flop #(.trigger("falling")) d_ff_2 (
    .clk(not_1_out), .D(or_2_out), .Q(Q1), .Qn(d_ff_2_qn), .reset(CLR));  // open: preset
  D_Flip_Flop #(.trigger("falling")) d_ff_3 (
    .clk(not_1_out), .D(or_3_out), .Q(Q2), .Qn(d_ff_3_qn), .reset(CLR));  // open: preset
  D_Flip_Flop #(.trigger("falling")) d_ff_4 (
    .clk(not_1_out), .D(or_4_out), .Q(Q3), .Qn(d_ff_4_qn), .reset(CLR));  // open: preset

  // Notes on the sheet:
  //   4位二进制同步计数器
endmodule

module \无符号除法器  (
  input  [3:0] Y,
  input  [3:0] X,
  input  S0,
  input  S1,
  output [7:0] \乘积 
);

  wire \_4位加法器_cf_进_借位 , CLK, d_ff_1_q, d_ff_2_q, LOAD, multiplexer_1_out, multiplexer_3_out, not_1_out,
       not_2_out, not_3_out, not_4_out, RST, STA, STOP, xor_1_out;
  wire [3:0] \_4位加法器_f , cntr4u_2_1_q0, multiplexer_2_out, multiplexer_4_out, \n8位移位器_1_dataout ,
       \n8位移位器_1_dataout_2 ;

  Button \u_复位  (.out(RST));
  Clock \u_时钟  (.out(CLK));
  Hex_Digit_Display hex_digit_display_1 (.value(Y));  // open: dp
  not not_1 (not_1_out, STOP);
  // Probe on \_4位加法器_f 
  // Probe on X
  Multiplexer #(.enable("false")) multiplexer_1 (.in0(not_2_out), .in1(1'b1), .out(multiplexer_1_out), .sel(STA));
  not not_2 (not_2_out, xor_1_out);
  Hex_Digit_Display hex_digit_display_2 (.value(X));  // open: dp
  \_4位加法器  \_4位加法器  (
    .X(\乘积 [7:4]), .F(\_4位加法器_f ), .Y(X), .Cin(multiplexer_1_out), .\CF_进_借位 (\_4位加法器_cf_进_借位 ));  // open: Cout
  xor xor_1 (xor_1_out, d_ff_2_q, d_ff_1_q);
  // Probe on \乘积 [7:4]
  Register #(.width(4), .Select("low")) register_1 (
    .D(multiplexer_2_out), .en(not_1_out), .Q(\乘积 [7:4]), .clk(CLK), .clr(RST));
  // Probe on \乘积 [7:4]
  not not_3 (not_3_out, not_2_out);
  D_Flip_Flop d_ff_1 (.clk(CLK), .D(\_4位加法器_cf_进_借位 ), .Q(d_ff_1_q), .reset(RST));  // open: Qn, preset
  Hex_Digit_Display hex_digit_display_3 (.value(\乘积 [7:4]));  // open: dp
  Register #(.width(4), .Select("low")) u_Y (
    .D(multiplexer_4_out), .en(not_1_out), .Q(\乘积 [3:0]), .clk(CLK), .clr(RST));
  not not_4 (not_4_out, CLK);
  // Probe on multiplexer_2_out
  Multiplexer #(.select(2), .width(4), .enable("false")) multiplexer_2 (
    .in0(\n8位移位器_1_dataout_2 ), .in1(\n8位移位器_1_dataout_2 ), .in2(\n8位移位器_1_dataout_2 ), .in3(Y),
    .out(multiplexer_2_out), .sel({S1, LOAD}));
  \_8位移位器  \u_8位移位器_1  (
    .DataIn({\_4位加法器_f , \乘积 [3:0]}), .shamt(3'b001), .DataOut({\n8位移位器_1_dataout_2 , \n8位移位器_1_dataout }),
    .L_R(1'b1), .A_L(1'b1), .IN(not_3_out));
  Hex_Digit_Display hex_digit_display_4 (.value(\乘积 [3:0]));  // open: dp
  // Probe on \乘积 [3:0]
  // Probe on \n8位移位器_1_dataout 
  Multiplexer #(.enable("false")) multiplexer_3 (.in0(\_4位加法器_f [3]), .in1(1'b0), .out(multiplexer_3_out), .sel(STA));
  CNTR4U_2 cntr4u_2_1 (
    .CLK(not_4_out), .LD(1'b0), .CLR(RST), .D0(1'b0), .D1(1'b0), .D2(1'b0), .D3(1'b0), .ENP(1'b1),
    .ENT(1'b1), .Q0(cntr4u_2_1_q0[0]), .Q1(cntr4u_2_1_q0[1]), .Q2(cntr4u_2_1_q0[2]), .Q3(cntr4u_2_1_q0[3]));  // open: RCO
  // Probe on multiplexer_4_out
  Multiplexer #(.select(2), .width(4), .enable("false")) multiplexer_4 (
    .in0(\n8位移位器_1_dataout ), .in1(\n8位移位器_1_dataout ), .in2(\n8位移位器_1_dataout ), .in3(Y),
    .out(multiplexer_4_out), .sel({S0, LOAD}));
  D_Flip_Flop d_ff_2 (.clk(CLK), .D(multiplexer_3_out), .Q(d_ff_2_q), .reset(RST));  // open: Qn, preset
  // Probe on Y
  // Probe on X
  // Probe on \乘积 
  // Probe on cntr4u_2_1_q0
  Comparator #(.width(4), .mode("unsigned")) comparator_1 (.a(cntr4u_2_1_q0), .b(4'b0010), .eq(STA));  // open: gt, lt
  Comparator #(.width(4), .mode("unsigned")) comparator_2 (.a(cntr4u_2_1_q0), .b(4'b0001), .eq(LOAD));  // open: gt, lt
  Comparator #(.width(4), .mode("unsigned")) comparator_3 (.a(cntr4u_2_1_q0), .b(4'b0101), .gt(STOP));  // open: eq, lt

  // Other names for the same wires on the sheet: Z[7:0] = \乘积 

  // Notes on the sheet:
  //   输入引脚区
  //   /
  //   4位无符号数一位乘法器
  //   =
  //   P
  //   输出引脚区
  //   /
  //   =
endmodule

module \_5位加法器  (
  input  [4:0] X,
  input  [4:0] Y,
  input  Cin,
  output [4:0] F,
  output Cout
);

  wire nor_1_out, \全加器_1_cout , \全加器_2_cout , \全加器_3_cout , \全加器_4_cout ;
  wire [3:0] undriven;
  wire [4:0] multiplexer_1_out, not_1_out;

  assign not_1_out = ~Y;  // NOT_Gate not_1, 5 bits wide
  Multiplexer #(.width(5), .enable("false")) multiplexer_1 (
    .in0(Y), .in1(not_1_out), .out(multiplexer_1_out), .sel(Cin));
  \全加器  \u_全加器_1  (.A(X[0]), .B(multiplexer_1_out[0]), .Cin(Cin), .F(F[0]), .Cout(\全加器_1_cout ));
  \全加器  \u_全加器_2  (.A(X[1]), .B(multiplexer_1_out[1]), .Cin(\全加器_1_cout ), .F(F[1]), .Cout(\全加器_2_cout ));
  \全加器  \u_全加器_3  (.A(X[2]), .B(multiplexer_1_out[2]), .Cin(\全加器_2_cout ), .F(F[2]), .Cout(\全加器_3_cout ));
  \全加器  \u_全加器_4  (.A(X[3]), .B(multiplexer_1_out[3]), .Cin(\全加器_3_cout ), .F(F[3]), .Cout(\全加器_4_cout ));
  \全加器  \u_全加器_5  (.A(X[4]), .B(multiplexer_1_out[4]), .Cin(\全加器_4_cout ), .F(F[4]), .Cout(Cout));
  nor nor_1 (nor_1_out, undriven[0], undriven[1], undriven[2], undriven[3]);

  // Other names for the same wires on the sheet: 操作数x[4:0] = X; 操作数y[4:0] = Y; 运算结果[4:0] = F

  // Notes on the sheet:
  //   输入
  //   输出
  //   =
endmodule

module \无符号除法器2  (
  input  [7:0] Y,
  input  [3:0] X,
  output [3:0] \商 ,
  output [3:0] \余数 ,
  output \溢出标志 
);

  wire CLK, d_ff_1_qn, LOAD, multiplexer_1_out, not_1_out, not_2_out, not_3_out, RST, STA, STOP;
  wire [3:0] cntr4u_2_1_q0, multiplexer_2_out, multiplexer_2_out_2;
  wire [4:0] bit_extender_1_out, \n5位加法器_1_f ;
  wire [7:0] \n8位移位器_1_dataout ;

  Button \u_复位  (.out(RST));
  Clock \u_时钟  (.out(CLK));
  D_Flip_Flop d_ff_1 (.clk(CLK), .D(\n5位加法器_1_f [4]), .Qn(d_ff_1_qn), .reset(RST));  // open: Q, preset
  Hex_Digit_Display hex_digit_display_1 (.value(Y[7:4]));  // open: dp
  Hex_Digit_Display hex_digit_display_2 (.value(Y[3:0]));  // open: dp
  not not_1 (not_1_out, STOP);
  assign bit_extender_1_out = {{1{1'b0}}, X};  // Bit_Extender bit_extender_1
  // Probe on \n5位加法器_1_f 
  Multiplexer #(.enable("false")) multiplexer_1 (.in0(d_ff_1_qn), .in1(1'b1), .out(multiplexer_1_out), .sel(STA));
  Hex_Digit_Display hex_digit_display_3 (.value(X));  // open: dp
  // Probe on {\余数 , \溢出标志 }
  \_5位加法器  \u_5位加法器_1  (
    .X({\余数 , \溢出标志 }), .F(\n5位加法器_1_f ), .Y(bit_extender_1_out), .Cin(multiplexer_1_out));  // open: Cout
  Register #(.width(5), .Select("low")) register_1 (
    .D({\n5位加法器_1_f [3], multiplexer_2_out_2}), .en(not_1_out), .Q({\余数 , \溢出标志 }), .clk(CLK), .clr(RST));
  not not_2 (not_2_out, \n5位加法器_1_f [4]);
  Hex_Digit_Display hex_digit_display_4 (.value(\商 ));  // open: dp
  Register #(.width(4), .Select("low")) Q (.D(multiplexer_2_out), .en(not_1_out), .Q(\商 ), .clk(CLK), .clr(RST));
  not not_3 (not_3_out, CLK);
  \_8位移位器  \u_8位移位器_1  (
    .DataIn({\n5位加法器_1_f [3:0], \商 }), .shamt(3'b001), .DataOut(\n8位移位器_1_dataout ), .L_R(1'b1), .A_L(1'b1),
    .IN(not_2_out));
  Hex_Digit_Display hex_digit_display_5 (.value(\余数 ));  // open: dp
  CNTR4U_2 cntr4u_2_1 (
    .CLK(not_3_out), .LD(1'b0), .CLR(RST), .D0(1'b0), .D1(1'b0), .D2(1'b0), .D3(1'b0), .ENP(1'b1),
    .ENT(1'b1), .Q0(cntr4u_2_1_q0[0]), .Q1(cntr4u_2_1_q0[1]), .Q2(cntr4u_2_1_q0[2]), .Q3(cntr4u_2_1_q0[3]));  // open: RCO
  Multiplexer #(.width(8), .enable("false")) multiplexer_2 (
    .in0(\n8位移位器_1_dataout ), .in1(Y), .out({multiplexer_2_out_2, multiplexer_2_out}), .sel(LOAD));
  // Probe on Y
  // Probe on X
  // Probe on \商 
  // Probe on \余数 
  // Probe on cntr4u_2_1_q0
  Comparator #(.width(4), .mode("unsigned")) comparator_1 (.a(cntr4u_2_1_q0), .b(4'b0010), .eq(STA));  // open: gt, lt
  Comparator #(.width(4), .mode("unsigned")) comparator_2 (.a(cntr4u_2_1_q0), .b(4'b0001), .eq(LOAD));  // open: gt, lt
  Comparator #(.width(4), .mode("unsigned")) comparator_3 (.a(cntr4u_2_1_q0), .b(4'b0110), .gt(STOP));  // open: eq, lt

  // Other names for the same wires on the sheet: OF = \溢出标志 ; R[3:0] = \余数 ; Q[3:0] = \商 

  // Notes on the sheet:
  //   输入引脚区
  //   /
  //   4位无符号数一位乘法器
  //   R
  //   =
  //   输出引脚区
  //   /
  //   =
endmodule
