// Logisim project lab5(1).circ as structural Verilog
module \ASCII码显示实验  (
  input  [7:0] ASCII_CODE,
  input  Sel
);

  wire [7:0] row1, row2, row3, row4, row5, row6, row7, row8, row9, row10, row11, row12, row13, row14, row15,
       row16, subtractor_1_out;

  Subtractor subtractor_1 (.a(ASCII_CODE), .b(8'h20), .out(subtractor_1_out), .bin(1'b0));  // open: bout
  ROM #(.addrWidth(16), .Select("high"), .simpleMode("false")) rom_1 (
    .addr({4'b0000, subtractor_1_out, 4'b0000}), .data(row1), .sel(Sel));
  ROM #(.addrWidth(16), .Select("high")) rom_2 (.addr({4'b0000, subtractor_1_out, 4'b0001}), .data(row2), .sel(Sel));
  ROM #(.addrWidth(16), .Select("high")) rom_3 (.addr({4'b0000, subtractor_1_out, 4'b0010}), .data(row3), .sel(Sel));
  ROM #(.addrWidth(16), .Select("high")) rom_4 (.addr({4'b0000, subtractor_1_out, 4'b0011}), .data(row4), .sel(Sel));
  ROM #(.addrWidth(16), .Select("high")) rom_5 (.addr({4'b0000, subtractor_1_out, 4'b0100}), .data(row5), .sel(Sel));
  ROM #(.addrWidth(16), .Select("high")) rom_6 (.addr({4'b0000, subtractor_1_out, 4'b0101}), .data(row6), .sel(Sel));
  ROM #(.addrWidth(16), .Select("high")) rom_7 (.addr({4'b0000, subtractor_1_out, 4'b0110}), .data(row7), .sel(Sel));
  ROM #(.addrWidth(16), .Select("high")) rom_8 (.addr({4'b0000, subtractor_1_out, 4'b0111}), .data(row8), .sel(Sel));
  DotMatrix #(.inputtype("row"), .matrixcols(8), .matrixrows(16)) dotmatrix_1 (
    .row0(row1), .row1(row2), .row2(row3), .row3(row4), .row4(row5), .row5(row6), .row6(row7), .row7(row8),
    .row8(row9), .row9(row10), .row10(row11), .row11(row12), .row12(row13), .row13(row14), .row14(row15),
    .row15(row16));
  ROM #(.addrWidth(16), .Select("high")) rom_9 (.addr({4'b0000, subtractor_1_out, 4'b1000}), .data(row9), .sel(Sel));
  ROM #(.addrWidth(16), .Select("high")) rom_10 (.addr({4'b0000, subtractor_1_out, 4'b1001}), .data(row10), .sel(Sel));
  ROM #(.addrWidth(16), .Select("high")) rom_11 (.addr({4'b0000, subtractor_1_out, 4'b1010}), .data(row11), .sel(Sel));
  ROM #(.addrWidth(16), .Select("high")) rom_12 (.addr({4'b0000, subtractor_1_out, 4'b1011}), .data(row12), .sel(Sel));
  ROM #(.addrWidth(16), .Select("high")) rom_13 (.addr({4'b0000, subtractor_1_out, 4'b1100}), .data(row13), .sel(Sel));
  ROM #(.addrWidth(16), .Select("high")) rom_14 (.addr({4'b0000, subtractor_1_out, 4'b1101}), .data(row14), .sel(Sel));
  ROM #(.addrWidth(16), .Select("high")) rom_15 (.addr({4'b0000, subtractor_1_out, 4'b1110}), .data(row15), .sel(Sel));
  ROM #(.addrWidth(16), .Select("high")) rom_16 (.addr({4'b0000, subtractor_1_out, 4'b1111}), .data(row16), .sel(Sel));

  // Other names for the same wires on the sheet: Code[7:0] = ASCII_CODE

  // Notes on the sheet:
  //   ASCII字库地址
  //   contents of rom_1 (hex, n*v repeats v):
  //   18*0 18 3c 3c 3c 18 18 18 0 18 18 5*0 63 63 63 22 14*0 36 36 7f 36 36 36 7f 36 36 4*0 c c 3e 63 61
  //   60 3e 3 3 43 63 3e c c 7*0 61 63 6 c 18 33 63 7*0 1c 36 36 1c 3b 6e 66 66 3b 5*0 30 30 30 60 13*0 c
  //   18 18 4*30 18 18 c 6*0 18 c c 4*6 c c 18 8*0 42 66 3c ff 3c 66 42 9*0 18 18 18 ff 18 18 18 15*0 18
  //   18 18 30 9*0 ff 18*0 18 18 6*0 1 3 7 e 1c 38 70 e0 c0 80 6*0 3e 63 63 63 6b 6b 63 63 63 3e 6*0 c 1c
  //   3c 6*c 3f 6*0 3e 63 3 6 c 18 30 61 63 7f 6*0 3e 63 3 3 1e 3 3 3 63 3e 6*0 6 e 1e 36 66 66 7f 6 6 f
  //   6*0 7f 60 60 60 7e 3 3 63 73 3e 6*0 1c 30 60 60 7e 4*63 3e 6*0 7f 63 3 6 6 c c 18 18 18 6*0 3e 63 63
  //   63 3e 4*63 3e 6*0 3e 4*63 3f 3 3 6 3c 9*0 18 18 0 0 0 18 18 9*0 18 18 0 0 0 18 18 18 30 5*0 6 c 18
  //   30 60 30 18 c 6 10*0 7e 0 0 7e 9*0 60 30 18 c 6 c 18 30 60 6*0 3e 63 63 6 c c c 0 c c 6*0 3e 63 63
  //   6f 6b 6b 6e 60 60 3e 6*0 8 1c 36 63 63 63 7f 63 63 63 6*0 7e 33 33 33 3e 4*33 7e 6*0 1e 33 61 4*60
  //   61 33 1e 6*0 7c 36 6*33 36 7c 6*0 7f 33 31 34 3c 34 30 31 33 7f 6*0 7f 33 31 34 3c 34 30 30 30 78
  //   6*0 1e 33 61 60 60 6f 63 63 37 1d 6*0 4*63 7f 5*63 6*0 3c 8*18 3c 6*0 f 6*6 66 66 3c 6*0 73 33 36 36
  //   3c 36 36 33 33 73 6*0 78 6*30 31 33 7f 6*0 63 77 7f 6b 6*63 6*0 63 63 73 7b 7f 6f 67 63 63 63 6*0 1c
  //   36 6*63 36 1c 6*0 7e 33 33 33 3e 4*30 78 6*0 3e 6*63 6b 6f 3e 6 7 4*0 7e 33 33 33 3e 36 36 33 33 73
  //   6*0 3e 63 63 30 1c 6 3 63 63 3e 6*0 ff db 99 6*18 3c 6*0 9*63 3e 6*0 7*63 36 1c 8 6*0 5*63 6b 6b 7f
  //   36 36 6*0 c3 c3 66 3c 18 18 3c 66 c3 c3 6*0 c3 c3 c3 66 3c 4*18 3c 6*0 7f 63 43 6 c 18 30 61 63 7f
  //   6*0 3c 8*30 3c 6*0 80 c0 e0 70 38 1c e 7 3 1 6*0 3c 8*c 3c 4*0 8 1c 36 63 24*0 ff 0 0 0 18 18 c 18*0
  //   3c 46 6 3e 66 66 3b 6*0 70 30 30 3c 36 4*33 6e 9*0 3e 63 60 60 60 63 3e 6*0 e 6 6 1e 36 4*66 3b 9*0
  //   3e 63 63 7e 60 63 3e 6*0 1c 36 32 30 7c 4*30 78 9*0 3b 4*66 3e 6 66 3c 4*0 70 30 30 36 3b 4*33 73
  //   6*0 c c 0 1c 5*c 1e 6*0 6 6 0 e 5*6 66 66 3c 4*0 70 30 30 33 33 36 3c 36 33 73 6*0 1c 8*c 1e 9*0 6e
  //   7f 5*6b 9*0 6e 6*33 9*0 3e 5*63 3e 9*0 6e 4*33 3e 30 30 78 7*0 3b 4*66 3e 6 6 f 7*0 6e 3b 33 30 30
  //   30 78 9*0 3e 63 38 e 3 63 3e 6*0 8 18 18 7e 4*18 1b e 9*0 6*66 3b 9*0 63 63 36 36 1c 1c 8 9*0 63 63
  //   63 6b 6b 7f 36 9*0 63 36 1c 1c 1c 36 63 9*0 5*63 3f 3 6 3c 7*0 7f 66 c 18 30 63 7f 6*0 e 18 18 18 70
  //   4*18 e 6*0 5*18 0 5*18 5*0 70 18 18 18 e 4*18 70 6*0 3b 6e 13*0 70 d8 d8 70
  //   contents of rom_2 (hex, n*v repeats v):
  //   18*0 18 3c 3c 3c 18 18 18 0 18 18 5*0 63 63 63 22 14*0 36 36 7f 36 36 36 7f 36 36 4*0 c c 3e 63 61
  //   60 3e 3 3 43 63 3e c c 7*0 61 63 6 c 18 33 63 7*0 1c 36 36 1c 3b 6e 66 66 3b 5*0 30 30 30 60 13*0 c
  //   18 18 4*30 18 18 c 6*0 18 c c 4*6 c c 18 8*0 42 66 3c ff 3c 66 42 9*0 18 18 18 ff 18 18 18 15*0 18
  //   18 18 30 9*0 ff 18*0 18 18 6*0 1 3 7 e 1c 38 70 e0 c0 80 6*0 3e 63 63 63 6b 6b 63 63 63 3e 6*0 c 1c
  //   3c 6*c 3f 6*0 3e 63 3 6 c 18 30 61 63 7f 6*0 3e 63 3 3 1e 3 3 3 63 3e 6*0 6 e 1e 36 66 66 7f 6 6 f
  //   6*0 7f 60 60 60 7e 3 3 63 73 3e 6*0 1c 30 60 60 7e 4*63 3e 6*0 7f 63 3 6 6 c c 18 18 18 6*0 3e 63 63
  //   63 3e 4*63 3e 6*0 3e 4*63 3f 3 3 6 3c 9*0 18 18 0 0 0 18 18 9*0 18 18 0 0 0 18 18 18 30 5*0 6 c 18
  //   30 60 30 18 c 6 10*0 7e 0 0 7e 9*0 60 30 18 c 6 c 18 30 60 6*0 3e 63 63 6 c c c 0 c c 6*0 3e 63 63
  //   6f 6b 6b 6e 60 60 3e 6*0 8 1c 36 63 63 63 7f 63 63 63 6*0 7e 33 33 33 3e 4*33 7e 6*0 1e 33 61 4*60
  //   61 33 1e 6*0 7c 36 6*33 36 7c 6*0 7f 33 31 34 3c 34 30 31 33 7f 6*0 7f 33 31 34 3c 34 30 30 30 78
  //   6*0 1e 33 61 60 60 6f 63 63 37 1d 6*0 4*63 7f 5*63 6*0 3c 8*18 3c 6*0 f 6*6 66 66 3c 6*0 73 33 36 36
  //   3c 36 36 33 33 73 6*0 78 6*30 31 33 7f 6*0 63 77 7f 6b 6*63 6*0 63 63 73 7b 7f 6f 67 63 63 63 6*0 1c
  //   36 6*63 36 1c 6*0 7e 33 33 33 3e 4*30 78 6*0 3e 6*63 6b 6f 3e 6 7 4*0 7e 33 33 33 3e 36 36 33 33 73
  //   6*0 3e 63 63 30 1c 6 3 63 63 3e 6*0 ff db 99 6*18 3c 6*0 9*63 3e 6*0 7*63 36 1c 8 6*0 5*63 6b 6b 7f
  //   36 36 6*0 c3 c3 66 3c 18 18 3c 66 c3 c3 6*0 c3 c3 c3 66 3c 4*18 3c 6*0 7f 63 43 6 c 18 30 61 63 7f
  //   6*0 3c 8*30 3c 6*0 80 c0 e0 70 38 1c e 7 3 1 6*0 3c 8*c 3c 4*0 8 1c 36 63 24*0 ff 0 0 0 18 18 c 18*0
  //   3c 46 6 3e 66 66 3b 6*0 70 30 30 3c 36 4*33 6e 9*0 3e 63 60 60 60 63 3e 6*0 e 6 6 1e 36 4*66 3b 9*0
  //   3e 63 63 7e 60 63 3e 6*0 1c 36 32 30 7c 4*30 78 9*0 3b 4*66 3e 6 66 3c 4*0 70 30 30 36 3b 4*33 73
  //   6*0 c c 0 1c 5*c 1e 6*0 6 6 0 e 5*6 66 66 3c 4*0 70 30 30 33 33 36 3c 36 33 73 6*0 1c 8*c 1e 9*0 6e
  //   7f 5*6b 9*0 6e 6*33 9*0 3e 5*63 3e 9*0 6e 4*33 3e 30 30 78 7*0 3b 4*66 3e 6 6 f 7*0 6e 3b 33 30 30
  //   30 78 9*0 3e 63 38 e 3 63 3e 6*0 8 18 18 7e 4*18 1b e 9*0 6*66 3b 9*0 63 63 36 36 1c 1c 8 9*0 63 63
  //   63 6b 6b 7f 36 9*0 63 36 1c 1c 1c 36 63 9*0 5*63 3f 3 6 3c 7*0 7f 66 c 18 30 63 7f 6*0 e 18 18 18 70
  //   4*18 e 6*0 5*18 0 5*18 5*0 70 18 18 18 e 4*18 70 6*0 3b 6e 13*0 70 d8 d8 70
  //   contents of rom_3 (hex, n*v repeats v):
  //   18*0 18 3c 3c 3c 18 18 18 0 18 18 5*0 63 63 63 22 14*0 36 36 7f 36 36 36 7f 36 36 4*0 c c 3e 63 61
  //   60 3e 3 3 43 63 3e c c 7*0 61 63 6 c 18 33 63 7*0 1c 36 36 1c 3b 6e 66 66 3b 5*0 30 30 30 60 13*0 c
  //   18 18 4*30 18 18 c 6*0 18 c c 4*6 c c 18 8*0 42 66 3c ff 3c 66 42 9*0 18 18 18 ff 18 18 18 15*0 18
  //   18 18 30 9*0 ff 18*0 18 18 6*0 1 3 7 e 1c 38 70 e0 c0 80 6*0 3e 63 63 63 6b 6b 63 63 63 3e 6*0 c 1c
  //   3c 6*c 3f 6*0 3e 63 3 6 c 18 30 61 63 7f 6*0 3e 63 3 3 1e 3 3 3 63 3e 6*0 6 e 1e 36 66 66 7f 6 6 f
  //   6*0 7f 60 60 60 7e 3 3 63 73 3e 6*0 1c 30 60 60 7e 4*63 3e 6*0 7f 63 3 6 6 c c 18 18 18 6*0 3e 63 63
  //   63 3e 4*63 3e 6*0 3e 4*63 3f 3 3 6 3c 9*0 18 18 0 0 0 18 18 9*0 18 18 0 0 0 18 18 18 30 5*0 6 c 18
  //   30 60 30 18 c 6 10*0 7e 0 0 7e 9*0 60 30 18 c 6 c 18 30 60 6*0 3e 63 63 6 c c c 0 c c 6*0 3e 63 63
  //   6f 6b 6b 6e 60 60 3e 6*0 8 1c 36 63 63 63 7f 63 63 63 6*0 7e 33 33 33 3e 4*33 7e 6*0 1e 33 61 4*60
  //   61 33 1e 6*0 7c 36 6*33 36 7c 6*0 7f 33 31 34 3c 34 30 31 33 7f 6*0 7f 33 31 34 3c 34 30 30 30 78
  //   6*0 1e 33 61 60 60 6f 63 63 37 1d 6*0 4*63 7f 5*63 6*0 3c 8*18 3c 6*0 f 6*6 66 66 3c 6*0 73 33 36 36
  //   3c 36 36 33 33 73 6*0 78 6*30 31 33 7f 6*0 63 77 7f 6b 6*63 6*0 63 63 73 7b 7f 6f 67 63 63 63 6*0 1c
  //   36 6*63 36 1c 6*0 7e 33 33 33 3e 4*30 78 6*0 3e 6*63 6b 6f 3e 6 7 4*0 7e 33 33 33 3e 36 36 33 33 73
  //   6*0 3e 63 63 30 1c 6 3 63 63 3e 6*0 ff db 99 6*18 3c 6*0 9*63 3e 6*0 7*63 36 1c 8 6*0 5*63 6b 6b 7f
  //   36 36 6*0 c3 c3 66 3c 18 18 3c 66 c3 c3 6*0 c3 c3 c3 66 3c 4*18 3c 6*0 7f 63 43 6 c 18 30 61 63 7f
  //   6*0 3c 8*30 3c 6*0 80 c0 e0 70 38 1c e 7 3 1 6*0 3c 8*c 3c 4*0 8 1c 36 63 24*0 ff 0 0 0 18 18 c 18*0
  //   3c 46 6 3e 66 66 3b 6*0 70 30 30 3c 36 4*33 6e 9*0 3e 63 60 60 60 63 3e 6*0 e 6 6 1e 36 4*66 3b 9*0
  //   3e 63 63 7e 60 63 3e 6*0 1c 36 32 30 7c 4*30 78 9*0 3b 4*66 3e 6 66 3c 4*0 70 30 30 36 3b 4*33 73
  //   6*0 c c 0 1c 5*c 1e 6*0 6 6 0 e 5*6 66 66 3c 4*0 70 30 30 33 33 36 3c 36 33 73 6*0 1c 8*c 1e 9*0 6e
  //   7f 5*6b 9*0 6e 6*33 9*0 3e 5*63 3e 9*0 6e 4*33 3e 30 30 78 7*0 3b 4*66 3e 6 6 f 7*0 6e 3b 33 30 30
  //   30 78 9*0 3e 63 38 e 3 63 3e 6*0 8 18 18 7e 4*18 1b e 9*0 6*66 3b 9*0 63 63 36 36 1c 1c 8 9*0 63 63
  //   63 6b 6b 7f 36 9*0 63 36 1c 1c 1c 36 63 9*0 5*63 3f 3 6 3c 7*0 7f 66 c 18 30 63 7f 6*0 e 18 18 18 70
  //   4*18 e 6*0 5*18 0 5*18 5*0 70 18 18 18 e 4*18 70 6*0 3b 6e 13*0 70 d8 d8 70
  //   contents of rom_4 (hex, n*v repeats v):
  //   18*0 18 3c 3c 3c 18 18 18 0 18 18 5*0 63 63 63 22 14*0 36 36 7f 36 36 36 7f 36 36 4*0 c c 3e 63 61
  //   60 3e 3 3 43 63 3e c c 7*0 61 63 6 c 18 33 63 7*0 1c 36 36 1c 3b 6e 66 66 3b 5*0 30 30 30 60 13*0 c
  //   18 18 4*30 18 18 c 6*0 18 c c 4*6 c c 18 8*0 42 66 3c ff 3c 66 42 9*0 18 18 18 ff 18 18 18 15*0 18
  //   18 18 30 9*0 ff 18*0 18 18 6*0 1 3 7 e 1c 38 70 e0 c0 80 6*0 3e 63 63 63 6b 6b 63 63 63 3e 6*0 c 1c
  //   3c 6*c 3f 6*0 3e 63 3 6 c 18 30 61 63 7f 6*0 3e 63 3 3 1e 3 3 3 63 3e 6*0 6 e 1e 36 66 66 7f 6 6 f
  //   6*0 7f 60 60 60 7e 3 3 63 73 3e 6*0 1c 30 60 60 7e 4*63 3e 6*0 7f 63 3 6 6 c c 18 18 18 6*0 3e 63 63
  //   63 3e 4*63 3e 6*0 3e 4*63 3f 3 3 6 3c 9*0 18 18 0 0 0 18 18 9*0 18 18 0 0 0 18 18 18 30 5*0 6 c 18
  //   30 60 30 18 c 6 10*0 7e 0 0 7e 9*0 60 30 18 c 6 c 18 30 60 6*0 3e 63 63 6 c c c 0 c c 6*0 3e 63 63
  //   6f 6b 6b 6e 60 60 3e 6*0 8 1c 36 63 63 63 7f 63 63 63 6*0 7e 33 33 33 3e 4*33 7e 6*0 1e 33 61 4*60
  //   61 33 1e 6*0 7c 36 6*33 36 7c 6*0 7f 33 31 34 3c 34 30 31 33 7f 6*0 7f 33 31 34 3c 34 30 30 30 78
  //   6*0 1e 33 61 60 60 6f 63 63 37 1d 6*0 4*63 7f 5*63 6*0 3c 8*18 3c 6*0 f 6*6 66 66 3c 6*0 73 33 36 36
  //   3c 36 36 33 33 73 6*0 78 6*30 31 33 7f 6*0 63 77 7f 6b 6*63 6*0 63 63 73 7b 7f 6f 67 63 63 63 6*0 1c
  //   36 6*63 36 1c 6*0 7e 33 33 33 3e 4*30 78 6*0 3e 6*63 6b 6f 3e 6 7 4*0 7e 33 33 33 3e 36 36 33 33 73
  //   6*0 3e 63 63 30 1c 6 3 63 63 3e 6*0 ff db 99 6*18 3c 6*0 9*63 3e 6*0 7*63 36 1c 8 6*0 5*63 6b 6b 7f
  //   36 36 6*0 c3 c3 66 3c 18 18 3c 66 c3 c3 6*0 c3 c3 c3 66 3c 4*18 3c 6*0 7f 63 43 6 c 18 30 61 63 7f
  //   6*0 3c 8*30 3c 6*0 80 c0 e0 70 38 1c e 7 3 1 6*0 3c 8*c 3c 4*0 8 1c 36 63 24*0 ff 0 0 0 18 18 c 18*0
  //   3c 46 6 3e 66 66 3b 6*0 70 30 30 3c 36 4*33 6e 9*0 3e 63 60 60 60 63 3e 6*0 e 6 6 1e 36 4*66 3b 9*0
  //   3e 63 63 7e 60 63 3e 6*0 1c 36 32 30 7c 4*30 78 9*0 3b 4*66 3e 6 66 3c 4*0 70 30 30 36 3b 4*33 73
  //   6*0 c c 0 1c 5*c 1e 6*0 6 6 0 e 5*6 66 66 3c 4*0 70 30 30 33 33 36 3c 36 33 73 6*0 1c 8*c 1e 9*0 6e
  //   7f 5*6b 9*0 6e 6*33 9*0 3e 5*63 3e 9*0 6e 4*33 3e 30 30 78 7*0 3b 4*66 3e 6 6 f 7*0 6e 3b 33 30 30
  //   30 78 9*0 3e 63 38 e 3 63 3e 6*0 8 18 18 7e 4*18 1b e 9*0 6*66 3b 9*0 63 63 36 36 1c 1c 8 9*0 63 63
  //   63 6b 6b 7f 36 9*0 63 36 1c 1c 1c 36 63 9*0 5*63 3f 3 6 3c 7*0 7f 66 c 18 30 63 7f 6*0 e 18 18 18 70
  //   4*18 e 6*0 5*18 0 5*18 5*0 70 18 18 18 e 4*18 70 6*0 3b 6e 13*0 70 d8 d8 70
  //   contents of rom_5 (hex, n*v repeats v):
  //   18*0 18 3c 3c 3c 18 18 18 0 18 18 5*0 63 63 63 22 14*0 36 36 7f 36 36 36 7f 36 36 4*0 c c 3e 63 61
  //   60 3e 3 3 43 63 3e c c 7*0 61 63 6 c 18 33 63 7*0 1c 36 36 1c 3b 6e 66 66 3b 5*0 30 30 30 60 13*0 c
  //   18 18 4*30 18 18 c 6*0 18 c c 4*6 c c 18 8*0 42 66 3c ff 3c 66 42 9*0 18 18 18 ff 18 18 18 15*0 18
  //   18 18 30 9*0 ff 18*0 18 18 6*0 1 3 7 e 1c 38 70 e0 c0 80 6*0 3e 63 63 63 6b 6b 63 63 63 3e 6*0 c 1c
  //   3c 6*c 3f 6*0 3e 63 3 6 c 18 30 61 63 7f 6*0 3e 63 3 3 1e 3 3 3 63 3e 6*0 6 e 1e 36 66 66 7f 6 6 f
  //   6*0 7f 60 60 60 7e 3 3 63 73 3e 6*0 1c 30 60 60 7e 4*63 3e 6*0 7f 63 3 6 6 c c 18 18 18 6*0 3e 63 63
  //   63 3e 4*63 3e 6*0 3e 4*63 3f 3 3 6 3c 9*0 18 18 0 0 0 18 18 9*0 18 18 0 0 0 18 18 18 30 5*0 6 c 18
  //   30 60 30 18 c 6 10*0 7e 0 0 7e 9*0 60 30 18 c 6 c 18 30 60 6*0 3e 63 63 6 c c c 0 c c 6*0 3e 63 63
  //   6f 6b 6b 6e 60 60 3e 6*0 8 1c 36 63 63 63 7f 63 63 63 6*0 7e 33 33 33 3e 4*33 7e 6*0 1e 33 61 4*60
  //   61 33 1e 6*0 7c 36 6*33 36 7c 6*0 7f 33 31 34 3c 34 30 31 33 7f 6*0 7f 33 31 34 3c 34 30 30 30 78
  //   6*0 1e 33 61 60 60 6f 63 63 37 1d 6*0 4*63 7f 5*63 6*0 3c 8*18 3c 6*0 f 6*6 66 66 3c 6*0 73 33 36 36
  //   3c 36 36 33 33 73 6*0 78 6*30 31 33 7f 6*0 63 77 7f 6b 6*63 6*0 63 63 73 7b 7f 6f 67 63 63 63 6*0 1c
  //   36 6*63 36 1c 6*0 7e 33 33 33 3e 4*30 78 6*0 3e 6*63 6b 6f 3e 6 7 4*0 7e 33 33 33 3e 36 36 33 33 73
  //   6*0 3e 63 63 30 1c 6 3 63 63 3e 6*0 ff db 99 6*18 3c 6*0 9*63 3e 6*0 7*63 36 1c 8 6*0 5*63 6b 6b 7f
  //   36 36 6*0 c3 c3 66 3c 18 18 3c 66 c3 c3 6*0 c3 c3 c3 66 3c 4*18 3c 6*0 7f 63 43 6 c 18 30 61 63 7f
  //   6*0 3c 8*30 3c 6*0 80 c0 e0 70 38 1c e 7 3 1 6*0 3c 8*c 3c 4*0 8 1c 36 63 24*0 ff 0 0 0 18 18 c 18*0
  //   3c 46 6 3e 66 66 3b 6*0 70 30 30 3c 36 4*33 6e 9*0 3e 63 60 60 60 63 3e 6*0 e 6 6 1e 36 4*66 3b 9*0
  //   3e 63 63 7e 60 63 3e 6*0 1c 36 32 30 7c 4*30 78 9*0 3b 4*66 3e 6 66 3c 4*0 70 30 30 36 3b 4*33 73
  //   6*0 c c 0 1c 5*c 1e 6*0 6 6 0 e 5*6 66 66 3c 4*0 70 30 30 33 33 36 3c 36 33 73 6*0 1c 8*c 1e 9*0 6e
  //   7f 5*6b 9*0 6e 6*33 9*0 3e 5*63 3e 9*0 6e 4*33 3e 30 30 78 7*0 3b 4*66 3e 6 6 f 7*0 6e 3b 33 30 30
  //   30 78 9*0 3e 63 38 e 3 63 3e 6*0 8 18 18 7e 4*18 1b e 9*0 6*66 3b 9*0 63 63 36 36 1c 1c 8 9*0 63 63
  //   63 6b 6b 7f 36 9*0 63 36 1c 1c 1c 36 63 9*0 5*63 3f 3 6 3c 7*0 7f 66 c 18 30 63 7f 6*0 e 18 18 18 70
  //   4*18 e 6*0 5*18 0 5*18 5*0 70 18 18 18 e 4*18 70 6*0 3b 6e 13*0 70 d8 d8 70
  //   contents of rom_6 (hex, n*v repeats v):
  //   18*0 18 3c 3c 3c 18 18 18 0 18 18 5*0 63 63 63 22 14*0 36 36 7f 36 36 36 7f 36 36 4*0 c c 3e 63 61
  //   60 3e 3 3 43 63 3e c c 7*0 61 63 6 c 18 33 63 7*0 1c 36 36 1c 3b 6e 66 66 3b 5*0 30 30 30 60 13*0 c
  //   18 18 4*30 18 18 c 6*0 18 c c 4*6 c c 18 8*0 42 66 3c ff 3c 66 42 9*0 18 18 18 ff 18 18 18 15*0 18
  //   18 18 30 9*0 ff 18*0 18 18 6*0 1 3 7 e 1c 38 70 e0 c0 80 6*0 3e 63 63 63 6b 6b 63 63 63 3e 6*0 c 1c
  //   3c 6*c 3f 6*0 3e 63 3 6 c 18 30 61 63 7f 6*0 3e 63 3 3 1e 3 3 3 63 3e 6*0 6 e 1e 36 66 66 7f 6 6 f
  //   6*0 7f 60 60 60 7e 3 3 63 73 3e 6*0 1c 30 60 60 7e 4*63 3e 6*0 7f 63 3 6 6 c c 18 18 18 6*0 3e 63 63
  //   63 3e 4*63 3e 6*0 3e 4*63 3f 3 3 6 3c 9*0 18 18 0 0 0 18 18 9*0 18 18 0 0 0 18 18 18 30 5*0 6 c 18
  //   30 60 30 18 c 6 10*0 7e 0 0 7e 9*0 60 30 18 c 6 c 18 30 60 6*0 3e 63 63 6 c c c 0 c c 6*0 3e 63 63
  //   6f 6b 6b 6e 60 60 3e 6*0 8 1c 36 63 63 63 7f 63 63 63 6*0 7e 33 33 33 3e 4*33 7e 6*0 1e 33 61 4*60
  //   61 33 1e 6*0 7c 36 6*33 36 7c 6*0 7f 33 31 34 3c 34 30 31 33 7f 6*0 7f 33 31 34 3c 34 30 30 30 78
  //   6*0 1e 33 61 60 60 6f 63 63 37 1d 6*0 4*63 7f 5*63 6*0 3c 8*18 3c 6*0 f 6*6 66 66 3c 6*0 73 33 36 36
  //   3c 36 36 33 33 73 6*0 78 6*30 31 33 7f 6*0 63 77 7f 6b 6*63 6*0 63 63 73 7b 7f 6f 67 63 63 63 6*0 1c
  //   36 6*63 36 1c 6*0 7e 33 33 33 3e 4*30 78 6*0 3e 6*63 6b 6f 3e 6 7 4*0 7e 33 33 33 3e 36 36 33 33 73
  //   6*0 3e 63 63 30 1c 6 3 63 63 3e 6*0 ff db 99 6*18 3c 6*0 9*63 3e 6*0 7*63 36 1c 8 6*0 5*63 6b 6b 7f
  //   36 36 6*0 c3 c3 66 3c 18 18 3c 66 c3 c3 6*0 c3 c3 c3 66 3c 4*18 3c 6*0 7f 63 43 6 c 18 30 61 63 7f
  //   6*0 3c 8*30 3c 6*0 80 c0 e0 70 38 1c e 7 3 1 6*0 3c 8*c 3c 4*0 8 1c 36 63 24*0 ff 0 0 0 18 18 c 18*0
  //   3c 46 6 3e 66 66 3b 6*0 70 30 30 3c 36 4*33 6e 9*0 3e 63 60 60 60 63 3e 6*0 e 6 6 1e 36 4*66 3b 9*0
  //   3e 63 63 7e 60 63 3e 6*0 1c 36 32 30 7c 4*30 78 9*0 3b 4*66 3e 6 66 3c 4*0 70 30 30 36 3b 4*33 73
  //   6*0 c c 0 1c 5*c 1e 6*0 6 6 0 e 5*6 66 66 3c 4*0 70 30 30 33 33 36 3c 36 33 73 6*0 1c 8*c 1e 9*0 6e
  //   7f 5*6b 9*0 6e 6*33 9*0 3e 5*63 3e 9*0 6e 4*33 3e 30 30 78 7*0 3b 4*66 3e 6 6 f 7*0 6e 3b 33 30 30
  //   30 78 9*0 3e 63 38 e 3 63 3e 6*0 8 18 18 7e 4*18 1b e 9*0 6*66 3b 9*0 63 63 36 36 1c 1c 8 9*0 63 63
  //   63 6b 6b 7f 36 9*0 63 36 1c 1c 1c 36 63 9*0 5*63 3f 3 6 3c 7*0 7f 66 c 18 30 63 7f 6*0 e 18 18 18 70
  //   4*18 e 6*0 5*18 0 5*18 5*0 70 18 18 18 e 4*18 70 6*0 3b 6e 13*0 70 d8 d8 70
  //   contents of rom_7 (hex, n*v repeats v):
  //   18*0 18 3c 3c 3c 18 18 18 0 18 18 5*0 63 63 63 22 14*0 36 36 7f 36 36 36 7f 36 36 4*0 c c 3e 63 61
  //   60 3e 3 3 43 63 3e c c 7*0 61 63 6 c 18 33 63 7*0 1c 36 36 1c 3b 6e 66 66 3b 5*0 30 30 30 60 13*0 c
  //   18 18 4*30 18 18 c 6*0 18 c c 4*6 c c 18 8*0 42 66 3c ff 3c 66 42 9*0 18 18 18 ff 18 18 18 15*0 18
  //   18 18 30 9*0 ff 18*0 18 18 6*0 1 3 7 e 1c 38 70 e0 c0 80 6*0 3e 63 63 63 6b 6b 63 63 63 3e 6*0 c 1c
  //   3c 6*c 3f 6*0 3e 63 3 6 c 18 30 61 63 7f 6*0 3e 63 3 3 1e 3 3 3 63 3e 6*0 6 e 1e 36 66 66 7f 6 6 f
  //   6*0 7f 60 60 60 7e 3 3 63 73 3e 6*0 1c 30 60 60 7e 4*63 3e 6*0 7f 63 3 6 6 c c 18 18 18 6*0 3e 63 63
  //   63 3e 4*63 3e 6*0 3e 4*63 3f 3 3 6 3c 9*0 18 18 0 0 0 18 18 9*0 18 18 0 0 0 18 18 18 30 5*0 6 c 18
  //   30 60 30 18 c 6 10*0 7e 0 0 7e 9*0 60 30 18 c 6 c 18 30 60 6*0 3e 63 63 6 c c c 0 c c 6*0 3e 63 63
  //   6f 6b 6b 6e 60 60 3e 6*0 8 1c 36 63 63 63 7f 63 63 63 6*0 7e 33 33 33 3e 4*33 7e 6*0 1e 33 61 4*60
  //   61 33 1e 6*0 7c 36 6*33 36 7c 6*0 7f 33 31 34 3c 34 30 31 33 7f 6*0 7f 33 31 34 3c 34 30 30 30 78
  //   6*0 1e 33 61 60 60 6f 63 63 37 1d 6*0 4*63 7f 5*63 6*0 3c 8*18 3c 6*0 f 6*6 66 66 3c 6*0 73 33 36 36
  //   3c 36 36 33 33 73 6*0 78 6*30 31 33 7f 6*0 63 77 7f 6b 6*63 6*0 63 63 73 7b 7f 6f 67 63 63 63 6*0 1c
  //   36 6*63 36 1c 6*0 7e 33 33 33 3e 4*30 78 6*0 3e 6*63 6b 6f 3e 6 7 4*0 7e 33 33 33 3e 36 36 33 33 73
  //   6*0 3e 63 63 30 1c 6 3 63 63 3e 6*0 ff db 99 6*18 3c 6*0 9*63 3e 6*0 7*63 36 1c 8 6*0 5*63 6b 6b 7f
  //   36 36 6*0 c3 c3 66 3c 18 18 3c 66 c3 c3 6*0 c3 c3 c3 66 3c 4*18 3c 6*0 7f 63 43 6 c 18 30 61 63 7f
  //   6*0 3c 8*30 3c 6*0 80 c0 e0 70 38 1c e 7 3 1 6*0 3c 8*c 3c 4*0 8 1c 36 63 24*0 ff 0 0 0 18 18 c 18*0
  //   3c 46 6 3e 66 66 3b 6*0 70 30 30 3c 36 4*33 6e 9*0 3e 63 60 60 60 63 3e 6*0 e 6 6 1e 36 4*66 3b 9*0
  //   3e 63 63 7e 60 63 3e 6*0 1c 36 32 30 7c 4*30 78 9*0 3b 4*66 3e 6 66 3c 4*0 70 30 30 36 3b 4*33 73
  //   6*0 c c 0 1c 5*c 1e 6*0 6 6 0 e 5*6 66 66 3c 4*0 70 30 30 33 33 36 3c 36 33 73 6*0 1c 8*c 1e 9*0 6e
  //   7f 5*6b 9*0 6e 6*33 9*0 3e 5*63 3e 9*0 6e 4*33 3e 30 30 78 7*0 3b 4*66 3e 6 6 f 7*0 6e 3b 33 30 30
  //   30 78 9*0 3e 63 38 e 3 63 3e 6*0 8 18 18 7e 4*18 1b e 9*0 6*66 3b 9*0 63 63 36 36 1c 1c 8 9*0 63 63
  //   63 6b 6b 7f 36 9*0 63 36 1c 1c 1c 36 63 9*0 5*63 3f 3 6 3c 7*0 7f 66 c 18 30 63 7f 6*0 e 18 18 18 70
  //   4*18 e 6*0 5*18 0 5*18 5*0 70 18 18 18 e 4*18 70 6*0 3b 6e 13*0 70 d8 d8 70
  //   contents of rom_8 (hex, n*v repeats v):
  //   18*0 18 3c 3c 3c 18 18 18 0 18 18 5*0 63 63 63 22 14*0 36 36 7f 36 36 36 7f 36 36 4*0 c c 3e 63 61
  //   60 3e 3 3 43 63 3e c c 7*0 61 63 6 c 18 33 63 7*0 1c 36 36 1c 3b 6e 66 66 3b 5*0 30 30 30 60 13*0 c
  //   18 18 4*30 18 18 c 6*0 18 c c 4*6 c c 18 8*0 42 66 3c ff 3c 66 42 9*0 18 18 18 ff 18 18 18 15*0 18
  //   18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
  //   contents of rom_9 (hex, n*v repeats v):
  //   18*0 18 3c 3c 3c 18 18 18 0 18 18 5*0 63 63 63 22 14*0 36 36 7f 36 36 36 7f 36 36 4*0 c c 3e 63 61
  //   60 3e 3 3 43 63 3e c c 7*0 61 63 6 c 18 33 63 7*0 1c 36 36 1c 3b 6e 66 66 3b 5*0 30 30 30 60 13*0 c
  //   18 18 4*30 18 18 c 6*0 18 c c 4*6 c c 18 8*0 42 66 3c ff 3c 66 42 9*0 18 18 18 ff 18 18 18 15*0 18
  //   18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
  //   contents of rom_10 (hex, n*v repeats v):
  //   18*0 18 3c 3c 3c 18 18 18 0 18 18 5*0 63 63 63 22 14*0 36 36 7f 36 36 36 7f 36 36 4*0 c c 3e 63 61
  //   60 3e 3 3 43 63 3e c c 7*0 61 63 6 c 18 33 63 7*0 1c 36 36 1c 3b 6e 66 66 3b 5*0 30 30 30 60 13*0 c
  //   18 18 4*30 18 18 c 6*0 18 c c 4*6 c c 18 8*0 42 66 3c ff 3c 66 42 9*0 18 18 18 ff 18 18 18 15*0 18
  //   18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
  //   contents of rom_11 (hex, n*v repeats v):
  //   18*0 18 3c 3c 3c 18 18 18 0 18 18 5*0 63 63 63 22 14*0 36 36 7f 36 36 36 7f 36 36 4*0 c c 3e 63 61
  //   60 3e 3 3 43 63 3e c c 7*0 61 63 6 c 18 33 63 7*0 1c 36 36 1c 3b 6e 66 66 3b 5*0 30 30 30 60 13*0 c
  //   18 18 4*30 18 18 c 6*0 18 c c 4*6 c c 18 8*0 42 66 3c ff 3c 66 42 9*0 18 18 18 ff 18 18 18 15*0 18
  //   18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
  //   contents of rom_12 (hex, n*v repeats v):
  //   18*0 18 3c 3c 3c 18 18 18 0 18 18 5*0 63 63 63 22 14*0 36 36 7f 36 36 36 7f 36 36 4*0 c c 3e 63 61
  //   60 3e 3 3 43 63 3e c c 7*0 61 63 6 c 18 33 63 7*0 1c 36 36 1c 3b 6e 66 66 3b 5*0 30 30 30 60 13*0 c
  //   18 18 4*30 18 18 c 6*0 18 c c 4*6 c c 18 8*0 42 66 3c ff 3c 66 42 9*0 18 18 18 ff 18 18 18 15*0 18
  //   18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
  //   contents of rom_13 (hex, n*v repeats v):
  //   18*0 18 3c 3c 3c 18 18 18 0 18 18 5*0 63 63 63 22 14*0 36 36 7f 36 36 36 7f 36 36 4*0 c c 3e 63 61
  //   60 3e 3 3 43 63 3e c c 7*0 61 63 6 c 18 33 63 7*0 1c 36 36 1c 3b 6e 66 66 3b 5*0 30 30 30 60 13*0 c
  //   18 18 4*30 18 18 c 6*0 18 c c 4*6 c c 18 8*0 42 66 3c ff 3c 66 42 9*0 18 18 18 ff 18 18 18 15*0 18
  //   18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
  //   contents of rom_14 (hex, n*v repeats v):
  //   18*0 18 3c 3c 3c 18 18 18 0 18 18 5*0 63 63 63 22 14*0 36 36 7f 36 36 36 7f 36 36 4*0 c c 3e 63 61
  //   60 3e 3 3 43 63 3e c c 7*0 61 63 6 c 18 33 63 7*0 1c 36 36 1c 3b 6e 66 66 3b 5*0 30 30 30 60 13*0 c
  //   18 18 4*30 18 18 c 6*0 18 c c 4*6 c c 18 8*0 42 66 3c ff 3c 66 42 9*0 18 18 18 ff 18 18 18 15*0 18
  //   18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
  //   contents of rom_15 (hex, n*v repeats v):
  //   18*0 18 3c 3c 3c 18 18 18 0 18 18 5*0 63 63 63 22 14*0 36 36 7f 36 36 36 7f 36 36 4*0 c c 3e 63 61
  //   60 3e 3 3 43 63 3e c c 7*0 61 63 6 c 18 33 63 7*0 1c 36 36 1c 3b 6e 66 66 3b 5*0 30 30 30 60 13*0 c
  //   18 18 4*30 18 18 c 6*0 18 c c 4*6 c c 18 8*0 42 66 3c ff 3c 66 42 9*0 18 18 18 ff 18 18 18 15*0 18
  //   18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
  //   contents of rom_16 (hex, n*v repeats v):
  //   18*0 18 3c 3c 3c 18 18 18 0 18 18 5*0 63 63 63 22 14*0 36 36 7f 36 36 36 7f 36 36 4*0 c c 3e 63 61
  //   60 3e 3 3 43 63 3e c c 7*0 61 63 6 c 18 33 63 7*0 1c 36 36 1c 3b 6e 66 66 3b 5*0 30 30 30 60 13*0 c
  //   18 18 4*30 18 18 c 6*0 18 c c 4*6 c c 18 8*0 42 66 3c ff 3c 66 42 9*0 18 18 18 ff 18 18 18 15*0 18
  //   18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
endmodule

module IFU (
  input  [31:0] Initial_Address,
  input  [31:0] Imm,
  input  [31:0] BusA,
  input  CLK,
  input  Reset,
  input  Halt,
  input  NxtASrc,
  input  NxtBSrc,
  output [31:0] PC
);

  wire not_1_out;
  wire [31:0] multiplexer_1_out, multiplexer_2_out, multiplexer_3_out, NxtPC;

  Multiplexer #(.width(32), .enable("false")) multiplexer_1 (
    .in0(NxtPC), .in1(Initial_Address), .out(multiplexer_1_out), .sel(Reset));
  not not_1 (not_1_out, Halt);
  Register #(.width(32), .Select("high")) u_PC (
    .D(multiplexer_1_out), .en(not_1_out), .Q(PC), .clk(CLK), .clr(1'b0), .cs(1'b1), .preset(1'b0));
  Multiplexer #(.width(32), .enable("false")) multiplexer_2 (
    .in0(PC), .in1(BusA), .out(multiplexer_2_out), .sel(NxtASrc));
  Multiplexer #(.width(32), .enable("false")) multiplexer_3 (
    .in0(32'h4), .in1(Imm), .out(multiplexer_3_out), .sel(NxtBSrc));
  \_32位加法器  \u_32位加法器_1  (
    .Cin(1'b0), .X(multiplexer_2_out), .Y(multiplexer_3_out), .S(NxtPC));  // open: Cout, OF, CF, ZF, SF

  // Other names for the same wires on the sheet: Init_Addr[31:0] = Initial_Address

  // Notes on the sheet:
  //   Halt: pull=down
  //   BusA: pull=down
  //   NxtBSrc: pull=down
  //   NxtASrc: pull=down
  //   Imm: pull=down
  //   指令存储器的数据位设置为32位，地址位设置为16位。存储器按照32位字长编址，地址位最低2位舍弃。
  //   输入信号
  //   输出信号
endmodule

module \立即数扩展器  (
  input  [31:0] Instr,
  input  [2:0] Extop,
  output [31:0] imm
);

  wire [31:0] bit_extender_1_out, bit_extender_2_out, bit_extender_3_out, bit_extender_4_out;

  assign bit_extender_1_out = {{20{Instr[31]}}, Instr[31:20]};  // Bit_Extender bit_extender_1
  assign bit_extender_2_out = {{20{Instr[31]}}, {Instr[31:25], Instr[11:7]}};  // Bit_Extender bit_extender_2
  assign bit_extender_3_out = {{19{Instr[31]}}, {Instr[31], Instr[7], Instr[30:25], Instr[11:8], 1'b0}};  // Bit_Extender bit_extender_3
  assign bit_extender_4_out = {{11{Instr[31]}}, {Instr[31], Instr[19:12], Instr[20], Instr[30:21], 1'b0}};  // Bit_Extender bit_extender_4
  Multiplexer #(.select(3), .width(32), .enable("false")) multiplexer_1 (
    .in0(bit_extender_1_out), .in1({Instr[31:12], {12{1'b0}}}), .in2(bit_extender_2_out),
    .in3(bit_extender_3_out), .in4(bit_extender_4_out), .in5(bit_extender_4_out), .out(imm), .sel(Extop));  // open: in6, in7

  // Notes on the sheet:
  //   Instr: pull=down
  //   Extop: pull=down
  //   输入引脚
  //   I
  //   U
  //   S
  //   B
  //   J
  //   输出引脚
endmodule

module IDU (
  input  [31:0] IR,
  input  [31:0] BusW,
  input  [31:0] PC,
  input  [2:0] ExtOp,
  input  RegWr,
  input  ALUASrc,
  input  [1:0] ALUBSrc,
  input  CLK,
  output [31:0] DataA,
  output [31:0] DataB,
  output [31:0] BusA,
  output [6:0] OpCode,
  output [31:0] BusB,
  output [31:0] Imm,
  output [2:0] Funct3,
  output [6:0] Funct7
);

  // Probe on IR[24:20]
  \立即数扩展器  \u_立即数扩展器_1  (.Instr(IR), .Extop(ExtOp), .imm(Imm));
  // Probe on IR[11:7]
  // Probe on IR[19:15]
  RegFile regfile_1 (
    .R1_num(IR[19:15]), .R2_num(IR[24:20]), .Din(BusW), .Reg1Out(BusA), .Reg2Out(BusB),
    .Write_Reg_num(IR[11:7]), .Write_Enable(RegWr), .Clock(CLK));
  Multiplexer #(.width(32), .enable("false")) multiplexer_1 (.in0(BusA), .in1(PC), .out(DataA), .sel(ALUASrc));
  Multiplexer #(.select(2), .width(32), .enable("false")) multiplexer_2 (
    .in0(BusB), .in1(32'h4), .in2(Imm), .out(DataB), .sel(ALUBSrc));  // open: in3

  assign Funct3 = IR[14:12];
  assign Funct7 = IR[31:25];
  assign OpCode = IR[6:0];

  // Other names for the same wires on the sheet: DataIn[31:0] = BusB; op[6:0] = IR[6:0]

  // Notes on the sheet:
  //   BusW: pull=down
  //   ALUASrc: pull=down
  //   ExtOp: pull=down
  //   ALUBSrc: pull=down
  //   PC: pull=down
  //   RegWr: pull=down
  //   指令解析
  //   输入信号
  //   rd
  //   rs1
  //   rs2
  //   imm
  //   访问寄存器堆
  //   输出信号
  //   输出数据
endmodule

module RegFile (
  input  [4:0] R1_num,
  input  [4:0] R2_num,
  input  [31:0] Din,
  input  [4:0] Write_Reg_num,
  input  Write_Enable,
  input  Clock,
  output [31:0] Reg1Out,
  output [31:0] Reg2Out
);

  wire _0_out, _1_out, _2_out, _3_out, _4_out, _5_out, _6_out, _7_out, _8_out, _9_out, _10_out, _11_out,
       _12_out, _13_out, _14_out, _15_out, _16_out, _17_out, _18_out, _19_out, _20_out, _21_out, _22_out,
       _23_out, _24_out, _25_out, _26_out, _27_out, _28_out, _29_out, _30_out, _31_out, undriven, undriven_2,
       undriven_3, undriven_4;
  wire [31:0] D0, D1, D2, D3, D4, D5, D6, D7, D8, D9, D10, D11, D12, D13, D14, D15, D16, D17, D18, D19, D20,
       D21, D22, D23, D24, D25, D26, D27, D28, D29, D30, D31, dec;

  Decoder #(.select(5), .enable("false")) decoder_1 (
    .out0(dec[0]), .out1(dec[1]), .out2(dec[2]), .out3(dec[3]), .out4(dec[4]), .out5(dec[5]), .out6(dec[6]),
    .out7(dec[7]), .out8(dec[8]), .out9(dec[9]), .out10(dec[10]), .out11(dec[11]), .out12(dec[12]),
    .out13(dec[13]), .out14(dec[14]), .out15(dec[15]), .out16(dec[16]), .out17(dec[17]), .out18(dec[18]),
    .out19(dec[19]), .out20(dec[20]), .out21(dec[21]), .out22(dec[22]), .out23(dec[23]), .out24(dec[24]),
    .out25(dec[25]), .out26(dec[26]), .out27(dec[27]), .out28(dec[28]), .out29(dec[29]), .out30(dec[30]),
    .out31(dec[31]), .sel(Write_Reg_num));
  // Probe on Write_Reg_num
  and _0 (_0_out, dec[0], Write_Enable);
  and _1 (_1_out, dec[1], Write_Enable);
  and _2 (_2_out, dec[2], Write_Enable);
  and _3 (_3_out, dec[3], Write_Enable);
  and _4 (_4_out, dec[4], Write_Enable);
  and _5 (_5_out, dec[5], Write_Enable);
  and _6 (_6_out, dec[6], Write_Enable);
  and _7 (_7_out, dec[7], Write_Enable);
  and _8 (_8_out, dec[8], Write_Enable);
  and _9 (_9_out, dec[9], Write_Enable);
  and _10 (_10_out, dec[10], Write_Enable);
  and _11 (_11_out, dec[11], Write_Enable);
  and _12 (_12_out, dec[12], Write_Enable);
  and _13 (_13_out, dec[13], Write_Enable);
  and _14 (_14_out, dec[14], Write_Enable);
  and _15 (_15_out, dec[15], Write_Enable);
  Register #(.width(32), .Select("low")) register_1 (.D(Din), .en(_0_out), .Q(D0), .clk(Clock));  // open: clr
  Register #(.width(32), .Select("low")) register_2 (.D(Din), .en(_1_out), .Q(D1), .clk(Clock));  // open: clr
  Register #(.width(32), .Select("low")) register_3 (.D(Din), .en(_2_out), .Q(D2), .clk(Clock));  // open: clr
  Register #(.width(32), .Select("low")) register_4 (.D(Din), .en(_3_out), .Q(D3), .clk(Clock), .clr(undriven));
  Register #(.width(32), .Select("low")) register_5 (.D(Din), .en(_4_out), .Q(D4), .clk(Clock));  // open: clr
  Register #(.width(32), .Select("low")) register_6 (.D(Din), .en(_5_out), .Q(D5), .clk(Clock));  // open: clr
  Register #(.width(32), .Select("low")) register_7 (.D(Din), .en(_6_out), .Q(D6), .clk(Clock));  // open: clr
  Register #(.width(32), .Select("low")) register_8 (.D(Din), .en(_7_out), .Q(D7), .clk(Clock));  // open: clr
  Register #(.width(32), .Select("low")) register_9 (.D(Din), .en(_8_out), .Q(D8), .clk(Clock));  // open: clr
  Register #(.width(32), .Select("low")) register_10 (.D(Din), .en(_9_out), .Q(D9), .clk(Clock));  // open: clr
  Register #(.width(32), .Select("low")) register_11 (.D(Din), .en(_10_out), .Q(D10), .clk(Clock));  // open: clr
  Register #(.width(32), .Select("low")) register_12 (.D(Din), .en(_11_out), .Q(D11), .clk(Clock), .clr(undriven_2));
  Register #(.width(32), .Select("low")) register_13 (.D(Din), .en(_12_out), .Q(D12), .clk(Clock));  // open: clr
  Register #(.width(32), .Select("low")) register_14 (.D(Din), .en(_13_out), .Q(D13), .clk(Clock));  // open: clr
  Register #(.width(32), .Select("low")) register_15 (.D(Din), .en(_14_out), .Q(D14), .clk(Clock));  // open: clr
  Register #(.width(32), .Select("low")) register_16 (.D(Din), .en(_15_out), .Q(D15), .clk(Clock));  // open: clr
  and _16 (_16_out, dec[16], Write_Enable);
  and _17 (_17_out, dec[17], Write_Enable);
  and _18 (_18_out, dec[18], Write_Enable);
  and _19 (_19_out, dec[19], Write_Enable);
  and _20 (_20_out, dec[20], Write_Enable);
  and _21 (_21_out, dec[21], Write_Enable);
  and _22 (_22_out, dec[22], Write_Enable);
  and _23 (_23_out, dec[23], Write_Enable);
  and _24 (_24_out, dec[24], Write_Enable);
  and _25 (_25_out, dec[25], Write_Enable);
  and _26 (_26_out, dec[26], Write_Enable);
  and _27 (_27_out, dec[27], Write_Enable);
  and _28 (_28_out, dec[28], Write_Enable);
  and _29 (_29_out, dec[29], Write_Enable);
  and _30 (_30_out, dec[30], Write_Enable);
  and _31 (_31_out, dec[31], Write_Enable);
  Register #(.width(32), .Select("low")) register_17 (.D(Din), .en(_16_out), .Q(D16), .clk(Clock));  // open: clr
  Register #(.width(32), .Select("low")) register_18 (.D(Din), .en(_17_out), .Q(D17), .clk(Clock));  // open: clr
  Register #(.width(32), .Select("low")) register_19 (.D(Din), .en(_18_out), .Q(D18), .clk(Clock));  // open: clr
  Register #(.width(32), .Select("low")) register_20 (.D(Din), .en(_19_out), .Q(D19), .clk(Clock), .clr(undriven_3));
  Register #(.width(32), .Select("low")) register_21 (.D(Din), .en(_20_out), .Q(D20), .clk(Clock));  // open: clr
  Register #(.width(32), .Select("low")) register_22 (.D(Din), .en(_21_out), .Q(D21), .clk(Clock));  // open: clr
  Register #(.width(32), .Select("low")) register_23 (.D(Din), .en(_22_out), .Q(D22), .clk(Clock));  // open: clr
  Register #(.width(32), .Select("low")) register_24 (.D(Din), .en(_23_out), .Q(D23), .clk(Clock));  // open: clr
  Register #(.width(32), .Select("low")) register_25 (.D(Din), .en(_24_out), .Q(D24), .clk(Clock));  // open: clr
  Register #(.width(32), .Select("low")) register_26 (.D(Din), .en(_25_out), .Q(D25), .clk(Clock));  // open: clr
  Register #(.width(32), .Select("low")) register_27 (.D(Din), .en(_26_out), .Q(D26), .clk(Clock));  // open: clr
  Register #(.width(32), .Select("low")) register_28 (.D(Din), .en(_27_out), .Q(D27), .clk(Clock), .clr(undriven_4));
  Register #(.width(32), .Select("low")) register_29 (.D(Din), .en(_28_out), .Q(D28), .clk(Clock));  // open: clr
  Register #(.width(32), .Select("low")) register_30 (.D(Din), .en(_29_out), .Q(D29), .clk(Clock));  // open: clr
  Register #(.width(32), .Select("low")) register_31 (.D(Din), .en(_30_out), .Q(D30), .clk(Clock));  // open: clr
  Register #(.width(32), .Select("low")) register_32 (.D(Din), .en(_31_out), .Q(D31), .clk(Clock));  // open: clr
  Multiplexer #(.select(5), .width(32), .enable("false")) multiplexer_1 (
    .in0(D0), .in1(D1), .in2(D2), .in3(D3), .in4(D4), .in5(D5), .in6(D6), .in7(D7), .in8(D8), .in9(D9),
    .in10(D10), .in11(D11), .in12(D12), .in13(D13), .in14(D14), .in15(D15), .in16(D16), .in17(D17),
    .in18(D18), .in19(D19), .in20(D20), .in21(D21), .in22(D22), .in23(D23), .in24(D24), .in25(D25),
    .in26(D26), .in27(D27), .in28(D28), .in29(D29), .in30(D30), .in31(D31), .out(Reg1Out), .sel(R1_num));
  Multiplexer #(.select(5), .width(32), .enable("false")) multiplexer_2 (
    .in0(D0), .in1(D1), .in2(D2), .in3(D3), .in4(D4), .in5(D5), .in6(D6), .in7(D7), .in8(D8), .in9(D9),
    .in10(D10), .in11(D11), .in12(D12), .in13(D13), .in14(D14), .in15(D15), .in16(D16), .in17(D17),
    .in18(D18), .in19(D19), .in20(D20), .in21(D21), .in22(D22), .in23(D23), .in24(D24), .in25(D25),
    .in26(D26), .in27(D27), .in28(D28), .in29(D29), .in30(D30), .in31(D31), .out(Reg2Out), .sel(R2_num));

  // Other names for the same wires on the sheet: CLK = Clock; RA[4:0] = R1_num; RB[4:0] = R2_num; RDA[31:0] = Reg1Out;
  //   RDB[31:0] = Reg2Out; RW[4:0] = Write_Reg_num; WE = Write_Enable

  // Notes on the sheet:
  //   输入引脚
  //   电路功能：实现寄存器堆功能，实现0-31号寄存器。写使能有效且时钟边沿有效后写入数据，随时读出双口数据
  //   输出引脚
endmodule

module \数据存储器  (
  input  [15:0] Addr,
  input  [31:0] Din,
  input  CLK,
  input  CLR,
  input  [2:0] MemOp,
  input  WE,
  input  SEL,
  output [31:0] DataOut
);

  wire _1b_out, _2b_out, _4b_out, and_1_out, and_2_out, and_3_out, or_1_out, or_2_out;
  wire [7:0] HIGH_data, LOW_data, ram_1_data, ram_2_data;
  wire [31:0] bit_extender_1_out, bit_extender_2_out, bit_extender_3_out, bit_extender_4_out,
       multiplexer_1_out, multiplexer_2_out;

  and and_1 (and_1_out, WE, or_1_out);
  or or_1 (or_1_out, _4b_out, _1b_out, _2b_out);
  and _4b (_4b_out, ~MemOp[0], ~MemOp[1]);  // AND_Gate
  and _1b (_1b_out, MemOp[0], ~MemOp[1]);  // AND_Gate
  and _2b (_2b_out, ~MemOp[0], MemOp[1]);  // AND_Gate
  RAM #(.addrWidth(16), .bus("separate"), .Select("high"), .simpleMode("false")) LOW (
    .addr(Addr), .din(Din[7:0]), .data(LOW_data), .str(and_1_out), .sel(SEL), .clk(CLK), .clr(CLR));  // open: ld
  assign bit_extender_1_out = {{24{1'b0}}, LOW_data};  // Bit_Extender bit_extender_1
  assign bit_extender_2_out = {{24{LOW_data[7]}}, LOW_data};  // Bit_Extender bit_extender_2
  and and_2 (and_2_out, WE, or_2_out);
  or or_2 (or_2_out, _4b_out, _2b_out);
  Multiplexer #(.width(32), .enable("false")) multiplexer_1 (
    .in0(bit_extender_1_out), .in1(bit_extender_2_out), .out(multiplexer_1_out), .sel(MemOp[2]));
  RAM #(.addrWidth(16), .bus("separate"), .Select("high"), .simpleMode("false")) ram_1 (
    .addr(Addr), .din(Din[15:8]), .data(ram_1_data), .str(and_2_out), .sel(SEL), .clk(CLK), .clr(CLR));  // open: ld
  and and_3 (and_3_out, WE, _4b_out);
  assign bit_extender_3_out = {{16{1'b0}}, {ram_1_data, LOW_data}};  // Bit_Extender bit_extender_3
  Multiplexer #(.width(32), .enable("false")) multiplexer_2 (
    .in0(bit_extender_3_out), .in1(bit_extender_4_out), .out(multiplexer_2_out), .sel(MemOp[2]));
  assign bit_extender_4_out = {{16{ram_1_data[7]}}, {ram_1_data, LOW_data}};  // Bit_Extender bit_extender_4
  RAM #(.addrWidth(16), .bus("separate"), .Select("high"), .simpleMode("false")) ram_2 (
    .addr(Addr), .din(Din[23:16]), .data(ram_2_data), .str(and_3_out), .sel(SEL), .clk(CLK), .clr(CLR));  // open: ld
  RAM #(.addrWidth(16), .bus("separate"), .Select("high"), .simpleMode("false")) HIGH (
    .addr(Addr), .din(Din[31:24]), .data(HIGH_data), .str(and_3_out), .sel(SEL), .clk(CLK), .clr(CLR));  // open: ld
  Multiplexer #(.select(2), .width(32), .enable("false")) multiplexer_3 (
    .in0({HIGH_data, ram_2_data, ram_1_data, LOW_data}), .in1(multiplexer_1_out), .in2(multiplexer_2_out),
    .in3({32{1'b0}}), .out(DataOut), .sel(MemOp[1:0]));

  // Other names for the same wires on the sheet: Dout[31:0] = DataOut

  // Notes on the sheet:
  //   输入引脚区
  //   32位数据存储器，按字节分4片存储，可按照字节、半字和字进行存储；读取字节或半字时，支持0扩展和符号位扩展。
  //   为了后续实验中的引用，不要修改MemOp的编码定义，以及引脚名称和在布局图中位置。
  //   输出引脚区
endmodule

module DataPath (
  input  [2:0] ExtOp,
  input  [2:0] MemOp,
  input  RegWr,
  input  ALUASrc,
  input  MemWr,
  input  [1:0] ALUBSrc,
  input  [31:0] Initial_Address,
  input  [3:0] ALUctr,
  input  MemToReg,
  input  [2:0] Branch,
  input  Halt,
  output [6:0] OpCode,
  output [2:0] Funct3,
  output [6:0] Funct7
);

  wire alu_1_zero, branch_1_nxtasrc, branch_1_nxtbsrc, clk, RESET;
  wire [0:0] alu_1_s;
  wire [30:0] alu_1_s_2;
  wire [31:0] idu_1_busa, idu_1_busb, idu_1_dataa, idu_1_datab, idu_1_imm, ifu_1_pc, multiplexer_1_out,
       \指令存储器_data , \数据存储器_1_dataout ;

  Clock clock_1 (.out(clk));
  Button u_Reset (.out(RESET));
  IFU ifu_1 (
    .PC(ifu_1_pc), .Initial_Address(Initial_Address), .BusA(idu_1_busa), .Halt(Halt),
    .NxtASrc(branch_1_nxtasrc), .NxtBSrc(branch_1_nxtbsrc), .Imm(idu_1_imm), .CLK(clk), .Reset(RESET));
  ROM #(.addrWidth(16), .dataWidth(32), .Select("high")) \u_指令存储器  (
    .addr(ifu_1_pc[17:2]), .data(\指令存储器_data ), .sel(1'b1));
  IDU idu_1 (
    .ExtOp(ExtOp), .RegWr(RegWr), .OpCode(OpCode), .ALUASrc(ALUASrc), .ALUBSrc(ALUBSrc), .Funct3(Funct3),
    .Funct7(Funct7), .IR(\指令存储器_data ), .BusW(multiplexer_1_out), .PC(ifu_1_pc), .DataA(idu_1_dataa),
    .BusB(idu_1_busb), .DataB(idu_1_datab), .Imm(idu_1_imm), .BusA(idu_1_busa), .CLK(clk));
  ALU alu_1 (.A(idu_1_dataa), .B(idu_1_datab), .S({alu_1_s_2, alu_1_s[0]}), .ALUctr(ALUctr), .Zero(alu_1_zero));
  Branch branch_1 (
    .Branch(Branch), .NxtASrc(branch_1_nxtasrc), .Zero(alu_1_zero), .NxtBSrc(branch_1_nxtbsrc),
    .Result0(alu_1_s[0]));
  \数据存储器  \u_数据存储器_1  (
    .Addr(alu_1_s_2[16:1]), .Din(idu_1_busb), .DataOut(\数据存储器_1_dataout ), .CLK(clk), .CLR(1'b0),
    .MemOp(MemOp), .WE(MemWr), .SEL(1'b1));
  Multiplexer #(.width(32), .enable("false")) multiplexer_1 (
    .in0({alu_1_s_2, alu_1_s[0]}), .in1(\数据存储器_1_dataout ), .out(multiplexer_1_out), .sel(MemToReg));

  // Other names for the same wires on the sheet: Init_Addr[31:0] = Initial_Address; op[6:0] = OpCode

  // Notes on the sheet:
  //   ALUBSrc: pull=down
  //   ExtOp: pull=down
  //   Branch: pull=down
  //   Halt: pull=down
  //   ALUASrc: pull=down
  //   RegWr: pull=down
  //   ALUctr: pull=down
  //   contents of 指令存储器 (hex, n*v repeats v):
  //   fffff2b7 6428293 502023 4032d313 602223 401383 fff3c413 802423 7424b3 902623 fc049ce3 3000567 a02823
  //   64597
  //   输入信号
  //   数据通路设计，提示指令存储器和数据存储器数据位32位，编址以字为单位，地址信号低2位舍弃。
  //   输出信号
endmodule

module Branch (
  input  [2:0] Branch,
  input  Zero,
  input  Result0,
  output NxtASrc,
  output NxtBSrc
);

  wire not_1_out, or_1_out;

  not not_1 (not_1_out, Zero);
  or or_1 (or_1_out, Zero, ~Result0);  // OR_Gate
  Multiplexer #(.select(3), .enable("false")) multiplexer_1 (
    .in0(1'b0), .in1(1'b0), .in2(1'b1), .in3(1'b0), .in4(1'b0), .in5(1'b0), .in6(1'b0), .in7(1'b0),
    .out(NxtASrc), .sel(Branch));
  Multiplexer #(.select(3), .enable("false")) multiplexer_2 (
    .in0(1'b0), .in1(1'b1), .in2(1'b1), .in3(1'b0), .in4(Zero), .in5(not_1_out), .in6(Result0),
    .in7(or_1_out), .out(NxtBSrc), .sel(Branch));

  // Notes on the sheet:
  //   Zero: pull=down
  //   Branch: pull=down
  //   输入信号
  //   输出信号
endmodule
