// Logisim project lab6(hwr).circ as structural Verilog: 2 circuits, main circuit 单周期CPU
module \单周期CPU  (
  input  [31:0] Initial_Address,
  output halt
);

  wire alu_1_zero, branch_1_nxtasrc, branch_1_nxtbsrc, clk, clock_2_out, Halt0, not_1_out, or_1_out, RESET,
       \控制器_1_aluasrc , \控制器_1_memtoreg , \控制器_1_memwr , \控制器_1_regwr ;
  wire [1:0] \控制器_1_alubsrc ;
  wire [2:0] func3, \控制器_1_branch , \控制器_1_extop , \控制器_1_memop ;
  wire [3:0] \控制器_1_aluctr ;
  wire [6:0] func7, opcode;
  wire [15:0] counter_1_q;
  wire [31:0] alu_1_s, idu_1_busa, idu_1_busb, idu_1_dataa, idu_1_datab, idu_1_imm, ifu_1_pc, IR,
       multiplexer_1_out, \数据存储器_1_dataout ;

  IFU ifu_1 (
    .PC(ifu_1_pc), .Initial_Address(Initial_Address), .BusA(idu_1_busa), .Halt(halt),
    .NxtASrc(branch_1_nxtasrc), .NxtBSrc(branch_1_nxtbsrc), .Imm(idu_1_imm), .CLK(clk), .Reset(RESET));
  Clock clock_1 (.out(clk));
  Button u_Reset (.out(RESET));
  ROM #(.addrWidth(16), .dataWidth(32), .Select("high")) \u_指令存储器  (.addr(ifu_1_pc[17:2]), .data(IR), .sel(1'b1));
  \控制器  \u_控制器_1  (
    .funct3(func3), .opcode(opcode), .Branch(\控制器_1_branch ), .MemOp(\控制器_1_memop ),
    .ALUASrc(\控制器_1_aluasrc ), .ALUBSrc(\控制器_1_alubsrc ), .ALUctr(\控制器_1_aluctr ),
    .MemtoReg(\控制器_1_memtoreg ), .RegWr(\控制器_1_regwr ), .MemWr(\控制器_1_memwr ), .ExtOp(\控制器_1_extop ),
    .funct7(func7), .halt(halt));
  IDU idu_1 (
    .ExtOp(\控制器_1_extop ), .RegWr(\控制器_1_regwr ), .OpCode(opcode), .ALUASrc(\控制器_1_aluasrc ),
    .ALUBSrc(\控制器_1_alubsrc ), .Funct3(func3), .Funct7(func7), .IR(IR), .BusW(multiplexer_1_out),
    .PC(ifu_1_pc), .DataA(idu_1_dataa), .BusB(idu_1_busb), .DataB(idu_1_datab), .Imm(idu_1_imm),
    .BusA(idu_1_busa), .CLK(clk));
  ALU alu_1 (.A(idu_1_dataa), .B(idu_1_datab), .S(alu_1_s), .ALUctr(\控制器_1_aluctr ), .Zero(alu_1_zero));
  or or_1 (or_1_out, halt, Halt0);
  Comparator #(.width(32)) comparator_1 (.a(IR), .b(32'h6f), .eq(Halt0));  // open: gt, lt
  // Probe on counter_1_q
  Counter #(.width(16), .max('hffff), .behavior("old")) counter_1 (
    .count(not_1_out), .Q(counter_1_q), .clk(clock_2_out), .clr(RESET));  // open: load, D, carry, preset
  not not_1 (not_1_out, or_1_out);
  Clock clock_2 (.out(clock_2_out));
  Branch branch_1 (
    .Branch(\控制器_1_branch ), .NxtASrc(branch_1_nxtasrc), .Zero(alu_1_zero), .NxtBSrc(branch_1_nxtbsrc),
    .Result0(alu_1_s[0]));
  \数据存储器  \u_数据存储器_1  (
    .Addr(alu_1_s[17:2]), .Din(idu_1_busb), .DataOut(\数据存储器_1_dataout ), .CLK(clk), .CLR(RESET),
    .MemOp(\控制器_1_memop ), .WE(\控制器_1_memwr ), .SEL(1'b1));
  Multiplexer #(.width(32), .enable("false")) multiplexer_1 (
    .in0(alu_1_s), .in1(\数据存储器_1_dataout ), .out(multiplexer_1_out), .sel(\控制器_1_memtoreg ));

  // Other names for the same wires on the sheet: Init_Addr[31:0] = Initial_Address

  // Notes on the sheet:
  //   输入信号
  //   RV32I单周期CPU设计
  //   contents of 指令存储器 (hex, n*v repeats v):
  //   413 9117 ffc10113 10c000ef 50463 8067 ff010113 100513 112623 ec000ef 13400513 4c50613 1300593 50793
  //   2b05063 7a703 47a683 e6d663 d7a023 e7a223 478793 fec794e3 fff58593 ffc60793 a60663 78613 fcdff06f
  //   8067 fe010113 912a23 812c23 1212823 1312623 112e23 13400913 f9dff0ef 13400493 413 1400993 4a503
  //   448493 40850533 153513 140413 f61ff0ef ff3414e3 100513 f55ff0ef 413 f65ff0ef 1400493 92503 490913
  //   40850533 153513 140413 f31ff0ef fe9414e3 100513 f25ff0ef 1c12083 1812403 1412483 1012903 c12983 513
  //   2010113 8067 18a02223 6f ff010113 13000513 112623 f4dff0ef 18a02223 6f 0 c8 4bc c2a 4c 391 145f 220c
  //   38e 7530 4650 1e1f be 27 15 57 997 190 21 320 aa deadbeef
  //   输出信号
  //   程序执行周期数
endmodule

module \控制器  (
  input  [6:0] opcode,
  input  [2:0] funct3,
  input  [6:0] funct7,
  output [2:0] ExtOp,
  output RegWr,
  output ALUASrc,
  output [1:0] ALUBSrc,
  output [3:0] ALUctr,
  output [2:0] Branch,
  output MemtoReg,
  output [2:0] MemOp,
  output MemWr,
  output halt
);

  wire and_1_out, and_2_out, and_3_out, and_4_out, and_5_out, and_6_out, and_7_out, and_8_out, and_9_out,
       and_10_out, and_11_out, and_12_out, and_13_out, and_14_out, and_15_out, I_Arith, J_jalr, or_1_out,
       R_Arith, U_auipc, U_lui;

  Comparator #(.width(7)) comparator_1 (.a(opcode), .b(7'b0110111), .eq(U_lui));  // open: gt, lt
  Comparator #(.width(7)) comparator_2 (.a(opcode), .b(7'b1100111), .eq(J_jalr));  // open: gt, lt
  Comparator #(.width(7)) comparator_3 (.a(opcode), .b(7'b0010111), .eq(U_auipc));  // open: gt, lt
  Comparator #(.width(7)) comparator_4 (.a(opcode), .b(7'b1100011), .eq(Branch[2]));  // open: gt, lt
  Comparator #(.width(7)) comparator_5 (.a(opcode), .b(7'b0010011), .eq(I_Arith));  // open: gt, lt
  Comparator #(.width(7)) comparator_6 (.a(opcode), .b(7'b0000011), .eq(MemtoReg));  // open: gt, lt
  and and_1 (and_1_out, Branch[2], ~funct3[1], funct3[0]);  // AND_Gate
  and and_2 (and_2_out, Branch[2], funct3[2], funct3[1], funct3[0]);
  or or_1 (or_1_out, I_Arith, R_Arith);
  Comparator #(.width(7)) comparator_7 (.a(opcode), .b(7'b0110011), .eq(R_Arith));  // open: gt, lt
  Comparator #(.width(7)) comparator_8 (.a(opcode), .b(7'b0100011), .eq(MemWr));  // open: gt, lt
  or or_2 (ALUBSrc[1], U_lui, U_auipc, I_Arith, MemtoReg, MemWr);
  or or_3 (ALUBSrc[0], ExtOp[2], J_jalr);
  or or_4 (ExtOp[1], Branch[2], MemWr);
  or or_5 (ExtOp[0], U_lui, U_auipc, Branch[2]);
  or or_6 (Branch[1], J_jalr, and_3_out);
  and and_3 (and_3_out, Branch[2], funct3[2]);
  or or_7 (Branch[0], ExtOp[2], and_1_out, and_2_out);
  or or_8 (RegWr, U_lui, U_auipc, ExtOp[2], J_jalr, I_Arith, R_Arith, MemtoReg);
  or or_9 (ALUASrc, U_auipc, ExtOp[2], J_jalr);
  and and_4 (and_4_out, I_Arith, funct7[5], funct3[0], ~funct3[1], funct3[2]);  // AND_Gate
  and and_5 (and_5_out, R_Arith, funct7[5]);
  and and_6 (and_6_out, or_1_out, funct3[2]);
  and and_7 (and_7_out, or_1_out, funct3[1]);
  and and_8 (and_8_out, Branch[2], funct3[1]);
  and and_9 (and_9_out, or_1_out, funct3[0]);
  and and_10 (and_10_out, MemtoReg, ~funct3[2], ~funct3[1]);  // AND_Gate
  and and_11 (and_11_out, MemWr, ~funct3[2], ~funct3[1]);  // AND_Gate
  and and_12 (and_12_out, MemtoReg, ~funct3[1], funct3[0]);  // AND_Gate
  and and_13 (and_13_out, MemWr, ~funct3[2], ~funct3[1], funct3[0]);  // AND_Gate
  and and_14 (and_14_out, MemtoReg, ~funct3[1], ~funct3[0]);  // AND_Gate
  and and_15 (and_15_out, MemWr, ~funct3[2], ~funct3[1], ~funct3[0]);  // AND_Gate
  Comparator #(.width(7)) comparator_9 (.a(opcode), .b(7'b1101111), .eq(ExtOp[2]));  // open: gt, lt
  Comparator #(.width(7)) comparator_10 (.a(opcode), .b({7{1'b0}}), .eq(halt));  // open: gt, lt
  or or_10 (ALUctr[3], U_lui, and_4_out, and_5_out);
  or or_11 (ALUctr[2], U_lui, and_6_out);
  or or_12 (ALUctr[1], U_lui, Branch[2], and_7_out);
  or or_13 (ALUctr[0], U_lui, and_8_out, and_9_out);
  or or_14 (MemOp[2], and_10_out, and_11_out);
  or or_15 (MemOp[1], and_12_out, and_13_out);
  or or_16 (MemOp[0], and_14_out, and_15_out);

  // Other names for the same wires on the sheet: B_Instr = Branch[2]; J_jal = ExtOp[2]; I_load = MemtoReg;
  //   S_Instr = MemWr

  // Notes on the sheet:
  //   输入信号
  //   提示：根据指令种类和代码，把7位指令code用一位标志位来表示。
  //   输出信号
endmodule
