// Logisim project 3.circ as structural Verilog
module _2_1MUX_hazard (
  input  D0,
  input  D1,
  input  S,
  output F
);

  wire AND1_out, AND2_out, not_1_out;

  not not_1 (not_1_out, S);
  // Probe on S
  // Probe on not_1_out
  and AND1 (AND1_out, D0, not_1_out);
  and AND2 (AND2_out, D1, S);
  \或门  \u_或门_1  (.X(AND1_out), .Y(AND2_out), .z(F));

  // Notes on the sheet:
  //   Probe1
  //   Probe2
  //   OR
endmodule

module \或门  (
  input  X,
  input  Y,
  output z
);

  wire transistor_1_out, transistor_2_out;

  Transistor transistor_1 (.in(1'b1), .out(transistor_1_out), .gate(X));
  Transistor transistor_2 (.in(transistor_1_out), .out(transistor_2_out), .gate(Y));
  Transistor #(.\type ("n")) transistor_3 (.in(1'b0), .out(transistor_2_out), .gate(X));
  Transistor #(.\type ("n")) transistor_4 (.in(1'b0), .out(transistor_2_out), .gate(Y));
  Transistor transistor_5 (.in(1'b1), .out(z), .gate(transistor_2_out));
  Transistor #(.\type ("n")) transistor_6 (.in(1'b0), .out(z), .gate(transistor_2_out));

  // Notes on the sheet:
  //   Q2
  //   Q4
  //   Q1
  //   或门实现电路
  //   Q3
  //   Q6
  //   Q5
endmodule

module _2_1MUX (
  input  D0,
  input  D1,
  input  S,
  output Y
);

  wire transistor_1_out;

  Transistor transistor_1 (.in(1'b1), .out(transistor_1_out), .gate(S));
  Transistor #(.\type ("n")) transistor_2 (.in(1'b0), .out(transistor_1_out), .gate(S));
  // Transmission_Gate transmission_1: pin names not known; wires that end beside it: D0, S, transistor_1_out, Y
  // Transmission_Gate transmission_2: pin names not known; wires that end beside it: D1, transistor_1_out, S, Y

  // Notes on the sheet:
  //   2选1多路选择器
endmodule

module _4_1MUX (
  input  [15:0] INPUT,
  input  [1:0] SELECT,
  output [3:0] OUTPUT
);

  wire [3:0] multiplexer_1_out, multiplexer_2_out;

  Multiplexer #(.width(4), .enable("false")) multiplexer_1 (
    .in0(INPUT[3:0]), .in1(INPUT[7:4]), .out(multiplexer_1_out), .sel(SELECT[0]));
  Multiplexer #(.width(4), .enable("false")) multiplexer_2 (
    .in0(INPUT[11:8]), .in1(INPUT[15:12]), .out(multiplexer_2_out), .sel(SELECT[0]));
  Multiplexer #(.width(4), .enable("false")) multiplexer_3 (
    .in0(multiplexer_1_out), .in1(multiplexer_2_out), .out(OUTPUT), .sel(SELECT[1]));

  // Other names for the same wires on the sheet: DATA[15:0] = INPUT; S[1:0] = SELECT; Y[3:0] = OUTPUT
endmodule

module \奇偶  (
  input  N0,
  input  N1,
  input  N2,
  input  N3,
  output EVEN,
  output ODD
);

  wire xor_1_out, xor_2_out;

  xor xor_1 (xor_1_out, N0, N1);
  xor xor_2 (xor_2_out, N2, N3);
  xor xor_3 (EVEN, xor_1_out, xor_2_out);
  not not_1 (ODD, EVEN);
endmodule

module \_4路选择器  (
  input  [3:0] INPUT,
  input  [1:0] SELECT,
  output out_3
);

  wire n2_1mux_1_y, n2_1mux_2_y;

  _2_1MUX u_2_1mux_1 (.D0(INPUT[0]), .D1(INPUT[1]), .S(SELECT[0]), .Y(n2_1mux_1_y));
  _2_1MUX u_2_1mux_2 (.D0(INPUT[2]), .D1(INPUT[3]), .S(SELECT[0]), .Y(n2_1mux_2_y));
  _2_1MUX u_2_1mux_3 (.D0(n2_1mux_1_y), .D1(n2_1mux_2_y), .S(SELECT[1]), .Y(out_3));

  // Other names for the same wires on the sheet: DATA[3:0] = INPUT; S[1:0] = SELECT; Y = out_3

  // Notes on the sheet:
  //   4选1多路选择器
endmodule
