// Logisim project 8位桶.circ as structural Verilog: 2 circuits, main circuit main
module main (
  input  [7:0] DataIn,
  input  [2:0] shamt,
  input  L_R,
  input  A_L,
  output [7:0] DataOut
);

  wire [7:0] multiplexer_2_out, multiplexer_3_out;
  wire [7:7] multiplexer_1_out;

  Multiplexer #(.enable("false")) multiplexer_1 (.in0(1'b0), .in1(DataIn[7]), .out(multiplexer_1_out[7]), .sel(A_L));
  Multiplexer #(.select(2), .width(8), .enable("false")) multiplexer_2 (
    .in0(DataIn), .in1({multiplexer_1_out[7], DataIn[7:1]}), .in2(DataIn), .in3({DataIn[6:0], 1'b0}),
    .out(multiplexer_2_out), .sel({L_R, shamt[0]}));
  Multiplexer #(.select(2), .width(8), .enable("false")) multiplexer_3 (
    .in0(multiplexer_2_out), .in1({{2{multiplexer_1_out[7]}}, multiplexer_2_out[7:2]}),
    .in2(multiplexer_2_out), .in3({multiplexer_2_out[5:0], 2'b00}), .out(multiplexer_3_out),
    .sel({L_R, shamt[1]}));
  Multiplexer #(.select(2), .width(8), .enable("false")) multiplexer_4 (
    .in0(multiplexer_3_out), .in1({{4{multiplexer_1_out[7]}}, multiplexer_3_out[7:4]}),
    .in2(multiplexer_3_out), .in3({multiplexer_3_out[3:0], 4'b0000}), .out(DataOut), .sel({L_R, shamt[2]}));

  // Other names for the same wires on the sheet: Din[7:0] = DataIn; Left_Right = L_R; Arth_Logic = A_L;
  //   Dout[7:0] = DataOut

  // Notes on the sheet:
  //   输入信号
  //   L/R=0：右移；=1：左移
  //   右移
  //   左移
  //   A/L=0：逻辑右移；=1：算术右移
  //   8位桶形移位器
  //   输出信号
endmodule

module \LED矩阵  (
);

  DotMatrix #(.inputtype("row"), .matrixcols(16), .matrixrows(16)) dotmatrix_1 (
    .row0({16{1'b0}}), .row1(16'h1c0), .row2(16'h1c0), .row3(16'h7fff), .row4(16'h1c0), .row5(16'h7fff),
    .row6(16'h7007), .row7(16'h7777), .row8(16'h7367), .row9(16'h7fff), .row10(16'h71c7), .row11(16'h7fff),
    .row12(16'h71c7), .row13(16'h71c7), .row14(16'h71df), .row15(16'h700c));
  DotMatrix #(.inputtype("row"), .matrixcols(16), .matrixrows(16)) dotmatrix_2 (
    .row0({16{1'b0}}), .row1(16'h1c0), .row2(16'h1c0), .row3(16'h1c0), .row4(16'h1c0), .row5(16'h7fff),
    .row6(16'h7fff), .row7(16'h1c0), .row8(16'h1e0), .row9(16'h3e0), .row10(16'h3f0), .row11(16'h738),
    .row12(16'he3c), .row13(16'h1c1e), .row14(16'h3807), .row15({16{1'b0}}));
endmodule
