// Logisim project lab2（实验4之后）.circ as structural Verilog: 9 circuits, main circuit 3-8译码器
module \_3_8译码器  (
  input  G1,
  input  G2A_L,
  input  G2B_L,
  input  A,
  input  B,
  input  C,
  output Y0_L,
  output Y1_L,
  output Y2_L,
  output Y3_L,
  output Y4_L,
  output Y5_L,
  output Y6_L,
  output Y7_L
);


  // Notes on the sheet:
  //   3-8译码器
endmodule

module \_8_3优先级编码器  (
  input  I0,
  input  I1,
  input  I2,
  input  I3,
  input  I4,
  input  I5,
  input  I6,
  input  I7
);

  Hex_Digit_Display hex_digit_display_1 ();  // open: value, dp

  // Notes on the sheet:
  //   8-3优先级编码器
endmodule

module \全加器  (
  input  A,
  input  B,
  input  Cin,
  output F,
  output Cout
);


  // Notes on the sheet:
  //   全加器
endmodule

module \_4位串行加法器  (
  input  [3:0] X,
  input  [3:0] Y,
  input  Cin,
  output [3:0] F,
  output Cout
);

  Hex_Digit_Display hex_digit_display_1 ();  // open: value, dp
  Hex_Digit_Display hex_digit_display_2 ();  // open: value, dp
  Hex_Digit_Display hex_digit_display_3 ();  // open: value, dp

  // Other names for the same wires on the sheet: 操作数x[3:0] = X; 操作数y[3:0] = Y; 运算结果[3:0] = F

  // Notes on the sheet:
  //   输入
  //   +
  //   输出
  //   4位串行进位加法器
  //   =
endmodule

module \_1位ALU  (
  input  A,
  input  B,
  input  S3,
  input  S2,
  input  S1,
  output F
);


  // Notes on the sheet:
  //   1位ALU
endmodule

module \_4位奇偶校验器  (
  input  N0,
  input  N1,
  input  N2,
  input  N3,
  output EVEN
);

  wire xor_1_out, xor_2_out;

  xor xor_1 (xor_1_out, N0, N1);
  xor xor_2 (xor_2_out, N2, N3);
  xor xor_3 (EVEN, xor_1_out, xor_2_out);

  // Notes on the sheet:
  //   4位奇偶校验电路
endmodule

module \_7位汉明码纠错电路  (
  input  [6:0] X,
  output [6:0] F,
  output OK,
  output Error
);

  wire decoder_1_out1, decoder_1_out2, decoder_1_out3, decoder_1_out4, decoder_1_out5, decoder_1_out6,
       decoder_1_out7;
  wire [2:0] \n4位奇偶校验器_1_even ;
  wire [3:0] \错误位 ;

  \_4位奇偶校验器  \u_4位奇偶校验器_1  (.N0(X[0]), .N1(X[5]), .N2(X[4]), .N3(X[6]), .EVEN(\n4位奇偶校验器_1_even [0]));
  \_4位奇偶校验器  \u_4位奇偶校验器_2  (.N0(X[1]), .N1(X[5]), .N2(X[5]), .N3(X[6]), .EVEN(\n4位奇偶校验器_1_even [1]));
  \_4位奇偶校验器  \u_4位奇偶校验器_3  (.N0(X[3]), .N1(X[4]), .N2(X[5]), .N3(X[6]), .EVEN(\n4位奇偶校验器_1_even [2]));
  Decoder #(.select(3), .enable("false")) decoder_1 (
    .out0(OK), .out1(decoder_1_out1), .out2(decoder_1_out2), .out3(decoder_1_out3), .out4(decoder_1_out4),
    .out5(decoder_1_out5), .out6(decoder_1_out6), .out7(decoder_1_out7), .sel(\n4位奇偶校验器_1_even ));
  assign \错误位  = {{1{1'b0}}, \n4位奇偶校验器_1_even };  // Bit_Extender bit_extender_1
  Hex_Digit_Display hex_digit_display_1 (.value(\错误位 ));  // open: dp
  xor xor_1 (F[0], X[0], decoder_1_out1);
  xor xor_2 (F[1], X[1], decoder_1_out2);
  xor xor_3 (F[2], X[5], decoder_1_out3);
  xor xor_4 (F[3], X[3], decoder_1_out4);
  xor xor_5 (F[4], X[4], decoder_1_out5);
  xor xor_6 (F[5], X[5], decoder_1_out6);
  xor xor_7 (F[6], X[6], decoder_1_out7);
  not not_1 (Error, OK);

  assign X[2] = X[5];

  // Other names for the same wires on the sheet: Input[6:0] = {X[6:3], X[5], X[1:0]}; Output[6:0] = F

  // Notes on the sheet:
  //   汉明码输入
  //   汉明码纠错输出
  //   7位汉明码纠错电路
endmodule

module \_4位加减法器  (
  input  [3:0] X,
  input  [3:0] Y,
  input  Cin,
  output [3:0] F,
  output Cout
);

  Hex_Digit_Display hex_digit_display_1 ();  // open: value, dp
  Hex_Digit_Display hex_digit_display_2 ();  // open: value, dp
  Hex_Digit_Display hex_digit_display_3 ();  // open: value, dp

  // Other names for the same wires on the sheet: 操作数x[3:0] = X; 操作数y[3:0] = Y; 运算结果[3:0] = F

  // Notes on the sheet:
  //   输入
  //   +
  //   4位加减法器
  //   输出
  //   =
endmodule

module \_8位桶形移位器  (
  input  [7:0] DataIn,
  input  [2:0] shamt,
  input  L_R,
  input  A_L,
  output [7:0] DataOut
);

  wire [1:0] undriven;

  Multiplexer #(.enable("false")) multiplexer_1 (.in0(1'b0), .sel(A_L));  // open: in1, out
  Multiplexer #(.select(2), .width(8), .enable("false")) multiplexer_2 ();  // open: in0, in1, in2, in3, out, sel
  Multiplexer #(.select(2), .width(8), .enable("false")) multiplexer_3 ();  // open: in0, in1, in2, in3, out, sel
  Multiplexer #(.select(2), .width(8), .enable("false")) multiplexer_4 (
    .out(DataOut), .sel(undriven));  // open: in0, in1, in2, in3

  // Other names for the same wires on the sheet: Arth_Logic = A_L; Din[7:0] = DataIn; Dout[7:0] = DataOut;
  //   Left_Right = L_R

  // Notes on the sheet:
  //   输入信号
  //   L/R=0：右移；=1：左移
  //   A/L=0：逻辑右移；=1：算术右移
  //   8位桶形移位器
  //   输出信号
endmodule
