// Logisim project 译码器.circ as structural Verilog
module main (
  input  G1,
  input  G2A_L,
  input  G2B_L,
  input  A,
  input  B,
  input  C,
  output Y0_L,
  output Y1_L,
  output Y2_L,
  output Y3_L,
  output Y4_L,
  output Y5_L,
  output Y6_L,
  output Y7_L
);

  wire and_1_out, not_1_out, not_2_out, not_3_out, not_4_out, not_5_out, not_6_out, not_7_out;

  not not_1 (not_1_out, G1);
  and and_1 (and_1_out, ~not_1_out, ~G2A_L, ~G2B_L);  // AND_Gate
  not not_2 (not_2_out, A);
  not not_3 (not_3_out, B);
  not not_4 (not_4_out, C);
  not not_5 (not_5_out, not_2_out);
  not not_6 (not_6_out, not_3_out);
  not not_7 (not_7_out, not_4_out);
  nand nand_1 (Y0_L, not_2_out, not_3_out, not_4_out, and_1_out);
  nand nand_2 (Y1_L, not_5_out, not_3_out, not_4_out, and_1_out);
  nand nand_3 (Y2_L, not_2_out, not_6_out, not_4_out, and_1_out);
  nand nand_4 (Y3_L, not_5_out, not_6_out, not_4_out, and_1_out);
  nand nand_5 (Y4_L, not_2_out, not_3_out, not_7_out, and_1_out);
  nand nand_6 (Y5_L, not_5_out, not_3_out, not_7_out, and_1_out);
  nand nand_7 (Y6_L, not_2_out, not_6_out, not_7_out, and_1_out);
  nand nand_8 (Y7_L, and_1_out, not_5_out, not_6_out, not_7_out);
endmodule

module \_8_3优先级编码器  (
  input  I0,
  input  I1,
  input  I2,
  input  I3,
  input  I4,
  input  I5,
  input  I6,
  input  I7,
  output O0,
  output O1,
  output O2
);

  wire and_1_out, and_2_out, and_3_out, and_4_out, and_5_out, and_6_out, and_7_out;

  and and_1 (and_1_out, ~I0, I1);  // AND_Gate
  and and_2 (and_2_out, ~I0, ~I1, I2);  // AND_Gate
  and and_3 (and_3_out, ~I0, ~I1, ~I2, I3);  // AND_Gate
  and and_4 (and_4_out, ~I0, ~I1, ~I2, ~I3, I4);  // AND_Gate
  and and_5 (and_5_out, ~I0, ~I1, ~I2, ~I3, ~I4, I5);  // AND_Gate
  and and_6 (and_6_out, ~I0, ~I1, ~I2, ~I3, ~I4, ~I5, I6);  // AND_Gate
  and and_7 (and_7_out, ~I0, ~I1, ~I2, ~I3, ~I4, ~I5, ~I6, I7);  // AND_Gate
  or or_1 (O0, and_4_out, and_5_out, and_6_out, and_7_out);
  or or_2 (O1, and_2_out, and_3_out, and_6_out, and_7_out);
  or or_3 (O2, and_1_out, and_3_out, and_5_out, and_7_out);
  Hex_Digit_Display hex_digit_display_1 (.value({1'b0, O0, O1, O2}));  // open: dp
endmodule

module \全加器  (
  input  A,
  input  B,
  input  Cin,
  output F,
  output Cout
);

  wire and_1_out, and_2_out, and_3_out;

  xor xor_1 (F, A, B, Cin);
  and and_1 (and_1_out, A, B);
  and and_2 (and_2_out, B, Cin);
  and and_3 (and_3_out, A, Cin);
  or or_1 (Cout, and_1_out, and_2_out, and_3_out);
endmodule

module \_4位串行进位加法器  (
  input  [3:0] x,
  input  [3:0] y,
  input  Cin,
  output [3:0] F,
  output Cout
);

  wire \全加器_1_cout , \全加器_2_cout , \全加器_3_cout ;

  Hex_Digit_Display hex_digit_display_1 (.value(x));  // open: dp
  Hex_Digit_Display hex_digit_display_2 (.value(y));  // open: dp
  Hex_Digit_Display hex_digit_display_3 (.value(F));  // open: dp
  \全加器  \u_全加器_1  (.A(x[0]), .B(y[0]), .Cin(Cin), .F(F[0]), .Cout(\全加器_1_cout ));
  \全加器  \u_全加器_2  (.A(x[1]), .B(y[1]), .Cin(\全加器_1_cout ), .F(F[1]), .Cout(\全加器_2_cout ));
  \全加器  \u_全加器_3  (.A(x[2]), .B(y[2]), .Cin(\全加器_2_cout ), .F(F[2]), .Cout(\全加器_3_cout ));
  \全加器  \u_全加器_4  (.A(x[3]), .B(y[3]), .Cin(\全加器_3_cout ), .F(F[3]), .Cout(Cout));

  // Other names for the same wires on the sheet: 操作数x[3:0] = x; 操作数y[3:0] = y; 运算结果[3:0] = F

  // Notes on the sheet:
  //   +
  //   =
endmodule

module \_4位加减法器  (
  input  [3:0] x,
  input  [3:0] y,
  input  Cin,
  output [3:0] F,
  output Cout,
  output \ZF_零 ,
  output \OF_溢出 ,
  output \SF_符号 ,
  output \CF_进_借位 
);

  wire \全加器_1_cout , \全加器_2_cout , \全加器_3_cout ;
  wire [3:0] multiplexer_1_out, not_1_out;

  Multiplexer #(.width(4), .enable("false")) multiplexer_1 (
    .in0(y), .in1(not_1_out), .out(multiplexer_1_out), .sel(Cin));
  assign not_1_out = ~y;  // NOT_Gate not_1, 4 bits wide
  Hex_Digit_Display hex_digit_display_1 (.value(x));  // open: dp
  Hex_Digit_Display hex_digit_display_2 (.value(y));  // open: dp
  \全加器  \u_全加器_1  (.A(x[0]), .B(multiplexer_1_out[0]), .Cin(Cin), .F(F[0]), .Cout(\全加器_1_cout ));
  \全加器  \u_全加器_2  (.A(x[1]), .B(multiplexer_1_out[1]), .Cin(\全加器_1_cout ), .F(F[1]), .Cout(\全加器_2_cout ));
  \全加器  \u_全加器_3  (.A(x[2]), .B(multiplexer_1_out[2]), .Cin(\全加器_2_cout ), .F(F[2]), .Cout(\全加器_3_cout ));
  \全加器  \u_全加器_4  (.A(x[3]), .B(multiplexer_1_out[3]), .Cin(\全加器_3_cout ), .F(F[3]), .Cout(Cout));
  Hex_Digit_Display hex_digit_display_3 (.value(F));  // open: dp
  xor xor_1 (\CF_进_借位 , Cout, Cin);
  nor nor_1 (\ZF_零 , F[0], F[1], F[2], F[3]);
  xor xor_2 (\OF_溢出 , \全加器_3_cout , Cout);

  assign \SF_符号  = F[3];

  // Other names for the same wires on the sheet: 操作数x[3:0] = x; 操作数y[3:0] = y; 运算结果[3:0] = F

  // Notes on the sheet:
  //   +
  //   =
endmodule
