// Logisim project lab3(hjr).circ as structural Verilog: 15 circuits, main circuit CNTR4U
module CNTR4U (
  input  CLK,
  input  LD,
  input  CLR,
  input  D0,
  input  D1,
  input  D2,
  input  D3,
  input  ENP,
  input  ENT,
  output Q0,
  output Q1,
  output Q2,
  output Q3,
  output RCO
);

  wire and_1_out, and_2_out, and_3_out, and_4_out, and_5_out, and_6_out, and_7_out, and_8_out, and_10_out,
       and_11_out, and_12_out, and_13_out, and_14_out, and_15_out, and_16_out, and_17_out, buffer_1_out,
       d_ff_1_qn, d_ff_2_qn, d_ff_3_qn, d_ff_4_qn, not_1_out, not_2_out, or_1_out, or_2_out, or_3_out,
       or_4_out, xor_1_out, xor_2_out, xor_3_out, xor_4_out;

  buf buffer_1 (buffer_1_out, CLR);
  not not_1 (not_1_out, d_ff_1_qn);
  and and_1 (and_1_out, ~d_ff_2_qn, ~d_ff_1_qn);  // AND_Gate
  and and_2 (and_2_out, ~d_ff_3_qn, ~d_ff_2_qn, ~d_ff_1_qn);  // AND_Gate
  and and_3 (and_3_out, ENP, ENT);
  and and_4 (and_4_out, LD, ~buffer_1_out);  // AND_Gate
  and and_5 (and_5_out, ~and_4_out, ~buffer_1_out);  // AND_Gate
  and and_6 (and_6_out, not_1_out, and_3_out);
  and and_7 (and_7_out, and_1_out, and_3_out);
  and and_8 (and_8_out, and_2_out, and_3_out);
  not not_2 (not_2_out, ENT);
  xor xor_1 (xor_1_out, and_3_out, ~d_ff_1_qn);  // XOR_Gate
  xor xor_2 (xor_2_out, and_6_out, ~d_ff_2_qn);  // XOR_Gate
  xor xor_3 (xor_3_out, and_7_out, ~d_ff_3_qn);  // XOR_Gate
  xor xor_4 (xor_4_out, and_8_out, ~d_ff_4_qn);  // XOR_Gate
  and and_9 (RCO, ~d_ff_4_qn, ~d_ff_3_qn, ~d_ff_2_qn, ~d_ff_1_qn, ~not_2_out);  // AND_Gate
  and and_10 (and_10_out, and_4_out, D0);
  and and_11 (and_11_out, and_5_out, xor_1_out);
  and and_12 (and_12_out, and_4_out, D1);
  and and_13 (and_13_out, and_5_out, xor_2_out);
  and and_14 (and_14_out, and_4_out, D2);
  and and_15 (and_15_out, and_5_out, xor_3_out);
  and and_16 (and_16_out, and_4_out, D3);
  and and_17 (and_17_out, and_5_out, xor_4_out);
  or or_1 (or_1_out, and_10_out, and_11_out);
  or or_2 (or_2_out, and_12_out, and_13_out);
  or or_3 (or_3_out, and_14_out, and_15_out);
  or or_4 (or_4_out, and_16_out, and_17_out);
  D_Flip_Flop #(.trigger("falling")) d_ff_1 (.clk(CLK), .D(or_1_out), .Q(Q0), .Qn(d_ff_1_qn));  // open: preset, reset
  D_Flip_Flop #(.trigger("falling")) d_ff_2 (.clk(CLK), .D(or_2_out), .Q(Q1), .Qn(d_ff_2_qn));  // open: preset, reset
  D_Flip_Flop #(.trigger("falling")) d_ff_3 (.clk(CLK), .D(or_3_out), .Q(Q2), .Qn(d_ff_3_qn));  // open: preset, reset
  D_Flip_Flop #(.trigger("falling")) d_ff_4 (.clk(CLK), .D(or_4_out), .Q(Q3), .Qn(d_ff_4_qn));  // open: preset, reset

  // Notes on the sheet:
  //   4位二进制同步计数器
endmodule

module SHRG4U (
  input  CLK,
  input  CLR,
  input  RIN,
  input  D3,
  input  D2,
  input  D1,
  input  D0,
  input  LIN,
  input  S1,
  input  S0,
  output Q3,
  output Q2,
  output Q1,
  output Q0
);

  wire _00_2_out, _00_3_out, _00_4_out, _00_out, _01_2_out, _01_3_out, _01_4_out, _01_out, _10_2_out,
       _10_3_out, _10_4_out, _10_out, _11_2_out, _11_3_out, _11_4_out, _11_out, buffer_1_out, not_1_out,
       not_2_out, not_3_out, not_4_out, not_5_out, or_1_out, or_2_out, or_3_out, or_4_out;

  not not_1 (not_1_out, S1);
  not not_2 (not_2_out, S0);
  not not_3 (not_3_out, CLK);
  buf buffer_1 (buffer_1_out, CLR);
  not not_4 (not_4_out, not_1_out);
  not not_5 (not_5_out, not_2_out);
  and _10 (_10_out, RIN, not_4_out, not_2_out);
  and _00 (_00_out, Q3, not_1_out, not_2_out);
  and _11 (_11_out, D3, not_4_out, not_5_out);
  and _01 (_01_out, Q2, not_1_out, not_5_out);
  and _10_2 (_10_2_out, Q3, not_4_out, not_2_out);
  and _00_2 (_00_2_out, Q2, not_1_out, not_2_out);
  and _11_2 (_11_2_out, D2, not_4_out, not_5_out);
  and _01_2 (_01_2_out, Q1, not_1_out, not_5_out);
  and _10_3 (_10_3_out, Q2, not_4_out, not_2_out);
  and _00_3 (_00_3_out, Q1, not_1_out, not_2_out);
  and _11_3 (_11_3_out, D1, not_4_out, not_5_out);
  and _01_3 (_01_3_out, Q0, not_1_out, not_5_out);
  and _10_4 (_10_4_out, Q1, not_4_out, not_2_out);
  and _00_4 (_00_4_out, Q0, not_1_out, not_2_out);
  and _11_4 (_11_4_out, D0, not_4_out, not_5_out);
  and _01_4 (_01_4_out, LIN, not_1_out, not_5_out);
  or or_1 (or_1_out, _10_out, _00_out, _11_out, _01_out);
  or or_2 (or_2_out, _10_2_out, _00_2_out, _11_2_out, _01_2_out);
  or or_3 (or_3_out, _10_3_out, _00_3_out, _11_3_out, _01_3_out);
  or or_4 (or_4_out, _10_4_out, _00_4_out, _11_4_out, _01_4_out);
  D_Flip_Flop #(.trigger("falling"), .NegatePresetClear("true")) d_ff_1 (
    .clk(not_3_out), .D(or_1_out), .Q(Q3), .reset(buffer_1_out));  // open: Qn, preset
  D_Flip_Flop #(.trigger("falling"), .NegatePresetClear("true")) d_ff_2 (
    .clk(not_3_out), .D(or_2_out), .Q(Q2), .reset(buffer_1_out));  // open: Qn, preset
  D_Flip_Flop #(.trigger("falling"), .NegatePresetClear("true")) d_ff_3 (
    .clk(not_3_out), .D(or_3_out), .Q(Q1), .reset(buffer_1_out));  // open: Qn, preset
  D_Flip_Flop #(.trigger("falling"), .NegatePresetClear("true")) d_ff_4 (
    .clk(not_3_out), .D(or_4_out), .Q(Q0), .reset(buffer_1_out));  // open: Qn, preset
endmodule

module \随机序列  (
  input  CLR,
  input  S1,
  input  S0
);

  wire CLK_out, xor_1_out;
  wire [3:0] shrg4u_1_q3;

  xor xor_1 (xor_1_out, shrg4u_1_q3[2], shrg4u_1_q3[3]);
  Clock CLK (.out(CLK_out));
  SHRG4U shrg4u_1 (
    .CLK(CLK_out), .CLR(CLR), .RIN(xor_1_out), .D3(1'b1), .D2(1'b0), .D1(1'b0), .D0(1'b0), .S1(S1), .S0(S0),
    .Q3(shrg4u_1_q3[0]), .Q2(shrg4u_1_q3[1]), .Q1(shrg4u_1_q3[2]), .Q0(shrg4u_1_q3[3]));  // open: LIN
  Hex_Digit_Display hex_digit_display_1 (.value(shrg4u_1_q3));  // open: dp
  // Digital_Oscilloscope #(.nState(20)) 数字示波器: pin names not known; wires that end beside it: CLK_out, shrg4u_1_q3[0], shrg4u_1_q3[1], shrg4u_1_q3[2], shrg4u_1_q3[3]

  // Notes on the sheet:
  //   CLK
  //   QD
  //   QC
  //   QB
  //   QA
endmodule

module regfiles (
  input  [4:0] R1_num,
  input  [4:0] R2_num,
  input  [31:0] Din,
  input  [4:0] Write_Reg_num,
  input  Write_Enable,
  input  Clock,
  output [31:0] Reg1Out,
  output [31:0] Reg2Out
);

  wire and_1_out, and_2_out, and_3_out, and_4_out, and_5_out, and_6_out, and_7_out, and_8_out, and_9_out,
       and_10_out, and_11_out, and_12_out, and_13_out, and_14_out, and_15_out, and_16_out, and_17_out,
       and_18_out, and_19_out, and_20_out, and_21_out, and_22_out, and_23_out, and_24_out, and_25_out,
       and_26_out, and_27_out, and_28_out, and_29_out, and_30_out, and_31_out, and_32_out,
       demultiplexer_1_out0, demultiplexer_1_out1, demultiplexer_1_out2, demultiplexer_1_out3,
       demultiplexer_2_out0, demultiplexer_2_out1, demultiplexer_2_out2, demultiplexer_2_out3,
       demultiplexer_2_out4, demultiplexer_2_out5, demultiplexer_2_out6, demultiplexer_2_out7,
       demultiplexer_3_out0, demultiplexer_3_out1, demultiplexer_3_out2, demultiplexer_3_out3,
       demultiplexer_3_out4, demultiplexer_3_out5, demultiplexer_3_out6, demultiplexer_3_out7,
       demultiplexer_4_out0, demultiplexer_4_out1, demultiplexer_4_out2, demultiplexer_4_out3,
       demultiplexer_4_out4, demultiplexer_4_out5, demultiplexer_4_out6, demultiplexer_4_out7,
       demultiplexer_5_out0, demultiplexer_5_out1, demultiplexer_5_out2, demultiplexer_5_out3,
       demultiplexer_5_out4, demultiplexer_5_out5, demultiplexer_5_out6, demultiplexer_5_out7;
  wire [31:0] register_1_q, register_2_q, register_3_q, register_4_q, register_5_q, register_6_q,
       register_7_q, register_8_q, register_9_q, register_10_q, register_11_q, register_12_q, register_13_q,
       register_14_q, register_15_q, register_16_q, register_17_q, register_18_q, register_19_q,
       register_20_q, register_21_q, register_22_q, register_23_q, register_24_q, register_25_q,
       register_26_q, register_27_q, register_28_q, register_29_q, register_30_q, register_31_q,
       register_32_q;

  Demultiplexer #(.select(2), .enable("false")) demultiplexer_1 (
    .out0(demultiplexer_1_out0), .out1(demultiplexer_1_out1), .out2(demultiplexer_1_out2),
    .out3(demultiplexer_1_out3), .in(Write_Enable), .sel(Write_Reg_num[4:3]));
  Demultiplexer #(.select(3), .enable("false")) demultiplexer_2 (
    .out0(demultiplexer_2_out0), .out1(demultiplexer_2_out1), .out2(demultiplexer_2_out2),
    .out3(demultiplexer_2_out3), .out4(demultiplexer_2_out4), .out5(demultiplexer_2_out5),
    .out6(demultiplexer_2_out6), .out7(demultiplexer_2_out7), .in(demultiplexer_1_out0),
    .sel(Write_Reg_num[2:0]));
  Register #(.width(32), .trigger("falling"), .Select("low")) register_1 (
    .D(Din), .en(and_1_out), .Q(register_1_q), .clk(Clock));  // open: clr
  and and_1 (and_1_out, Write_Enable, demultiplexer_2_out0);
  Register #(.width(32), .trigger("falling"), .Select("low")) register_2 (
    .D(Din), .en(and_2_out), .Q(register_2_q), .clk(Clock));  // open: clr
  and and_2 (and_2_out, Write_Enable, demultiplexer_2_out1);
  Register #(.width(32), .trigger("falling"), .Select("low")) register_3 (
    .D(Din), .en(and_3_out), .Q(register_3_q), .clk(Clock));  // open: clr
  and and_3 (and_3_out, Write_Enable, demultiplexer_2_out2);
  Register #(.width(32), .trigger("falling"), .Select("low")) register_4 (
    .D(Din), .en(and_4_out), .Q(register_4_q), .clk(Clock));  // open: clr
  and and_4 (and_4_out, Write_Enable, demultiplexer_2_out3);
  Register #(.width(32), .trigger("falling"), .Select("low")) register_5 (
    .D(Din), .en(and_5_out), .Q(register_5_q), .clk(Clock));  // open: clr
  and and_5 (and_5_out, Write_Enable, demultiplexer_2_out4);
  Register #(.width(32), .trigger("falling"), .Select("low")) register_6 (
    .D(Din), .en(and_6_out), .Q(register_6_q), .clk(Clock));  // open: clr
  and and_6 (and_6_out, Write_Enable, demultiplexer_2_out5);
  Register #(.width(32), .trigger("falling"), .Select("low")) register_7 (
    .D(Din), .en(and_7_out), .Q(register_7_q), .clk(Clock));  // open: clr
  and and_7 (and_7_out, Write_Enable, demultiplexer_2_out6);
  Register #(.width(32), .trigger("falling"), .Select("low")) register_8 (
    .D(Din), .en(and_8_out), .Q(register_8_q), .clk(Clock));  // open: clr
  and and_8 (and_8_out, Write_Enable, demultiplexer_2_out7);
  Demultiplexer #(.select(3), .enable("false")) demultiplexer_3 (
    .out0(demultiplexer_3_out0), .out1(demultiplexer_3_out1), .out2(demultiplexer_3_out2),
    .out3(demultiplexer_3_out3), .out4(demultiplexer_3_out4), .out5(demultiplexer_3_out5),
    .out6(demultiplexer_3_out6), .out7(demultiplexer_3_out7), .in(demultiplexer_1_out1),
    .sel(Write_Reg_num[2:0]));
  and and_9 (and_9_out, Write_Enable, demultiplexer_3_out0);
  and and_10 (and_10_out, Write_Enable, demultiplexer_3_out1);
  and and_11 (and_11_out, Write_Enable, demultiplexer_3_out2);
  and and_12 (and_12_out, Write_Enable, demultiplexer_3_out3);
  and and_13 (and_13_out, Write_Enable, demultiplexer_3_out4);
  and and_14 (and_14_out, Write_Enable, demultiplexer_3_out5);
  and and_15 (and_15_out, Write_Enable, demultiplexer_3_out6);
  and and_16 (and_16_out, Write_Enable, demultiplexer_3_out7);
  Demultiplexer #(.select(3), .enable("false")) demultiplexer_4 (
    .out0(demultiplexer_4_out0), .out1(demultiplexer_4_out1), .out2(demultiplexer_4_out2),
    .out3(demultiplexer_4_out3), .out4(demultiplexer_4_out4), .out5(demultiplexer_4_out5),
    .out6(demultiplexer_4_out6), .out7(demultiplexer_4_out7), .in(demultiplexer_1_out2),
    .sel(Write_Reg_num[2:0]));
  Register #(.width(32), .trigger("falling"), .Select("low")) register_9 (
    .D(Din), .en(and_9_out), .Q(register_9_q), .clk(Clock));  // open: clr
  Register #(.width(32), .trigger("falling"), .Select("low")) register_10 (
    .D(Din), .en(and_10_out), .Q(register_10_q), .clk(Clock));  // open: clr
  Register #(.width(32), .trigger("falling"), .Select("low")) register_11 (
    .D(Din), .en(and_11_out), .Q(register_11_q), .clk(Clock));  // open: clr
  Register #(.width(32), .trigger("falling"), .Select("low")) register_12 (
    .D(Din), .en(and_12_out), .Q(register_12_q), .clk(Clock));  // open: clr
  Register #(.width(32), .trigger("falling"), .Select("low")) register_13 (
    .D(Din), .en(and_13_out), .Q(register_13_q), .clk(Clock));  // open: clr
  Register #(.width(32), .trigger("falling"), .Select("low")) register_14 (
    .D(Din), .en(and_14_out), .Q(register_14_q), .clk(Clock));  // open: clr
  Register #(.width(32), .trigger("falling"), .Select("low")) register_15 (
    .D(Din), .en(and_15_out), .Q(register_15_q), .clk(Clock));  // open: clr
  Register #(.width(32), .trigger("falling"), .Select("low")) register_16 (
    .D(Din), .en(and_16_out), .Q(register_16_q), .clk(Clock));  // open: clr
  Register #(.width(32), .trigger("falling"), .Select("low")) register_17 (
    .D(Din), .en(and_17_out), .Q(register_17_q), .clk(Clock));  // open: clr
  and and_17 (and_17_out, Write_Enable, demultiplexer_4_out0);
  Register #(.width(32), .trigger("falling"), .Select("low")) register_18 (
    .D(Din), .en(and_18_out), .Q(register_18_q), .clk(Clock));  // open: clr
  and and_18 (and_18_out, Write_Enable, demultiplexer_4_out1);
  Register #(.width(32), .trigger("falling"), .Select("low")) register_19 (
    .D(Din), .en(and_19_out), .Q(register_19_q), .clk(Clock));  // open: clr
  and and_19 (and_19_out, Write_Enable, demultiplexer_4_out2);
  Register #(.width(32), .trigger("falling"), .Select("low")) register_20 (
    .D(Din), .en(and_20_out), .Q(register_20_q), .clk(Clock));  // open: clr
  and and_20 (and_20_out, Write_Enable, demultiplexer_4_out3);
  Register #(.width(32), .trigger("falling"), .Select("low")) register_21 (
    .D(Din), .en(and_21_out), .Q(register_21_q), .clk(Clock));  // open: clr
  and and_21 (and_21_out, Write_Enable, demultiplexer_4_out4);
  Register #(.width(32), .trigger("falling"), .Select("low")) register_22 (
    .D(Din), .en(and_22_out), .Q(register_22_q), .clk(Clock));  // open: clr
  and and_22 (and_22_out, Write_Enable, demultiplexer_4_out5);
  Register #(.width(32), .trigger("falling"), .Select("low")) register_23 (
    .D(Din), .en(and_23_out), .Q(register_23_q), .clk(Clock));  // open: clr
  and and_23 (and_23_out, Write_Enable, demultiplexer_4_out6);
  Register #(.width(32), .trigger("falling"), .Select("low")) register_24 (
    .D(Din), .en(and_24_out), .Q(register_24_q), .clk(Clock));  // open: clr
  and and_24 (and_24_out, Write_Enable, demultiplexer_4_out7);
  Demultiplexer #(.select(3), .enable("false")) demultiplexer_5 (
    .out0(demultiplexer_5_out0), .out1(demultiplexer_5_out1), .out2(demultiplexer_5_out2),
    .out3(demultiplexer_5_out3), .out4(demultiplexer_5_out4), .out5(demultiplexer_5_out5),
    .out6(demultiplexer_5_out6), .out7(demultiplexer_5_out7), .in(demultiplexer_1_out3),
    .sel(Write_Reg_num[2:0]));
  and and_25 (and_25_out, Write_Enable, demultiplexer_5_out0);
  and and_26 (and_26_out, Write_Enable, demultiplexer_5_out1);
  and and_27 (and_27_out, Write_Enable, demultiplexer_5_out2);
  and and_28 (and_28_out, Write_Enable, demultiplexer_5_out3);
  and and_29 (and_29_out, Write_Enable, demultiplexer_5_out4);
  and and_30 (and_30_out, Write_Enable, demultiplexer_5_out5);
  and and_31 (and_31_out, Write_Enable, demultiplexer_5_out6);
  and and_32 (and_32_out, Write_Enable, demultiplexer_5_out7);
  Register #(.width(32), .trigger("falling"), .Select("low")) register_25 (
    .D(Din), .en(and_25_out), .Q(register_25_q), .clk(Clock));  // open: clr
  Register #(.width(32), .trigger("falling"), .Select("low")) register_26 (
    .D(Din), .en(and_26_out), .Q(register_26_q), .clk(Clock));  // open: clr
  Register #(.width(32), .trigger("falling"), .Select("low")) register_27 (
    .D(Din), .en(and_27_out), .Q(register_27_q), .clk(Clock));  // open: clr
  Register #(.width(32), .trigger("falling"), .Select("low")) register_28 (
    .D(Din), .en(and_28_out), .Q(register_28_q), .clk(Clock));  // open: clr
  Register #(.width(32), .trigger("falling"), .Select("low")) register_29 (
    .D(Din), .en(and_29_out), .Q(register_29_q), .clk(Clock));  // open: clr
  Register #(.width(32), .trigger("falling"), .Select("low")) register_30 (
    .D(Din), .en(and_30_out), .Q(register_30_q), .clk(Clock));  // open: clr
  Register #(.width(32), .trigger("falling"), .Select("low")) register_31 (
    .D(Din), .en(and_31_out), .Q(register_31_q), .clk(Clock));  // open: clr
  Register #(.width(32), .trigger("falling"), .Select("low")) register_32 (
    .D(Din), .en(and_32_out), .Q(register_32_q), .clk(Clock));  // open: clr
  Multiplexer #(.select(5), .width(32), .enable("false")) multiplexer_1 (
    .in0(register_1_q), .in1(register_2_q), .in2(register_3_q), .in3(register_4_q), .in4(register_5_q),
    .in5(register_6_q), .in6(register_7_q), .in7(register_8_q), .in8(register_9_q), .in9(register_10_q),
    .in10(register_11_q), .in11(register_12_q), .in12(register_13_q), .in13(register_14_q),
    .in14(register_15_q), .in15(register_16_q), .in16(register_17_q), .in17(register_18_q),
    .in18(register_19_q), .in19(register_20_q), .in20(register_21_q), .in21(register_22_q),
    .in22(register_23_q), .in23(register_24_q), .in24(register_25_q), .in25(register_26_q),
    .in26(register_27_q), .in27(register_28_q), .in28(register_29_q), .in29(register_30_q),
    .in30(register_31_q), .in31(register_32_q), .out(Reg1Out), .sel(R1_num));
  Multiplexer #(.select(5), .width(32), .enable("false")) multiplexer_2 (
    .in0(register_1_q), .in1(register_2_q), .in2(register_3_q), .in3(register_4_q), .in4(register_5_q),
    .in5(register_6_q), .in6(register_7_q), .in7(register_8_q), .in8(register_9_q), .in9(register_10_q),
    .in10(register_11_q), .in11(register_12_q), .in12(register_13_q), .in13(register_14_q),
    .in14(register_15_q), .in15(register_16_q), .in16(register_17_q), .in17(register_18_q),
    .in18(register_19_q), .in19(register_20_q), .in20(register_21_q), .in21(register_22_q),
    .in22(register_23_q), .in23(register_24_q), .in24(register_25_q), .in25(register_26_q),
    .in26(register_27_q), .in27(register_28_q), .in28(register_29_q), .in29(register_30_q),
    .in30(register_31_q), .in31(register_32_q), .out(Reg2Out), .sel(R2_num));

  // Other names for the same wires on the sheet: CLK = Clock; RA[4:0] = R1_num; RB[4:0] = R2_num; RDA[31:0] = Reg1Out;
  //   RDB[31:0] = Reg2Out; RW[4:0] = Write_Reg_num; WE = Write_Enable

  // Notes on the sheet:
  //   000
  //   111
  //   输入引脚
  //   00
  //   电路功能：实现寄存器堆功能，实现0-31号寄存器。写使能有效且时钟边沿有效后写入数据，随时读出双口数据
  //   01
  //   输出引脚
  //   10
  //   11
endmodule

module \数字时钟  (
  input  \设置初值 ,
  input  [3:0] \时高位 ,
  input  [3:0] \时低位 ,
  input  [3:0] \分高位 ,
  input  [3:0] \分低位 ,
  input  [3:0] \秒高位 ,
  input  [3:0] \秒低位 
);

  wire and_1_out, and_2_out, and_3_out, and_4_out, and_5_out, and_6_out, buffer_1_out, CLK, LED,
       multiplexer_1_out, multiplexer_2_out, multiplexer_3_out, multiplexer_4_out, multiplexer_5_out,
       or_1_out, \蜂鸣使能 ;
  wire [3:0] H0, H1, M0, M1, S0, S1;

  Clock \u_时钟  (.out(CLK));
  Multiplexer #(.enable("false")) multiplexer_1 (.in0(and_1_out), .in1(CLK), .out(multiplexer_1_out), .sel(\设置初值 ));
  CNTR4U cntr4u_1 (
    .LD(\设置初值 ), .CLR(and_1_out), .D0(\秒低位 [0]), .D1(\秒低位 [1]), .D2(\秒低位 [2]), .D3(\秒低位 [3]), .ENP(1'b1),
    .ENT(1'b1), .Q0(S0[0]), .Q1(S0[1]), .Q2(S0[2]), .Q3(S0[3]), .CLK(CLK));  // open: RCO
  and and_1 (and_1_out, S0[3], S0[0]);
  CNTR4U cntr4u_2 (
    .LD(\设置初值 ), .CLR(and_2_out), .D0(\秒高位 [0]), .D1(\秒高位 [1]), .D2(\秒高位 [2]), .D3(\秒高位 [3]), .ENP(1'b1),
    .ENT(1'b1), .Q0(S1[0]), .Q1(S1[1]), .Q2(S1[2]), .Q3(S1[3]), .CLK(multiplexer_1_out));  // open: RCO
  and and_2 (and_2_out, S1[0], and_1_out, S1[2]);
  Multiplexer #(.enable("false")) multiplexer_2 (.in0(and_2_out), .in1(CLK), .out(multiplexer_2_out), .sel(\设置初值 ));
  Multiplexer #(.enable("false")) multiplexer_3 (.in0(and_3_out), .in1(CLK), .out(multiplexer_3_out), .sel(\设置初值 ));
  Hex_Digit_Display hex_digit_display_1 (.value(H1));  // open: dp
  Hex_Digit_Display hex_digit_display_2 (.value(H0), .dp(1'b1));
  CNTR4U cntr4u_3 (
    .LD(\设置初值 ), .CLR(and_3_out), .D0(\分低位 [0]), .D1(\分低位 [1]), .D2(\分低位 [2]), .D3(\分低位 [3]), .ENP(1'b1),
    .ENT(1'b1), .Q0(M0[0]), .Q1(M0[1]), .Q2(M0[2]), .Q3(M0[3]), .CLK(multiplexer_2_out));  // open: RCO
  and and_3 (and_3_out, M0[3], and_2_out, M0[0]);
  CNTR4U cntr4u_4 (
    .LD(\设置初值 ), .CLR(and_4_out), .D0(\分高位 [0]), .D1(\分高位 [1]), .D2(\分高位 [2]), .D3(\分高位 [3]), .ENP(1'b1),
    .ENT(1'b1), .Q0(M1[0]), .Q1(M1[1]), .Q2(M1[2]), .Q3(M1[3]), .CLK(multiplexer_3_out));  // open: RCO
  Hex_Digit_Display hex_digit_display_3 (.value(M0), .dp(1'b1));
  Hex_Digit_Display hex_digit_display_4 (.value(M1));  // open: dp
  Hex_Digit_Display hex_digit_display_5 (.value(S0), .dp(1'b1));
  Hex_Digit_Display hex_digit_display_6 (.value(S1));  // open: dp
  and and_4 (and_4_out, M1[0], and_3_out, M1[2]);
  LED \u_整点点亮  (.in(LED));
  Multiplexer #(.enable("false")) multiplexer_4 (.in0(and_4_out), .in1(CLK), .out(multiplexer_4_out), .sel(\设置初值 ));
  or or_1 (or_1_out, and_6_out, and_5_out);
  and and_5 (and_5_out, H0[3], and_4_out, H0[0]);
  Multiplexer #(.enable("false")) multiplexer_5 (.in0(or_1_out), .in1(CLK), .out(multiplexer_5_out), .sel(\设置初值 ));
  // Buzzer buzzer_1: pin names not known; wires that end beside it: 14'h1000, \蜂鸣使能 , 7'b0110000
  CNTR4U cntr4u_5 (
    .LD(\设置初值 ), .CLR(or_1_out), .D0(\时低位 [0]), .D1(\时低位 [1]), .D2(\时低位 [2]), .D3(\时低位 [3]), .ENP(1'b1),
    .ENT(1'b1), .Q0(H0[0]), .Q1(H0[1]), .Q2(H0[2]), .Q3(H0[3]), .CLK(multiplexer_4_out));  // open: RCO
  CNTR4U cntr4u_6 (
    .LD(\设置初值 ), .CLR(buffer_1_out), .D0(\时高位 [0]), .D1(\时高位 [1]), .D2(\时高位 [2]), .D3(\时高位 [3]), .ENP(1'b1),
    .ENT(1'b1), .Q0(H1[0]), .Q1(H1[1]), .Q2(H1[2]), .Q3(H1[3]), .CLK(multiplexer_5_out));  // open: RCO
  and and_6 (and_6_out, H0[0], H0[1], and_4_out, H1[1]);
  buf buffer_1 (buffer_1_out, and_6_out);
  D_Flip_Flop #(.trigger("falling")) d_ff_1 (.clk(and_4_out), .D(1'b1), .Q(LED), .reset(S0[0]));  // open: Qn, preset
  D_Flip_Flop #(.trigger("falling")) d_ff_2 (.clk(and_6_out), .D(1'b1), .Q(\蜂鸣使能 ), .reset(S0[0]));  // open: Qn, preset

  // Other names for the same wires on the sheet: LD = \设置初值 

  // Notes on the sheet:
  //   输入信号
  //   初始时间
  //   BCD码
  //   数字时钟
  //   频率
  //   蜂鸣器
  //   音量
endmodule

module \_60进制计数器  (
);

  wire and_1_out, and_2_out, clock_1_out;
  wire [3:0] cntr4u_1_q0, cntr4u_2_q0;

  Clock clock_1 (.out(clock_1_out));
  and and_1 (and_1_out, cntr4u_2_q0[2], and_2_out, cntr4u_2_q0[0]);
  and and_2 (and_2_out, cntr4u_1_q0[3], cntr4u_1_q0[0]);
  CNTR4U cntr4u_1 (
    .LD(1'b0), .CLR(and_2_out), .D0(1'b0), .D1(1'b0), .D2(1'b0), .D3(1'b0), .ENP(1'b1), .ENT(1'b1),
    .Q0(cntr4u_1_q0[0]), .Q1(cntr4u_1_q0[1]), .Q2(cntr4u_1_q0[2]), .Q3(cntr4u_1_q0[3]), .CLK(clock_1_out));  // open: RCO
  CNTR4U cntr4u_2 (
    .LD(1'b0), .CLR(and_1_out), .D0(1'b0), .D1(1'b0), .D2(1'b0), .D3(1'b0), .ENP(and_2_out), .ENT(and_2_out),
    .Q0(cntr4u_2_q0[0]), .Q1(cntr4u_2_q0[1]), .Q2(cntr4u_2_q0[2]), .Q3(cntr4u_2_q0[3]), .CLK(clock_1_out));  // open: RCO
  Hex_Digit_Display hex_digit_display_1 (.value(cntr4u_2_q0));  // open: dp
  Hex_Digit_Display hex_digit_display_2 (.value(cntr4u_1_q0));  // open: dp

  // Notes on the sheet:
  //   60进制计数器_分解计数
endmodule

module \_4位无符号数乘法器  (
  input  [3:0] X,
  input  [3:0] Y,
  output [7:0] \乘积 
);

  wire LOAD, \n4位加法器_1_cout , not_1_out, or_1_out, RST, STOP, \时钟_out ;
  wire [3:0] cntr4u_1_q0, multiplexer_1_out, multiplexer_2_out, \n4位加法器_1_f , \n8位移位器_1_dataout ,
       \n8位移位器_1_dataout_2 ;

  Button \u_复位  (.out(RST));
  Clock \u_时钟  (.out(\时钟_out ));
  Hex_Digit_Display hex_digit_display_1 (.value(X));  // open: dp
  not not_1 (not_1_out, STOP);
  Multiplexer #(.width(4), .enable("false")) multiplexer_1 (
    .in0(4'b0000), .in1(X), .out(multiplexer_1_out), .sel(multiplexer_2_out[0]));
  \_4位加法器  \u_4位加法器_1  (.X(multiplexer_1_out), .F(\n4位加法器_1_f ), .Cout(\n4位加法器_1_cout ), .Cin(1'b0), .Y(\乘积 [7:4]));
  Hex_Digit_Display hex_digit_display_2 (.value(Y));  // open: dp
  // Probe on \乘积 [7:4]
  Register #(.width(4), .trigger("falling"), .Select("low")) P_2 (
    .D(\n8位移位器_1_dataout_2 ), .en(not_1_out), .Q(\乘积 [7:4]), .clk(\时钟_out ), .clr(RST));
  \_8位移位器  \u_8位移位器_1  (
    .DataIn({\n4位加法器_1_f , multiplexer_2_out}), .shamt(3'b001),
    .DataOut({\n8位移位器_1_dataout_2 , \n8位移位器_1_dataout }), .IN(\n4位加法器_1_cout ), .L_R(1'b0), .A_L(1'b0));
  Register #(.width(4), .trigger("falling"), .Select("low")) u_Y (
    .D(\n8位移位器_1_dataout ), .en(not_1_out), .Q(\乘积 [3:0]), .clk(\时钟_out ), .clr(RST));
  Multiplexer #(.width(4), .enable("false")) multiplexer_2 (
    .in0(\乘积 [3:0]), .in1(Y), .out(multiplexer_2_out), .sel(LOAD));
  Hex_Digit_Display hex_digit_display_3 (.value(\乘积 [7:4]));  // open: dp
  // Probe on \乘积 [3:0]
  or or_1 (or_1_out, RST, \时钟_out );
  Hex_Digit_Display hex_digit_display_4 (.value(\乘积 [3:0]));  // open: dp
  CNTR4U cntr4u_1 (
    .LD(1'b0), .CLR(RST), .D0(1'b0), .D1(1'b0), .D2(1'b0), .D3(1'b0), .ENP(not_1_out), .ENT(not_1_out),
    .Q0(cntr4u_1_q0[0]), .Q1(cntr4u_1_q0[1]), .Q2(cntr4u_1_q0[2]), .Q3(cntr4u_1_q0[3]), .CLK(or_1_out));  // open: RCO
  // Probe on X
  // Probe on Y
  // Probe on \乘积 
  Comparator #(.width(4)) comparator_1 (.a(cntr4u_1_q0), .b(4'b0000), .eq(LOAD));  // open: gt, lt
  Comparator #(.width(4)) comparator_2 (.a(cntr4u_1_q0), .b(4'b0011), .gt(STOP));  // open: eq, lt

  // Other names for the same wires on the sheet: Z[7:0] = \乘积 

  // Notes on the sheet:
  //   输入引脚区
  //   X
  //   4位无符号数一位乘法器
  //   =
  //   输出引脚区
  //   ×
  //   =
endmodule

module \_8位移位器  (
  input  [7:0] DataIn,
  input  [2:0] shamt,
  input  IN,
  input  L_R,
  input  A_L,
  output [7:0] DataOut
);

  wire _1_0;
  wire [1:0] multiplexer_1_out, multiplexer_2_out, multiplexer_2_out_2, multiplexer_2_out_3,
       multiplexer_2_out_4;
  wire [3:0] multiplexer_3_out, multiplexer_3_out_2, multiplexer_4_out;
  wire [7:7] or_1_out;

  and and_1 (_1_0, DataIn[7], A_L);
  or or_1 (or_1_out[7], _1_0, IN);
  Multiplexer #(.width(2), .enable("false")) multiplexer_1 (
    .in0(2'b00), .in1(2'b11), .out(multiplexer_1_out), .sel(_1_0));
  Multiplexer #(.select(2), .width(8), .enable("false")) multiplexer_2 (
    .in0(DataIn), .in1({or_1_out[7], DataIn[7:1]}), .in2(DataIn), .in3({DataIn[6:0], IN}),
    .out({multiplexer_2_out, multiplexer_2_out_4, multiplexer_2_out_3, multiplexer_2_out_2}),
    .sel({L_R, shamt[0]}));
  Multiplexer #(.select(2), .width(8), .enable("false")) multiplexer_3 (
    .in0({multiplexer_2_out, multiplexer_2_out_4, multiplexer_2_out_3, multiplexer_2_out_2}),
    .in1({multiplexer_1_out, multiplexer_2_out, multiplexer_2_out_4, multiplexer_2_out_3}),
    .in2({multiplexer_2_out, multiplexer_2_out_4, multiplexer_2_out_3, multiplexer_2_out_2}),
    .in3({multiplexer_2_out_4, multiplexer_2_out_3, multiplexer_2_out_2, 2'b00}),
    .out({multiplexer_3_out, multiplexer_3_out_2}), .sel({L_R, shamt[1]}));
  Multiplexer #(.width(4), .enable("false")) multiplexer_4 (
    .in0(4'b0000), .in1(4'b1111), .out(multiplexer_4_out), .sel(_1_0));
  Multiplexer #(.select(2), .width(8), .enable("false")) multiplexer_5 (
    .in0({multiplexer_3_out, multiplexer_3_out_2}), .in1({multiplexer_4_out, multiplexer_3_out}),
    .in2({multiplexer_3_out, multiplexer_3_out_2}), .in3({multiplexer_3_out_2, 4'b0000}), .out(DataOut),
    .sel({L_R, shamt[2]}));

  // Other names for the same wires on the sheet: Din[7:0] = DataIn; Input = IN; Left_Right = L_R; Arth_Logic = A_L;
  //   Dout[7:0] = DataOut

  // Notes on the sheet:
  //   输入信号
  //   L/R=0：右移；=1：左移
  //   A/L=0：逻辑右移；=1：算术右移
  //   8位桶形移位器
  //   输出信号
endmodule

module \_4位加法器  (
  input  [3:0] X,
  input  [3:0] Y,
  input  Cin,
  output [3:0] F,
  output Cout
);

  wire \全加器_1_cout , \全加器_2_cout , \全加器_3_cout ;
  wire [3:0] xor_1_out, \操作数y ;

  Hex_Digit_Display hex_digit_display_1 (.value(X));  // open: dp
  Hex_Digit_Display hex_digit_display_2 (.value(\操作数y ));  // open: dp
  \全加器  \u_全加器_1  (.A(X[0]), .B(\操作数y [0]), .Cin(Cin), .F(F[0]), .Cout(\全加器_1_cout ));
  \全加器  \u_全加器_2  (.A(X[1]), .B(\操作数y [1]), .Cin(\全加器_1_cout ), .F(F[1]), .Cout(\全加器_2_cout ));
  Hex_Digit_Display hex_digit_display_3 (.value(F));  // open: dp
  \全加器  \u_全加器_3  (.A(X[2]), .B(\操作数y [2]), .Cin(\全加器_2_cout ), .F(F[2]), .Cout(\全加器_3_cout ));
  \全加器  \u_全加器_4  (.A(X[3]), .B(\操作数y [3]), .Cin(\全加器_3_cout ), .F(F[3]), .Cout(Cout));
  assign xor_1_out = Y ^ 4'b1111;  // XOR_Gate xor_1, 4 bits wide
  Multiplexer #(.width(4), .enable("false")) multiplexer_1 (.in0(Y), .in1(xor_1_out), .out(\操作数y ), .sel(Cin));

  // Other names for the same wires on the sheet: 操作数x[3:0] = X; 运算结果[3:0] = F

  // Notes on the sheet:
  //   输入
  //   输出
  //   +
  //   F1
  //   =
  //   F2
  //   F3
  //   F4
endmodule

module \全加器  (
  input  A,
  input  B,
  input  Cin,
  output F,
  output Cout
);

  wire and_1_out, and_2_out, and_3_out, xor_1_out;

  xor xor_1 (xor_1_out, A, Cin);
  xor xor_2 (F, xor_1_out, B);
  and and_1 (and_1_out, A, B);
  and and_2 (and_2_out, A, Cin);
  and and_3 (and_3_out, B, Cin);
  or or_1 (Cout, and_1_out, and_2_out, and_3_out);

  // Notes on the sheet:
  //   全加器
endmodule

module \寄存器堆读写  (
  input  [4:0] R2_num,
  input  [4:0] R1_num,
  input  [4:0] Write_Reg_num,
  input  [31:0] Din,
  input  Write_Enable,
  output [31:0] Reg1Out,
  output [31:0] Reg2Out
);

  wire clock_1_out;

  Clock clock_1 (.out(clock_1_out));
  regfiles \u_寄存器堆  (
    .R1_num(R1_num), .R2_num(R2_num), .Din(Din), .Write_Reg_num(Write_Reg_num), .Write_Enable(Write_Enable),
    .Clock(clock_1_out), .Reg1Out(Reg1Out), .Reg2Out(Reg2Out));
endmodule

module \闹钟  (
  input  \设置初值 ,
  input  [3:0] \时高位 ,
  input  [3:0] \时低位 ,
  input  [3:0] \分高位 ,
  input  [3:0] \分低位 ,
  input  [3:0] \秒高位 ,
  input  [3:0] \秒低位 
);

  wire and_1_out, and_2_out, and_3_out, and_4_out, and_5_out, and_6_out, buffer_1_out, CLK, comparator_1_eq,
       comparator_2_eq, comparator_3_eq, comparator_4_eq, comparator_5_eq, comparator_6_eq, LED,
       multiplexer_1_out, multiplexer_2_out, multiplexer_3_out, multiplexer_4_out, multiplexer_5_out,
       or_1_out, \蜂鸣使能 ;
  wire [3:0] H0, H1, M0, M1, S0, S1;

  Clock \u_时钟  (.out(CLK));
  Multiplexer #(.enable("false")) multiplexer_1 (.in0(and_1_out), .in1(CLK), .out(multiplexer_1_out), .sel(\设置初值 ));
  CNTR4U cntr4u_1 (
    .LD(\设置初值 ), .CLR(and_1_out), .D0(\秒低位 [0]), .D1(\秒低位 [1]), .D2(\秒低位 [2]), .D3(\秒低位 [3]), .ENP(1'b1),
    .ENT(1'b1), .Q0(S0[0]), .Q1(S0[1]), .Q2(S0[2]), .Q3(S0[3]), .CLK(CLK));  // open: RCO
  and and_1 (and_1_out, S0[3], S0[0]);
  CNTR4U cntr4u_2 (
    .LD(\设置初值 ), .CLR(and_2_out), .D0(\秒高位 [0]), .D1(\秒高位 [1]), .D2(\秒高位 [2]), .D3(\秒高位 [3]), .ENP(1'b1),
    .ENT(1'b1), .Q0(S1[0]), .Q1(S1[1]), .Q2(S1[2]), .Q3(S1[3]), .CLK(multiplexer_1_out));  // open: RCO
  and and_2 (and_2_out, S1[0], and_1_out, S1[2]);
  Comparator #(.width(4), .mode("unsigned")) comparator_1 (.a(\时高位 ), .b(H1), .eq(comparator_1_eq));  // open: gt, lt
  Comparator #(.width(4), .mode("unsigned")) comparator_2 (.a(\时低位 ), .b(H0), .eq(comparator_2_eq));  // open: gt, lt
  Comparator #(.width(4), .mode("unsigned")) comparator_3 (.a(\分高位 ), .b(M1), .eq(comparator_3_eq));  // open: gt, lt
  Comparator #(.width(4), .mode("unsigned")) comparator_4 (.a(\分低位 ), .b(M0), .eq(comparator_4_eq));  // open: gt, lt
  Comparator #(.width(4), .mode("unsigned")) comparator_5 (.a(\秒高位 ), .b(S1), .eq(comparator_5_eq));  // open: gt, lt
  Comparator #(.width(4), .mode("unsigned")) comparator_6 (.a(\秒低位 ), .b(S0), .eq(comparator_6_eq));  // open: gt, lt
  Multiplexer #(.enable("false")) multiplexer_2 (.in0(and_2_out), .in1(CLK), .out(multiplexer_2_out), .sel(\设置初值 ));
  Multiplexer #(.enable("false")) multiplexer_3 (.in0(and_3_out), .in1(CLK), .out(multiplexer_3_out), .sel(\设置初值 ));
  Hex_Digit_Display hex_digit_display_1 (.value(H0), .dp(1'b1));
  Hex_Digit_Display hex_digit_display_2 (.value(H1));  // open: dp
  CNTR4U cntr4u_3 (
    .LD(\设置初值 ), .CLR(and_3_out), .D0(\分低位 [0]), .D1(\分低位 [1]), .D2(\分低位 [2]), .D3(\分低位 [3]), .ENP(1'b1),
    .ENT(1'b1), .Q0(M0[0]), .Q1(M0[1]), .Q2(M0[2]), .Q3(M0[3]), .CLK(multiplexer_2_out));  // open: RCO
  and and_3 (and_3_out, M0[3], and_2_out, M0[0]);
  CNTR4U cntr4u_4 (
    .LD(\设置初值 ), .CLR(and_5_out), .D0(\分高位 [0]), .D1(\分高位 [1]), .D2(\分高位 [2]), .D3(\分高位 [3]), .ENP(1'b1),
    .ENT(1'b1), .Q0(M1[0]), .Q1(M1[1]), .Q2(M1[2]), .Q3(M1[3]), .CLK(multiplexer_3_out));  // open: RCO
  and and_4 (and_4_out, comparator_1_eq, comparator_2_eq, comparator_3_eq, comparator_4_eq, comparator_5_eq, comparator_6_eq);
  Hex_Digit_Display hex_digit_display_3 (.value(M1));  // open: dp
  Hex_Digit_Display hex_digit_display_4 (.value(M0), .dp(1'b1));
  // Buzzer buzzer_1: pin names not known; wires that end beside it: 14'h1000, and_4_out, 7'b0110000
  Hex_Digit_Display hex_digit_display_5 (.value(S1));  // open: dp
  Hex_Digit_Display hex_digit_display_6 (.value(S0), .dp(1'b1));
  and and_5 (and_5_out, M1[0], and_3_out, M1[2]);
  LED \u_整点点亮  (.in(LED));
  Multiplexer #(.enable("false")) multiplexer_4 (.in0(and_5_out), .in1(CLK), .out(multiplexer_4_out), .sel(\设置初值 ));
  or or_1 (or_1_out, \蜂鸣使能 , and_6_out);
  and and_6 (and_6_out, H0[3], and_5_out, H0[0]);
  Multiplexer #(.enable("false")) multiplexer_5 (.in0(or_1_out), .in1(CLK), .out(multiplexer_5_out), .sel(\设置初值 ));
  // Buzzer buzzer_2: pin names not known; wires that end beside it: 14'h1000, \蜂鸣使能 , 7'b0110000, CLK
  CNTR4U cntr4u_5 (
    .LD(\设置初值 ), .CLR(or_1_out), .D0(\时低位 [0]), .D1(\时低位 [1]), .D2(\时低位 [2]), .D3(\时低位 [3]), .ENP(1'b1),
    .ENT(1'b1), .Q0(H0[0]), .Q1(H0[1]), .Q2(H0[2]), .Q3(H0[3]), .CLK(multiplexer_4_out));  // open: RCO
  CNTR4U cntr4u_6 (
    .LD(\设置初值 ), .CLR(buffer_1_out), .D0(\时高位 [0]), .D1(\时高位 [1]), .D2(\时高位 [2]), .D3(\时高位 [3]), .ENP(1'b1),
    .ENT(1'b1), .Q0(H1[0]), .Q1(H1[1]), .Q2(H1[2]), .Q3(H1[3]), .CLK(multiplexer_5_out));  // open: RCO
  and and_7 (\蜂鸣使能 , H0[0], H0[1], and_5_out, H1[1]);
  buf buffer_1 (buffer_1_out, \蜂鸣使能 );
  D_Flip_Flop #(.trigger("falling")) d_ff_1 (.clk(and_5_out), .D(1'b1), .Q(LED), .reset(S0[0]));  // open: Qn, preset

  // Other names for the same wires on the sheet: LD = \设置初值 

  // Notes on the sheet:
  //   输入信号
  //   初始时间
  //   BCD码
  //   数字时钟
  //   频率
  //   蜂鸣器
  //   音量
endmodule

module \Booth乘法器  (
  input  [3:0] X,
  input  [3:0] Y,
  output [7:0] \乘积 
);

  wire LOAD, not_1_out, or_1_out, RST, STOP, \时钟_out ;
  wire [1:0] d_ff_1_q;
  wire [3:0] \_4位加法器_f , cntr4u_1_q0, multiplexer_1_out, multiplexer_2_out, multiplexer_3_out,
       multiplexer_5_out, multiplexer_5_out_2, \n8位移位器_1_dataout , \n8位移位器_1_dataout_2 , \补码生成器_1_out_2 ,
       \补码生成器_2_out_2 , \补码生成器_3_out_2 ;
  wire [3:1] multiplexer_4_out;
  wire [7:0] adder_1_out, not_2_out;

  Clock \u_时钟  (.out(\时钟_out ));
  \补码生成器  \u_补码生成器_1  (.in_1(X), .out_2(\补码生成器_1_out_2 ));
  \补码生成器  \u_补码生成器_2  (.in_1(X), .out_2(\补码生成器_2_out_2 ));
  Button \u_复位  (.out(RST));
  Multiplexer #(.select(2), .width(4), .enable("false")) multiplexer_1 (
    .in0(4'b0000), .in1(X), .in2(\补码生成器_1_out_2 ), .in3(4'b0000), .out(multiplexer_1_out), .sel(d_ff_1_q));
  Hex_Digit_Display hex_digit_display_1 (.value(multiplexer_2_out));  // open: dp
  Multiplexer #(.width(4), .enable("false")) multiplexer_2 (
    .in0(X), .in1(\补码生成器_2_out_2 ), .out(multiplexer_2_out), .sel(X[3]));
  not not_1 (not_1_out, STOP);
  D_Flip_Flop #(.Pre_Clr_Positions("LEGACY"), .NewFFLayout("false")) d_ff_1 (
    .clk(\时钟_out ), .D(d_ff_1_q[1]), .Q(d_ff_1_q[0]), .reset(RST));  // open: Qn, preset
  \补码生成器  \u_补码生成器_3  (.in_1(Y), .out_2(\补码生成器_3_out_2 ));
  \_4位加法器  \_4位加法器  (.X(multiplexer_1_out), .F(\_4位加法器_f ), .Cin(1'b0), .Y(\乘积 [7:4]));  // open: Cout
  Hex_Digit_Display hex_digit_display_2 (.value(multiplexer_3_out));  // open: dp
  Multiplexer #(.width(4), .enable("false")) multiplexer_3 (
    .in0(Y), .in1(\补码生成器_3_out_2 ), .out(multiplexer_3_out), .sel(Y[3]));
  // Probe on \乘积 [7:4]
  Register #(.width(4), .Select("low")) P_2 (
    .D(\n8位移位器_1_dataout_2 ), .en(not_1_out), .Q(\乘积 [7:4]), .clk(\时钟_out ), .clr(RST));
  \_8位移位器  \u_8位移位器_1  (
    .DataIn({\_4位加法器_f , multiplexer_4_out, d_ff_1_q[1]}), .shamt(3'b001),
    .DataOut({\n8位移位器_1_dataout_2 , \n8位移位器_1_dataout }), .IN(1'b0), .L_R(1'b0), .A_L(1'b1));
  // Probe on \乘积 [3:0]
  Register #(.width(4), .Select("low")) Y_2 (
    .D(\n8位移位器_1_dataout ), .en(not_1_out), .Q(\乘积 [3:0]), .clk(\时钟_out ), .clr(RST));
  Multiplexer #(.width(4), .enable("false")) multiplexer_4 (
    .in0(\乘积 [3:0]), .in1(Y), .out({multiplexer_4_out, d_ff_1_q[1]}), .sel(LOAD));
  Hex_Digit_Display hex_digit_display_3 (.value(multiplexer_5_out_2));  // open: dp
  or or_1 (or_1_out, RST, \时钟_out );
  Hex_Digit_Display hex_digit_display_4 (.value(multiplexer_5_out));  // open: dp
  Multiplexer #(.width(8), .enable("false")) multiplexer_5 (
    .in0(\乘积 ), .in1(adder_1_out), .out({multiplexer_5_out_2, multiplexer_5_out}), .sel(\乘积 [7]));
  CNTR4U cntr4u_1 (
    .LD(1'b0), .CLR(RST), .D0(1'b0), .D1(1'b0), .D2(1'b0), .D3(1'b0), .ENP(1'b1), .ENT(1'b1),
    .Q0(cntr4u_1_q0[0]), .Q1(cntr4u_1_q0[1]), .Q2(cntr4u_1_q0[2]), .Q3(cntr4u_1_q0[3]), .CLK(or_1_out));  // open: RCO
  Comparator #(.width(4)) comparator_1 (.a(cntr4u_1_q0), .b(4'b0000), .eq(LOAD));  // open: gt, lt
  Comparator #(.width(4)) comparator_2 (.a(cntr4u_1_q0), .b(4'b0011), .gt(STOP));  // open: eq, lt
  assign not_2_out = ~\乘积 ;  // NOT_Gate not_2, 8 bits wide
  Adder adder_1 (.a(not_2_out), .b(8'h1), .out(adder_1_out));  // open: cin, cout

  // Other names for the same wires on the sheet: Z[7:0] = \乘积 

  // Notes on the sheet:
  //   输入引脚区
  //   X
  //   4位无符号数一位乘法器
  //   =
  //   输出引脚区
endmodule

module \补码生成器  (
  input  [3:0] in_1,
  output [3:0] out_2
);

  wire [3:0] not_1_out;

  assign not_1_out = ~in_1;  // NOT_Gate not_1, 4 bits wide
  Adder #(.width(4)) adder_1 (.a(not_1_out), .b(4'b0001), .out(out_2));  // open: cin, cout
endmodule

module \除法器  (
  input  [7:0] X,
  input  [3:0] Y,
  output [3:0] \商 
);

  wire \_4位加法器_cout , LOAD, not_1_out, or_1_out, RST, STOP, \时钟_out ;
  wire [3:0] \_4位加法器_f , cntr4u_1_q0, multiplexer_1_out, \n8位移位器_1_dataout , \n8位移位器_1_dataout_2 , R_q;
  wire [7:0] multiplexer_2_out;

  Button \u_复位  (.out(RST));
  Clock \u_时钟  (.out(\时钟_out ));
  Hex_Digit_Display hex_digit_display_1 (.value(X[7:4]));  // open: dp
  not not_1 (not_1_out, STOP);
  Hex_Digit_Display hex_digit_display_2 (.value(X[3:0]));  // open: dp
  Multiplexer #(.width(4), .enable("false")) multiplexer_1 (
    .in0(R_q), .in1(\_4位加法器_f ), .out(multiplexer_1_out), .sel(\_4位加法器_cout ));
  \_4位加法器  \_4位加法器  (.X(R_q), .F(\_4位加法器_f ), .Cout(\_4位加法器_cout ), .Cin(1'b1), .Y(Y));
  Hex_Digit_Display hex_digit_display_3 (.value(Y));  // open: dp
  Register #(.width(4), .trigger("falling"), .Select("low")) R (
    .D(\n8位移位器_1_dataout_2 ), .en(not_1_out), .Q(R_q), .clk(\时钟_out ), .clr(RST));
  Multiplexer #(.width(8), .enable("false")) multiplexer_2 (
    .in0({multiplexer_1_out, \商 }), .in1(X), .out(multiplexer_2_out), .sel(LOAD));
  \_8位移位器  \u_8位移位器_1  (
    .DataIn(multiplexer_2_out), .shamt(3'b001), .DataOut({\n8位移位器_1_dataout_2 , \n8位移位器_1_dataout }),
    .IN(\_4位加法器_cout ), .L_R(1'b1), .A_L(1'b1));
  Register #(.width(4), .trigger("falling"), .Select("low")) S (
    .D(\n8位移位器_1_dataout ), .en(not_1_out), .Q(\商 ), .clk(\时钟_out ), .clr(RST));
  Hex_Digit_Display hex_digit_display_4 (.value(\商 ));  // open: dp
  or or_1 (or_1_out, RST, \时钟_out );
  CNTR4U cntr4u_1 (
    .LD(1'b0), .CLR(RST), .D0(1'b0), .D1(1'b0), .D2(1'b0), .D3(1'b0), .ENP(not_1_out), .ENT(not_1_out),
    .Q0(cntr4u_1_q0[0]), .Q1(cntr4u_1_q0[1]), .Q2(cntr4u_1_q0[2]), .Q3(cntr4u_1_q0[3]), .CLK(or_1_out));  // open: RCO
  // Probe on X
  // Probe on Y
  Comparator #(.width(4)) comparator_1 (.a(cntr4u_1_q0), .b(4'b0000), .eq(LOAD));  // open: gt, lt
  Comparator #(.width(4)) comparator_2 (.a(cntr4u_1_q0), .b(4'b0100), .gt(STOP));  // open: eq, lt
  // Probe on \商 

  // Other names for the same wires on the sheet: Z[3:0] = \商 

  // Notes on the sheet:
  //   输入引脚区
  //   /
  //   4位无符号数一位乘法器
  //   =
  //   输出引脚区
  //   =
endmodule
