// Logisim project lab5.circ as structural Verilog
module \ASCII码显示实验  (
  input  [7:0] ASCII_CODE,
  input  Sel
);

  wire [7:0] row1, row2, row3, row4, row5, row6, row7, row8, row9, row10, row11, row12, row13, row14, row15,
       row16, subtractor_1_out;

  Subtractor subtractor_1 (.a(ASCII_CODE), .b(8'h20), .out(subtractor_1_out), .bin(1'b0));  // open: bout
  ROM #(.addrWidth(16), .Select("high"), .simpleMode("false")) rom_1 (
    .addr({4'b0000, subtractor_1_out, 4'b0000}), .data(row1), .sel(Sel));
  ROM #(.addrWidth(16), .Select("high")) rom_2 (.addr({4'b0000, subtractor_1_out, 4'b0001}), .data(row2), .sel(Sel));
  ROM #(.addrWidth(16), .Select("high")) rom_3 (.addr({4'b0000, subtractor_1_out, 4'b0010}), .data(row3), .sel(Sel));
  ROM #(.addrWidth(16), .Select("high")) rom_4 (.addr({4'b0000, subtractor_1_out, 4'b0011}), .data(row4), .sel(Sel));
  ROM #(.addrWidth(16), .Select("high")) rom_5 (.addr({4'b0000, subtractor_1_out, 4'b0100}), .data(row5), .sel(Sel));
  ROM #(.addrWidth(16), .Select("high")) rom_6 (.addr({4'b0000, subtractor_1_out, 4'b0101}), .data(row6), .sel(Sel));
  ROM #(.addrWidth(16), .Select("high")) rom_7 (.addr({4'b0000, subtractor_1_out, 4'b0110}), .data(row7), .sel(Sel));
  ROM #(.addrWidth(16), .Select("high")) rom_8 (.addr({4'b0000, subtractor_1_out, 4'b0111}), .data(row8), .sel(Sel));
  DotMatrix #(.inputtype("row"), .matrixcols(8), .matrixrows(16)) dotmatrix_1 (
    .row0(row1), .row1(row2), .row2(row3), .row3(row4), .row4(row5), .row5(row6), .row6(row7), .row7(row8),
    .row8(row9), .row9(row10), .row10(row11), .row11(row12), .row12(row13), .row13(row14), .row14(row15),
    .row15(row16));
  ROM #(.addrWidth(16), .Select("high")) rom_9 (.addr({4'b0000, subtractor_1_out, 4'b1000}), .data(row9), .sel(Sel));
  ROM #(.addrWidth(16), .Select("high")) rom_10 (.addr({4'b0000, subtractor_1_out, 4'b1001}), .data(row10), .sel(Sel));
  ROM #(.addrWidth(16), .Select("high")) rom_11 (.addr({4'b0000, subtractor_1_out, 4'b1010}), .data(row11), .sel(Sel));
  ROM #(.addrWidth(16), .Select("high")) rom_12 (.addr({4'b0000, subtractor_1_out, 4'b1011}), .data(row12), .sel(Sel));
  ROM #(.addrWidth(16), .Select("high")) rom_13 (.addr({4'b0000, subtractor_1_out, 4'b1100}), .data(row13), .sel(Sel));
  ROM #(.addrWidth(16), .Select("high")) rom_14 (.addr({4'b0000, subtractor_1_out, 4'b1101}), .data(row14), .sel(Sel));
  ROM #(.addrWidth(16), .Select("high")) rom_15 (.addr({4'b0000, subtractor_1_out, 4'b1110}), .data(row15), .sel(Sel));
  ROM #(.addrWidth(16), .Select("high")) rom_16 (.addr({4'b0000, subtractor_1_out, 4'b1111}), .data(row16), .sel(Sel));

  // Other names for the same wires on the sheet: Code[7:0] = ASCII_CODE

  // Notes on the sheet:
  //   ASCII字库地址
  //   contents of rom_1 (hex, n*v repeats v):
  //   18*0 18 3c 3c 3c 18 18 18 0 18 18 5*0 63 63 63 22 14*0 36 36 7f 36 36 36 7f 36 36 4*0 c c 3e 63 61
  //   60 3e 3 3 43 63 3e c c 7*0 61 63 6 c 18 33 63 7*0 1c 36 36 1c 3b 6e 66 66 3b 5*0 30 30 30 60 13*0 c
  //   18 18 4*30 18 18 c 6*0 18 c c 4*6 c c 18 8*0 42 66 3c ff 3c 66 42 9*0 18 18 18 ff 18 18 18 15*0 18
  //   18 18 30 9*0 ff 18*0 18 18 6*0 1 3 7 e 1c 38 70 e0 c0 80 6*0 3e 63 63 63 6b 6b 63 63 63 3e 6*0 c 1c
  //   3c 6*c 3f 6*0 3e 63 3 6 c 18 30 61 63 7f 6*0 3e 63 3 3 1e 3 3 3 63 3e 6*0 6 e 1e 36 66 66 7f 6 6 f
  //   6*0 7f 60 60 60 7e 3 3 63 73 3e 6*0 1c 30 60 60 7e 4*63 3e 6*0 7f 63 3 6 6 c c 18 18 18 6*0 3e 63 63
  //   63 3e 4*63 3e 6*0 3e 4*63 3f 3 3 6 3c 9*0 18 18 0 0 0 18 18 9*0 18 18 0 0 0 18 18 18 30 5*0 6 c 18
  //   30 60 30 18 c 6 10*0 7e 0 0 7e 9*0 60 30 18 c 6 c 18 30 60 6*0 3e 63 63 6 c c c 0 c c 6*0 3e 63 63
  //   6f 6b 6b 6e 60 60 3e 6*0 8 1c 36 63 63 63 7f 63 63 63 6*0 7e 33 33 33 3e 4*33 7e 6*0 1e 33 61 4*60
  //   61 33 1e 6*0 7c 36 6*33 36 7c 6*0 7f 33 31 34 3c 34 30 31 33 7f 6*0 7f 33 31 34 3c 34 30 30 30 78
  //   6*0 1e 33 61 60 60 6f 63 63 37 1d 6*0 4*63 7f 5*63 6*0 3c 8*18 3c 6*0 f 6*6 66 66 3c 6*0 73 33 36 36
  //   3c 36 36 33 33 73 6*0 78 6*30 31 33 7f 6*0 63 77 7f 6b 6*63 6*0 63 63 73 7b 7f 6f 67 63 63 63 6*0 1c
  //   36 6*63 36 1c 6*0 7e 33 33 33 3e 4*30 78 6*0 3e 6*63 6b 6f 3e 6 7 4*0 7e 33 33 33 3e 36 36 33 33 73
  //   6*0 3e 63 63 30 1c 6 3 63 63 3e 6*0 ff db 99 6*18 3c 6*0 9*63 3e 6*0 7*63 36 1c 8 6*0 5*63 6b 6b 7f
  //   36 36 6*0 c3 c3 66 3c 18 18 3c 66 c3 c3 6*0 c3 c3 c3 66 3c 4*18 3c 6*0 7f 63 43 6 c 18 30 61 63 7f
  //   6*0 3c 8*30 3c 6*0 80 c0 e0 70 38 1c e 7 3 1 6*0 3c 8*c 3c 4*0 8 1c 36 63 24*0 ff 0 0 0 18 18 c 18*0
  //   3c 46 6 3e 66 66 3b 6*0 70 30 30 3c 36 4*33 6e 9*0 3e 63 60 60 60 63 3e 6*0 e 6 6 1e 36 4*66 3b 9*0
  //   3e 63 63 7e 60 63 3e 6*0 1c 36 32 30 7c 4*30 78 9*0 3b 4*66 3e 6 66 3c 4*0 70 30 30 36 3b 4*33 73
  //   6*0 c c 0 1c 5*c 1e 6*0 6 6 0 e 5*6 66 66 3c 4*0 70 30 30 33 33 36 3c 36 33 73 6*0 1c 8*c 1e 9*0 6e
  //   7f 5*6b 9*0 6e 6*33 9*0 3e 5*63 3e 9*0 6e 4*33 3e 30 30 78 7*0 3b 4*66 3e 6 6 f 7*0 6e 3b 33 30 30
  //   30 78 9*0 3e 63 38 e 3 63 3e 6*0 8 18 18 7e 4*18 1b e 9*0 6*66 3b 9*0 63 63 36 36 1c 1c 8 9*0 63 63
  //   63 6b 6b 7f 36 9*0 63 36 1c 1c 1c 36 63 9*0 5*63 3f 3 6 3c 7*0 7f 66 c 18 30 63 7f 6*0 e 18 18 18 70
  //   4*18 e 6*0 5*18 0 5*18 5*0 70 18 18 18 e 4*18 70 6*0 3b 6e 13*0 70 d8 d8 70
  //   contents of rom_2 (hex, n*v repeats v):
  //   18*0 18 3c 3c 3c 18 18 18 0 18 18 5*0 63 63 63 22 14*0 36 36 7f 36 36 36 7f 36 36 4*0 c c 3e 63 61
  //   60 3e 3 3 43 63 3e c c 7*0 61 63 6 c 18 33 63 7*0 1c 36 36 1c 3b 6e 66 66 3b 5*0 30 30 30 60 13*0 c
  //   18 18 4*30 18 18 c 6*0 18 c c 4*6 c c 18 8*0 42 66 3c ff 3c 66 42 9*0 18 18 18 ff 18 18 18 15*0 18
  //   18 18 30 9*0 ff 18*0 18 18 6*0 1 3 7 e 1c 38 70 e0 c0 80 6*0 3e 63 63 63 6b 6b 63 63 63 3e 6*0 c 1c
  //   3c 6*c 3f 6*0 3e 63 3 6 c 18 30 61 63 7f 6*0 3e 63 3 3 1e 3 3 3 63 3e 6*0 6 e 1e 36 66 66 7f 6 6 f
  //   6*0 7f 60 60 60 7e 3 3 63 73 3e 6*0 1c 30 60 60 7e 4*63 3e 6*0 7f 63 3 6 6 c c 18 18 18 6*0 3e 63 63
  //   63 3e 4*63 3e 6*0 3e 4*63 3f 3 3 6 3c 9*0 18 18 0 0 0 18 18 9*0 18 18 0 0 0 18 18 18 30 5*0 6 c 18
  //   30 60 30 18 c 6 10*0 7e 0 0 7e 9*0 60 30 18 c 6 c 18 30 60 6*0 3e 63 63 6 c c c 0 c c 6*0 3e 63 63
  //   6f 6b 6b 6e 60 60 3e 6*0 8 1c 36 63 63 63 7f 63 63 63 6*0 7e 33 33 33 3e 4*33 7e 6*0 1e 33 61 4*60
  //   61 33 1e 6*0 7c 36 6*33 36 7c 6*0 7f 33 31 34 3c 34 30 31 33 7f 6*0 7f 33 31 34 3c 34 30 30 30 78
  //   6*0 1e 33 61 60 60 6f 63 63 37 1d 6*0 4*63 7f 5*63 6*0 3c 8*18 3c 6*0 f 6*6 66 66 3c 6*0 73 33 36 36
  //   3c 36 36 33 33 73 6*0 78 6*30 31 33 7f 6*0 63 77 7f 6b 6*63 6*0 63 63 73 7b 7f 6f 67 63 63 63 6*0 1c
  //   36 6*63 36 1c 6*0 7e 33 33 33 3e 4*30 78 6*0 3e 6*63 6b 6f 3e 6 7 4*0 7e 33 33 33 3e 36 36 33 33 73
  //   6*0 3e 63 63 30 1c 6 3 63 63 3e 6*0 ff db 99 6*18 3c 6*0 9*63 3e 6*0 7*63 36 1c 8 6*0 5*63 6b 6b 7f
  //   36 36 6*0 c3 c3 66 3c 18 18 3c 66 c3 c3 6*0 c3 c3 c3 66 3c 4*18 3c 6*0 7f 63 43 6 c 18 30 61 63 7f
  //   6*0 3c 8*30 3c 6*0 80 c0 e0 70 38 1c e 7 3 1 6*0 3c 8*c 3c 4*0 8 1c 36 63 24*0 ff 0 0 0 18 18 c 18*0
  //   3c 46 6 3e 66 66 3b 6*0 70 30 30 3c 36 4*33 6e 9*0 3e 63 60 60 60 63 3e 6*0 e 6 6 1e 36 4*66 3b 9*0
  //   3e 63 63 7e 60 63 3e 6*0 1c 36 32 30 7c 4*30 78 9*0 3b 4*66 3e 6 66 3c 4*0 70 30 30 36 3b 4*33 73
  //   6*0 c c 0 1c 5*c 1e 6*0 6 6 0 e 5*6 66 66 3c 4*0 70 30 30 33 33 36 3c 36 33 73 6*0 1c 8*c 1e 9*0 6e
  //   7f 5*6b 9*0 6e 6*33 9*0 3e 5*63 3e 9*0 6e 4*33 3e 30 30 78 7*0 3b 4*66 3e 6 6 f 7*0 6e 3b 33 30 30
  //   30 78 9*0 3e 63 38 e 3 63 3e 6*0 8 18 18 7e 4*18 1b e 9*0 6*66 3b 9*0 63 63 36 36 1c 1c 8 9*0 63 63
  //   63 6b 6b 7f 36 9*0 63 36 1c 1c 1c 36 63 9*0 5*63 3f 3 6 3c 7*0 7f 66 c 18 30 63 7f 6*0 e 18 18 18 70
  //   4*18 e 6*0 5*18 0 5*18 5*0 70 18 18 18 e 4*18 70 6*0 3b 6e 13*0 70 d8 d8 70
  //   contents of rom_3 (hex, n*v repeats v):
  //   18*0 18 3c 3c 3c 18 18 18 0 18 18 5*0 63 63 63 22 14*0 36 36 7f 36 36 36 7f 36 36 4*0 c c 3e 63 61
  //   60 3e 3 3 43 63 3e c c 7*0 61 63 6 c 18 33 63 7*0 1c 36 36 1c 3b 6e 66 66 3b 5*0 30 30 30 60 13*0 c
  //   18 18 4*30 18 18 c 6*0 18 c c 4*6 c c 18 8*0 42 66 3c ff 3c 66 42 9*0 18 18 18 ff 18 18 18 15*0 18
  //   18 18 30 9*0 ff 18*0 18 18 6*0 1 3 7 e 1c 38 70 e0 c0 80 6*0 3e 63 63 63 6b 6b 63 63 63 3e 6*0 c 1c
  //   3c 6*c 3f 6*0 3e 63 3 6 c 18 30 61 63 7f 6*0 3e 63 3 3 1e 3 3 3 63 3e 6*0 6 e 1e 36 66 66 7f 6 6 f
  //   6*0 7f 60 60 60 7e 3 3 63 73 3e 6*0 1c 30 60 60 7e 4*63 3e 6*0 7f 63 3 6 6 c c 18 18 18 6*0 3e 63 63
  //   63 3e 4*63 3e 6*0 3e 4*63 3f 3 3 6 3c 9*0 18 18 0 0 0 18 18 9*0 18 18 0 0 0 18 18 18 30 5*0 6 c 18
  //   30 60 30 18 c 6 10*0 7e 0 0 7e 9*0 60 30 18 c 6 c 18 30 60 6*0 3e 63 63 6 c c c 0 c c 6*0 3e 63 63
  //   6f 6b 6b 6e 60 60 3e 6*0 8 1c 36 63 63 63 7f 63 63 63 6*0 7e 33 33 33 3e 4*33 7e 6*0 1e 33 61 4*60
  //   61 33 1e 6*0 7c 36 6*33 36 7c 6*0 7f 33 31 34 3c 34 30 31 33 7f 6*0 7f 33 31 34 3c 34 30 30 30 78
  //   6*0 1e 33 61 60 60 6f 63 63 37 1d 6*0 4*63 7f 5*63 6*0 3c 8*18 3c 6*0 f 6*6 66 66 3c 6*0 73 33 36 36
  //   3c 36 36 33 33 73 6*0 78 6*30 31 33 7f 6*0 63 77 7f 6b 6*63 6*0 63 63 73 7b 7f 6f 67 63 63 63 6*0 1c
  //   36 6*63 36 1c 6*0 7e 33 33 33 3e 4*30 78 6*0 3e 6*63 6b 6f 3e 6 7 4*0 7e 33 33 33 3e 36 36 33 33 73
  //   6*0 3e 63 63 30 1c 6 3 63 63 3e 6*0 ff db 99 6*18 3c 6*0 9*63 3e 6*0 7*63 36 1c 8 6*0 5*63 6b 6b 7f
  //   36 36 6*0 c3 c3 66 3c 18 18 3c 66 c3 c3 6*0 c3 c3 c3 66 3c 4*18 3c 6*0 7f 63 43 6 c 18 30 61 63 7f
  //   6*0 3c 8*30 3c 6*0 80 c0 e0 70 38 1c e 7 3 1 6*0 3c 8*c 3c 4*0 8 1c 36 63 24*0 ff 0 0 0 18 18 c 18*0
  //   3c 46 6 3e 66 66 3b 6*0 70 30 30 3c 36 4*33 6e 9*0 3e 63 60 60 60 63 3e 6*0 e 6 6 1e 36 4*66 3b 9*0
  //   3e 63 63 7e 60 63 3e 6*0 1c 36 32 30 7c 4*30 78 9*0 3b 4*66 3e 6 66 3c 4*0 70 30 30 36 3b 4*33 73
  //   6*0 c c 0 1c 5*c 1e 6*0 6 6 0 e 5*6 66 66 3c 4*0 70 30 30 33 33 36 3c 36 33 73 6*0 1c 8*c 1e 9*0 6e
  //   7f 5*6b 9*0 6e 6*33 9*0 3e 5*63 3e 9*0 6e 4*33 3e 30 30 78 7*0 3b 4*66 3e 6 6 f 7*0 6e 3b 33 30 30
  //   30 78 9*0 3e 63 38 e 3 63 3e 6*0 8 18 18 7e 4*18 1b e 9*0 6*66 3b 9*0 63 63 36 36 1c 1c 8 9*0 63 63
  //   63 6b 6b 7f 36 9*0 63 36 1c 1c 1c 36 63 9*0 5*63 3f 3 6 3c 7*0 7f 66 c 18 30 63 7f 6*0 e 18 18 18 70
  //   4*18 e 6*0 5*18 0 5*18 5*0 70 18 18 18 e 4*18 70 6*0 3b 6e 13*0 70 d8 d8 70
  //   contents of rom_4 (hex, n*v repeats v):
  //   18*0 18 3c 3c 3c 18 18 18 0 18 18 5*0 63 63 63 22 14*0 36 36 7f 36 36 36 7f 36 36 4*0 c c 3e 63 61
  //   60 3e 3 3 43 63 3e c c 7*0 61 63 6 c 18 33 63 7*0 1c 36 36 1c 3b 6e 66 66 3b 5*0 30 30 30 60 13*0 c
  //   18 18 4*30 18 18 c 6*0 18 c c 4*6 c c 18 8*0 42 66 3c ff 3c 66 42 9*0 18 18 18 ff 18 18 18 15*0 18
  //   18 18 30 9*0 ff 18*0 18 18 6*0 1 3 7 e 1c 38 70 e0 c0 80 6*0 3e 63 63 63 6b 6b 63 63 63 3e 6*0 c 1c
  //   3c 6*c 3f 6*0 3e 63 3 6 c 18 30 61 63 7f 6*0 3e 63 3 3 1e 3 3 3 63 3e 6*0 6 e 1e 36 66 66 7f 6 6 f
  //   6*0 7f 60 60 60 7e 3 3 63 73 3e 6*0 1c 30 60 60 7e 4*63 3e 6*0 7f 63 3 6 6 c c 18 18 18 6*0 3e 63 63
  //   63 3e 4*63 3e 6*0 3e 4*63 3f 3 3 6 3c 9*0 18 18 0 0 0 18 18 9*0 18 18 0 0 0 18 18 18 30 5*0 6 c 18
  //   30 60 30 18 c 6 10*0 7e 0 0 7e 9*0 60 30 18 c 6 c 18 30 60 6*0 3e 63 63 6 c c c 0 c c 6*0 3e 63 63
  //   6f 6b 6b 6e 60 60 3e 6*0 8 1c 36 63 63 63 7f 63 63 63 6*0 7e 33 33 33 3e 4*33 7e 6*0 1e 33 61 4*60
  //   61 33 1e 6*0 7c 36 6*33 36 7c 6*0 7f 33 31 34 3c 34 30 31 33 7f 6*0 7f 33 31 34 3c 34 30 30 30 78
  //   6*0 1e 33 61 60 60 6f 63 63 37 1d 6*0 4*63 7f 5*63 6*0 3c 8*18 3c 6*0 f 6*6 66 66 3c 6*0 73 33 36 36
  //   3c 36 36 33 33 73 6*0 78 6*30 31 33 7f 6*0 63 77 7f 6b 6*63 6*0 63 63 73 7b 7f 6f 67 63 63 63 6*0 1c
  //   36 6*63 36 1c 6*0 7e 33 33 33 3e 4*30 78 6*0 3e 6*63 6b 6f 3e 6 7 4*0 7e 33 33 33 3e 36 36 33 33 73
  //   6*0 3e 63 63 30 1c 6 3 63 63 3e 6*0 ff db 99 6*18 3c 6*0 9*63 3e 6*0 7*63 36 1c 8 6*0 5*63 6b 6b 7f
  //   36 36 6*0 c3 c3 66 3c 18 18 3c 66 c3 c3 6*0 c3 c3 c3 66 3c 4*18 3c 6*0 7f 63 43 6 c 18 30 61 63 7f
  //   6*0 3c 8*30 3c 6*0 80 c0 e0 70 38 1c e 7 3 1 6*0 3c 8*c 3c 4*0 8 1c 36 63 24*0 ff 0 0 0 18 18 c 18*0
  //   3c 46 6 3e 66 66 3b 6*0 70 30 30 3c 36 4*33 6e 9*0 3e 63 60 60 60 63 3e 6*0 e 6 6 1e 36 4*66 3b 9*0
  //   3e 63 63 7e 60 63 3e 6*0 1c 36 32 30 7c 4*30 78 9*0 3b 4*66 3e 6 66 3c 4*0 70 30 30 36 3b 4*33 73
  //   6*0 c c 0 1c 5*c 1e 6*0 6 6 0 e 5*6 66 66 3c 4*0 70 30 30 33 33 36 3c 36 33 73 6*0 1c 8*c 1e 9*0 6e
  //   7f 5*6b 9*0 6e 6*33 9*0 3e 5*63 3e 9*0 6e 4*33 3e 30 30 78 7*0 3b 4*66 3e 6 6 f 7*0 6e 3b 33 30 30
  //   30 78 9*0 3e 63 38 e 3 63 3e 6*0 8 18 18 7e 4*18 1b e 9*0 6*66 3b 9*0 63 63 36 36 1c 1c 8 9*0 63 63
  //   63 6b 6b 7f 36 9*0 63 36 1c 1c 1c 36 63 9*0 5*63 3f 3 6 3c 7*0 7f 66 c 18 30 63 7f 6*0 e 18 18 18 70
  //   4*18 e 6*0 5*18 0 5*18 5*0 70 18 18 18 e 4*18 70 6*0 3b 6e 13*0 70 d8 d8 70
  //   contents of rom_5 (hex, n*v repeats v):
  //   18*0 18 3c 3c 3c 18 18 18 0 18 18 5*0 63 63 63 22 14*0 36 36 7f 36 36 36 7f 36 36 4*0 c c 3e 63 61
  //   60 3e 3 3 43 63 3e c c 7*0 61 63 6 c 18 33 63 7*0 1c 36 36 1c 3b 6e 66 66 3b 5*0 30 30 30 60 13*0 c
  //   18 18 4*30 18 18 c 6*0 18 c c 4*6 c c 18 8*0 42 66 3c ff 3c 66 42 9*0 18 18 18 ff 18 18 18 15*0 18
  //   18 18 30 9*0 ff 18*0 18 18 6*0 1 3 7 e 1c 38 70 e0 c0 80 6*0 3e 63 63 63 6b 6b 63 63 63 3e 6*0 c 1c
  //   3c 6*c 3f 6*0 3e 63 3 6 c 18 30 61 63 7f 6*0 3e 63 3 3 1e 3 3 3 63 3e 6*0 6 e 1e 36 66 66 7f 6 6 f
  //   6*0 7f 60 60 60 7e 3 3 63 73 3e 6*0 1c 30 60 60 7e 4*63 3e 6*0 7f 63 3 6 6 c c 18 18 18 6*0 3e 63 63
  //   63 3e 4*63 3e 6*0 3e 4*63 3f 3 3 6 3c 9*0 18 18 0 0 0 18 18 9*0 18 18 0 0 0 18 18 18 30 5*0 6 c 18
  //   30 60 30 18 c 6 10*0 7e 0 0 7e 9*0 60 30 18 c 6 c 18 30 60 6*0 3e 63 63 6 c c c 0 c c 6*0 3e 63 63
  //   6f 6b 6b 6e 60 60 3e 6*0 8 1c 36 63 63 63 7f 63 63 63 6*0 7e 33 33 33 3e 4*33 7e 6*0 1e 33 61 4*60
  //   61 33 1e 6*0 7c 36 6*33 36 7c 6*0 7f 33 31 34 3c 34 30 31 33 7f 6*0 7f 33 31 34 3c 34 30 30 30 78
  //   6*0 1e 33 61 60 60 6f 63 63 37 1d 6*0 4*63 7f 5*63 6*0 3c 8*18 3c 6*0 f 6*6 66 66 3c 6*0 73 33 36 36
  //   3c 36 36 33 33 73 6*0 78 6*30 31 33 7f 6*0 63 77 7f 6b 6*63 6*0 63 63 73 7b 7f 6f 67 63 63 63 6*0 1c
  //   36 6*63 36 1c 6*0 7e 33 33 33 3e 4*30 78 6*0 3e 6*63 6b 6f 3e 6 7 4*0 7e 33 33 33 3e 36 36 33 33 73
  //   6*0 3e 63 63 30 1c 6 3 63 63 3e 6*0 ff db 99 6*18 3c 6*0 9*63 3e 6*0 7*63 36 1c 8 6*0 5*63 6b 6b 7f
  //   36 36 6*0 c3 c3 66 3c 18 18 3c 66 c3 c3 6*0 c3 c3 c3 66 3c 4*18 3c 6*0 7f 63 43 6 c 18 30 61 63 7f
  //   6*0 3c 8*30 3c 6*0 80 c0 e0 70 38 1c e 7 3 1 6*0 3c 8*c 3c 4*0 8 1c 36 63 24*0 ff 0 0 0 18 18 c 18*0
  //   3c 46 6 3e 66 66 3b 6*0 70 30 30 3c 36 4*33 6e 9*0 3e 63 60 60 60 63 3e 6*0 e 6 6 1e 36 4*66 3b 9*0
  //   3e 63 63 7e 60 63 3e 6*0 1c 36 32 30 7c 4*30 78 9*0 3b 4*66 3e 6 66 3c 4*0 70 30 30 36 3b 4*33 73
  //   6*0 c c 0 1c 5*c 1e 6*0 6 6 0 e 5*6 66 66 3c 4*0 70 30 30 33 33 36 3c 36 33 73 6*0 1c 8*c 1e 9*0 6e
  //   7f 5*6b 9*0 6e 6*33 9*0 3e 5*63 3e 9*0 6e 4*33 3e 30 30 78 7*0 3b 4*66 3e 6 6 f 7*0 6e 3b 33 30 30
  //   30 78 9*0 3e 63 38 e 3 63 3e 6*0 8 18 18 7e 4*18 1b e 9*0 6*66 3b 9*0 63 63 36 36 1c 1c 8 9*0 63 63
  //   63 6b 6b 7f 36 9*0 63 36 1c 1c 1c 36 63 9*0 5*63 3f 3 6 3c 7*0 7f 66 c 18 30 63 7f 6*0 e 18 18 18 70
  //   4*18 e 6*0 5*18 0 5*18 5*0 70 18 18 18 e 4*18 70 6*0 3b 6e 13*0 70 d8 d8 70
  //   contents of rom_6 (hex, n*v repeats v):
  //   18*0 18 3c 3c 3c 18 18 18 0 18 18 5*0 63 63 63 22 14*0 36 36 7f 36 36 36 7f 36 36 4*0 c c 3e 63 61
  //   60 3e 3 3 43 63 3e c c 7*0 61 63 6 c 18 33 63 7*0 1c 36 36 1c 3b 6e 66 66 3b 5*0 30 30 30 60 13*0 c
  //   18 18 4*30 18 18 c 6*0 18 c c 4*6 c c 18 8*0 42 66 3c ff 3c 66 42 9*0 18 18 18 ff 18 18 18 15*0 18
  //   18 18 30 9*0 ff 18*0 18 18 6*0 1 3 7 e 1c 38 70 e0 c0 80 6*0 3e 63 63 63 6b 6b 63 63 63 3e 6*0 c 1c
  //   3c 6*c 3f 6*0 3e 63 3 6 c 18 30 61 63 7f 6*0 3e 63 3 3 1e 3 3 3 63 3e 6*0 6 e 1e 36 66 66 7f 6 6 f
  //   6*0 7f 60 60 60 7e 3 3 63 73 3e 6*0 1c 30 60 60 7e 4*63 3e 6*0 7f 63 3 6 6 c c 18 18 18 6*0 3e 63 63
  //   63 3e 4*63 3e 6*0 3e 4*63 3f 3 3 6 3c 9*0 18 18 0 0 0 18 18 9*0 18 18 0 0 0 18 18 18 30 5*0 6 c 18
  //   30 60 30 18 c 6 10*0 7e 0 0 7e 9*0 60 30 18 c 6 c 18 30 60 6*0 3e 63 63 6 c c c 0 c c 6*0 3e 63 63
  //   6f 6b 6b 6e 60 60 3e 6*0 8 1c 36 63 63 63 7f 63 63 63 6*0 7e 33 33 33 3e 4*33 7e 6*0 1e 33 61 4*60
  //   61 33 1e 6*0 7c 36 6*33 36 7c 6*0 7f 33 31 34 3c 34 30 31 33 7f 6*0 7f 33 31 34 3c 34 30 30 30 78
  //   6*0 1e 33 61 60 60 6f 63 63 37 1d 6*0 4*63 7f 5*63 6*0 3c 8*18 3c 6*0 f 6*6 66 66 3c 6*0 73 33 36 36
  //   3c 36 36 33 33 73 6*0 78 6*30 31 33 7f 6*0 63 77 7f 6b 6*63 6*0 63 63 73 7b 7f 6f 67 63 63 63 6*0 1c
  //   36 6*63 36 1c 6*0 7e 33 33 33 3e 4*30 78 6*0 3e 6*63 6b 6f 3e 6 7 4*0 7e 33 33 33 3e 36 36 33 33 73
  //   6*0 3e 63 63 30 1c 6 3 63 63 3e 6*0 ff db 99 6*18 3c 6*0 9*63 3e 6*0 7*63 36 1c 8 6*0 5*63 6b 6b 7f
  //   36 36 6*0 c3 c3 66 3c 18 18 3c 66 c3 c3 6*0 c3 c3 c3 66 3c 4*18 3c 6*0 7f 63 43 6 c 18 30 61 63 7f
  //   6*0 3c 8*30 3c 6*0 80 c0 e0 70 38 1c e 7 3 1 6*0 3c 8*c 3c 4*0 8 1c 36 63 24*0 ff 0 0 0 18 18 c 18*0
  //   3c 46 6 3e 66 66 3b 6*0 70 30 30 3c 36 4*33 6e 9*0 3e 63 60 60 60 63 3e 6*0 e 6 6 1e 36 4*66 3b 9*0
  //   3e 63 63 7e 60 63 3e 6*0 1c 36 32 30 7c 4*30 78 9*0 3b 4*66 3e 6 66 3c 4*0 70 30 30 36 3b 4*33 73
  //   6*0 c c 0 1c 5*c 1e 6*0 6 6 0 e 5*6 66 66 3c 4*0 70 30 30 33 33 36 3c 36 33 73 6*0 1c 8*c 1e 9*0 6e
  //   7f 5*6b 9*0 6e 6*33 9*0 3e 5*63 3e 9*0 6e 4*33 3e 30 30 78 7*0 3b 4*66 3e 6 6 f 7*0 6e 3b 33 30 30
  //   30 78 9*0 3e 63 38 e 3 63 3e 6*0 8 18 18 7e 4*18 1b e 9*0 6*66 3b 9*0 63 63 36 36 1c 1c 8 9*0 63 63
  //   63 6b 6b 7f 36 9*0 63 36 1c 1c 1c 36 63 9*0 5*63 3f 3 6 3c 7*0 7f 66 c 18 30 63 7f 6*0 e 18 18 18 70
  //   4*18 e 6*0 5*18 0 5*18 5*0 70 18 18 18 e 4*18 70 6*0 3b 6e 13*0 70 d8 d8 70
  //   contents of rom_7 (hex, n*v repeats v):
  //   18*0 18 3c 3c 3c 18 18 18 0 18 18 5*0 63 63 63 22 14*0 36 36 7f 36 36 36 7f 36 36 4*0 c c 3e 63 61
  //   60 3e 3 3 43 63 3e c c 7*0 61 63 6 c 18 33 63 7*0 1c 36 36 1c 3b 6e 66 66 3b 5*0 30 30 30 60 13*0 c
  //   18 18 4*30 18 18 c 6*0 18 c c 4*6 c c 18 8*0 42 66 3c ff 3c 66 42 9*0 18 18 18 ff 18 18 18 15*0 18
  //   18 18 30 9*0 ff 18*0 18 18 6*0 1 3 7 e 1c 38 70 e0 c0 80 6*0 3e 63 63 63 6b 6b 63 63 63 3e 6*0 c 1c
  //   3c 6*c 3f 6*0 3e 63 3 6 c 18 30 61 63 7f 6*0 3e 63 3 3 1e 3 3 3 63 3e 6*0 6 e 1e 36 66 66 7f 6 6 f
  //   6*0 7f 60 60 60 7e 3 3 63 73 3e 6*0 1c 30 60 60 7e 4*63 3e 6*0 7f 63 3 6 6 c c 18 18 18 6*0 3e 63 63
  //   63 3e 4*63 3e 6*0 3e 4*63 3f 3 3 6 3c 9*0 18 18 0 0 0 18 18 9*0 18 18 0 0 0 18 18 18 30 5*0 6 c 18
  //   30 60 30 18 c 6 10*0 7e 0 0 7e 9*0 60 30 18 c 6 c 18 30 60 6*0 3e 63 63 6 c c c 0 c c 6*0 3e 63 63
  //   6f 6b 6b 6e 60 60 3e 6*0 8 1c 36 63 63 63 7f 63 63 63 6*0 7e 33 33 33 3e 4*33 7e 6*0 1e 33 61 4*60
  //   61 33 1e 6*0 7c 36 6*33 36 7c 6*0 7f 33 31 34 3c 34 30 31 33 7f 6*0 7f 33 31 34 3c 34 30 30 30 78
  //   6*0 1e 33 61 60 60 6f 63 63 37 1d 6*0 4*63 7f 5*63 6*0 3c 8*18 3c 6*0 f 6*6 66 66 3c 6*0 73 33 36 36
  //   3c 36 36 33 33 73 6*0 78 6*30 31 33 7f 6*0 63 77 7f 6b 6*63 6*0 63 63 73 7b 7f 6f 67 63 63 63 6*0 1c
  //   36 6*63 36 1c 6*0 7e 33 33 33 3e 4*30 78 6*0 3e 6*63 6b 6f 3e 6 7 4*0 7e 33 33 33 3e 36 36 33 33 73
  //   6*0 3e 63 63 30 1c 6 3 63 63 3e 6*0 ff db 99 6*18 3c 6*0 9*63 3e 6*0 7*63 36 1c 8 6*0 5*63 6b 6b 7f
  //   36 36 6*0 c3 c3 66 3c 18 18 3c 66 c3 c3 6*0 c3 c3 c3 66 3c 4*18 3c 6*0 7f 63 43 6 c 18 30 61 63 7f
  //   6*0 3c 8*30 3c 6*0 80 c0 e0 70 38 1c e 7 3 1 6*0 3c 8*c 3c 4*0 8 1c 36 63 24*0 ff 0 0 0 18 18 c 18*0
  //   3c 46 6 3e 66 66 3b 6*0 70 30 30 3c 36 4*33 6e 9*0 3e 63 60 60 60 63 3e 6*0 e 6 6 1e 36 4*66 3b 9*0
  //   3e 63 63 7e 60 63 3e 6*0 1c 36 32 30 7c 4*30 78 9*0 3b 4*66 3e 6 66 3c 4*0 70 30 30 36 3b 4*33 73
  //   6*0 c c 0 1c 5*c 1e 6*0 6 6 0 e 5*6 66 66 3c 4*0 70 30 30 33 33 36 3c 36 33 73 6*0 1c 8*c 1e 9*0 6e
  //   7f 5*6b 9*0 6e 6*33 9*0 3e 5*63 3e 9*0 6e 4*33 3e 30 30 78 7*0 3b 4*66 3e 6 6 f 7*0 6e 3b 33 30 30
  //   30 78 9*0 3e 63 38 e 3 63 3e 6*0 8 18 18 7e 4*18 1b e 9*0 6*66 3b 9*0 63 63 36 36 1c 1c 8 9*0 63 63
  //   63 6b 6b 7f 36 9*0 63 36 1c 1c 1c 36 63 9*0 5*63 3f 3 6 3c 7*0 7f 66 c 18 30 63 7f 6*0 e 18 18 18 70
  //   4*18 e 6*0 5*18 0 5*18 5*0 70 18 18 18 e 4*18 70 6*0 3b 6e 13*0 70 d8 d8 70
  //   contents of rom_8 (hex, n*v repeats v):
  //   18*0 18 3c 3c 3c 18 18 18 0 18 18 5*0 63 63 63 22 14*0 36 36 7f 36 36 36 7f 36 36 4*0 c c 3e 63 61
  //   60 3e 3 3 43 63 3e c c 7*0 61 63 6 c 18 33 63 7*0 1c 36 36 1c 3b 6e 66 66 3b 5*0 30 30 30 60 13*0 c
  //   18 18 4*30 18 18 c 6*0 18 c c 4*6 c c 18 8*0 42 66 3c ff 3c 66 42 9*0 18 18 18 ff 18 18 18 15*0 18
  //   18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
  //   contents of rom_9 (hex, n*v repeats v):
  //   18*0 18 3c 3c 3c 18 18 18 0 18 18 5*0 63 63 63 22 14*0 36 36 7f 36 36 36 7f 36 36 4*0 c c 3e 63 61
  //   60 3e 3 3 43 63 3e c c 7*0 61 63 6 c 18 33 63 7*0 1c 36 36 1c 3b 6e 66 66 3b 5*0 30 30 30 60 13*0 c
  //   18 18 4*30 18 18 c 6*0 18 c c 4*6 c c 18 8*0 42 66 3c ff 3c 66 42 9*0 18 18 18 ff 18 18 18 15*0 18
  //   18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
  //   contents of rom_10 (hex, n*v repeats v):
  //   18*0 18 3c 3c 3c 18 18 18 0 18 18 5*0 63 63 63 22 14*0 36 36 7f 36 36 36 7f 36 36 4*0 c c 3e 63 61
  //   60 3e 3 3 43 63 3e c c 7*0 61 63 6 c 18 33 63 7*0 1c 36 36 1c 3b 6e 66 66 3b 5*0 30 30 30 60 13*0 c
  //   18 18 4*30 18 18 c 6*0 18 c c 4*6 c c 18 8*0 42 66 3c ff 3c 66 42 9*0 18 18 18 ff 18 18 18 15*0 18
  //   18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
  //   contents of rom_11 (hex, n*v repeats v):
  //   18*0 18 3c 3c 3c 18 18 18 0 18 18 5*0 63 63 63 22 14*0 36 36 7f 36 36 36 7f 36 36 4*0 c c 3e 63 61
  //   60 3e 3 3 43 63 3e c c 7*0 61 63 6 c 18 33 63 7*0 1c 36 36 1c 3b 6e 66 66 3b 5*0 30 30 30 60 13*0 c
  //   18 18 4*30 18 18 c 6*0 18 c c 4*6 c c 18 8*0 42 66 3c ff 3c 66 42 9*0 18 18 18 ff 18 18 18 15*0 18
  //   18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
  //   contents of rom_12 (hex, n*v repeats v):
  //   18*0 18 3c 3c 3c 18 18 18 0 18 18 5*0 63 63 63 22 14*0 36 36 7f 36 36 36 7f 36 36 4*0 c c 3e 63 61
  //   60 3e 3 3 43 63 3e c c 7*0 61 63 6 c 18 33 63 7*0 1c 36 36 1c 3b 6e 66 66 3b 5*0 30 30 30 60 13*0 c
  //   18 18 4*30 18 18 c 6*0 18 c c 4*6 c c 18 8*0 42 66 3c ff 3c 66 42 9*0 18 18 18 ff 18 18 18 15*0 18
  //   18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
  //   contents of rom_13 (hex, n*v repeats v):
  //   18*0 18 3c 3c 3c 18 18 18 0 18 18 5*0 63 63 63 22 14*0 36 36 7f 36 36 36 7f 36 36 4*0 c c 3e 63 61
  //   60 3e 3 3 43 63 3e c c 7*0 61 63 6 c 18 33 63 7*0 1c 36 36 1c 3b 6e 66 66 3b 5*0 30 30 30 60 13*0 c
  //   18 18 4*30 18 18 c 6*0 18 c c 4*6 c c 18 8*0 42 66 3c ff 3c 66 42 9*0 18 18 18 ff 18 18 18 15*0 18
  //   18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
  //   contents of rom_14 (hex, n*v repeats v):
  //   18*0 18 3c 3c 3c 18 18 18 0 18 18 5*0 63 63 63 22 14*0 36 36 7f 36 36 36 7f 36 36 4*0 c c 3e 63 61
  //   60 3e 3 3 43 63 3e c c 7*0 61 63 6 c 18 33 63 7*0 1c 36 36 1c 3b 6e 66 66 3b 5*0 30 30 30 60 13*0 c
  //   18 18 4*30 18 18 c 6*0 18 c c 4*6 c c 18 8*0 42 66 3c ff 3c 66 42 9*0 18 18 18 ff 18 18 18 15*0 18
  //   18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
  //   contents of rom_15 (hex, n*v repeats v):
  //   18*0 18 3c 3c 3c 18 18 18 0 18 18 5*0 63 63 63 22 14*0 36 36 7f 36 36 36 7f 36 36 4*0 c c 3e 63 61
  //   60 3e 3 3 43 63 3e c c 7*0 61 63 6 c 18 33 63 7*0 1c 36 36 1c 3b 6e 66 66 3b 5*0 30 30 30 60 13*0 c
  //   18 18 4*30 18 18 c 6*0 18 c c 4*6 c c 18 8*0 42 66 3c ff 3c 66 42 9*0 18 18 18 ff 18 18 18 15*0 18
  //   18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
  //   contents of rom_16 (hex, n*v repeats v):
  //   18*0 18 3c 3c 3c 18 18 18 0 18 18 5*0 63 63 63 22 14*0 36 36 7f 36 36 36 7f 36 36 4*0 c c 3e 63 61
  //   60 3e 3 3 43 63 3e c c 7*0 61 63 6 c 18 33 63 7*0 1c 36 36 1c 3b 6e 66 66 3b 5*0 30 30 30 60 13*0 c
  //   18 18 4*30 18 18 c 6*0 18 c c 4*6 c c 18 8*0 42 66 3c ff 3c 66 42 9*0 18 18 18 ff 18 18 18 15*0 18
  //   18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
endmodule

module IFU (
  input  [31:0] Initial_Address,
  input  [31:0] Imm,
  input  [31:0] BusA,
  input  CLK,
  input  Reset,
  input  Halt,
  input  NxtASrc,
  input  NxtBSrc,
  output [31:0] PC
);

  wire not_1_out;
  wire [31:0] multiplexer_1_out, multiplexer_2_out, multiplexer_3_out, NxtPC;

  Multiplexer #(.width(32), .enable("false")) multiplexer_1 (
    .in0(NxtPC), .in1(Initial_Address), .out(multiplexer_1_out), .sel(Reset));
  not not_1 (not_1_out, Halt);
  Register #(.width(32), .Select("high")) u_PC (
    .D(multiplexer_1_out), .en(not_1_out), .Q(PC), .clk(CLK), .clr(1'b0), .cs(1'b1), .preset(1'b0));
  Multiplexer #(.width(32), .enable("false")) multiplexer_2 (
    .in0(PC), .in1(BusA), .out(multiplexer_2_out), .sel(NxtASrc));
  Multiplexer #(.width(32), .enable("false")) multiplexer_3 (
    .in0(32'h4), .in1(Imm), .out(multiplexer_3_out), .sel(NxtBSrc));
  \_32位加法器  \u_32位加法器_1  (
    .Cin(1'b0), .X(multiplexer_2_out), .Y(multiplexer_3_out), .S(NxtPC));  // open: Cout, OF, CF, ZF, SF
  ROM #(.addrWidth(16), .dataWidth(32), .Select("high")) \u_指令存储器  ();  // open: addr, data

  // Other names for the same wires on the sheet: Init_Addr[31:0] = Initial_Address

  // Notes on the sheet:
  //   Imm: pull=down
  //   NxtASrc: pull=down
  //   Halt: pull=down
  //   BusA: pull=down
  //   NxtBSrc: pull=down
  //   指令存储器的数据位设置为32位，地址位设置为16位。存储器按照32位字长编址，地址位最低2位舍弃。
  //   输入信号
  //   输出信号
  //   contents of 指令存储器 (hex, n*v repeats v):
  //   100*0 12b7 fff28293 5de1863 288000ef 112623
endmodule

module \立即数扩展器  (
  input  [31:0] Instr,
  input  [2:0] Extop,
  output [31:0] imm
);

  wire [31:0] bit_extender_1_out, bit_extender_2_out, bit_extender_3_out, bit_extender_4_out;

  assign bit_extender_1_out = {{20{Instr[31]}}, Instr[31:20]};  // Bit_Extender bit_extender_1
  assign bit_extender_2_out = {{20{Instr[31]}}, {Instr[31:25], Instr[11:7]}};  // Bit_Extender bit_extender_2
  assign bit_extender_3_out = {{19{Instr[31]}}, {Instr[31], Instr[7], Instr[30:25], Instr[11:8], 1'b0}};  // Bit_Extender bit_extender_3
  assign bit_extender_4_out = {{11{Instr[31]}}, {Instr[31], Instr[19:12], Instr[20], Instr[30:21], 1'b0}};  // Bit_Extender bit_extender_4
  Multiplexer #(.select(3), .width(32), .enable("false")) multiplexer_1 (
    .in0(bit_extender_1_out), .in1({Instr[31:12], {12{1'b0}}}), .in2(bit_extender_2_out),
    .in3(bit_extender_3_out), .in4(bit_extender_4_out), .in5(bit_extender_4_out), .out(imm), .sel(Extop));  // open: in6, in7

  // Notes on the sheet:
  //   Extop: pull=down
  //   Instr: pull=down
  //   输入引脚
  //   I
  //   U
  //   S
  //   B
  //   J
  //   输出引脚
endmodule

module IDU (
  input  [31:0] IR,
  input  [31:0] BusW,
  input  [31:0] PC,
  input  [2:0] ExtOp,
  input  RegWr,
  input  ALUASrc,
  input  [1:0] ALUBSrc,
  output [31:0] DataA,
  output [31:0] DataB,
  output [31:0] BusA,
  output [6:0] OpCode,
  output [31:0] BusB,
  output [31:0] Imm,
  output [2:0] Funct3,
  output [6:0] Funct7
);

  wire clk;

  Clock clock_1 (.out(clk));
  // Probe on IR[24:20]
  \立即数扩展器  \u_立即数扩展器_1  (.Instr(IR), .Extop(ExtOp), .imm(Imm));
  // Probe on IR[11:7]
  // Probe on IR[19:15]
  RegFile regfile_1 (
    .R1_num(IR[19:15]), .R2_num(IR[24:20]), .Din(BusW), .Reg1Out(BusA), .Reg2Out(BusB),
    .Write_Reg_num(IR[11:7]), .Write_Enable(RegWr), .Clock(clk));
  Multiplexer #(.width(32), .enable("false")) multiplexer_1 (.in0(BusA), .in1(PC), .out(DataA), .sel(ALUASrc));
  Multiplexer #(.select(2), .width(32), .enable("false")) multiplexer_2 (
    .in0(BusB), .in1(32'h4), .in2(Imm), .out(DataB), .sel(ALUBSrc));  // open: in3

  assign Funct3 = IR[14:12];
  assign Funct7 = IR[31:25];
  assign OpCode = IR[6:0];

  // Other names for the same wires on the sheet: DataIn[31:0] = BusB; op[6:0] = IR[6:0]

  // Notes on the sheet:
  //   ALUASrc: pull=down
  //   PC: pull=down
  //   ExtOp: pull=down
  //   RegWr: pull=down
  //   BusW: pull=down
  //   ALUBSrc: pull=down
  //   指令解析
  //   输入信号
  //   rd
  //   rs1
  //   rs2
  //   imm
  //   访问寄存器堆
  //   输出信号
  //   输出数据
endmodule

module RegFile (
  input  [4:0] R1_num,
  input  [4:0] R2_num,
  input  [31:0] Din,
  input  [4:0] Write_Reg_num,
  input  Write_Enable,
  input  Clock,
  output [31:0] Reg1Out,
  output [31:0] Reg2Out
);

  wire and_1_out, and_2_out, and_3_out, and_4_out, and_5_out, and_6_out, and_7_out, and_8_out, and_9_out,
       and_10_out, and_11_out, and_12_out, and_13_out, and_14_out, and_15_out, and_16_out, and_17_out,
       and_18_out, and_19_out, and_20_out, and_21_out, and_22_out, and_23_out, and_24_out, and_25_out,
       and_26_out, and_27_out, and_28_out, and_29_out, and_30_out, and_31_out, and_32_out,
       demultiplexer_1_out0, demultiplexer_1_out1, demultiplexer_1_out2, demultiplexer_1_out3,
       demultiplexer_2_out0, demultiplexer_2_out1, demultiplexer_2_out2, demultiplexer_2_out3,
       demultiplexer_2_out4, demultiplexer_2_out5, demultiplexer_2_out6, demultiplexer_2_out7,
       demultiplexer_3_out0, demultiplexer_3_out1, demultiplexer_3_out2, demultiplexer_3_out3,
       demultiplexer_3_out4, demultiplexer_3_out5, demultiplexer_3_out6, demultiplexer_3_out7,
       demultiplexer_4_out0, demultiplexer_4_out1, demultiplexer_4_out2, demultiplexer_4_out3,
       demultiplexer_4_out4, demultiplexer_4_out5, demultiplexer_4_out6, demultiplexer_4_out7,
       demultiplexer_5_out0, demultiplexer_5_out1, demultiplexer_5_out2, demultiplexer_5_out3,
       demultiplexer_5_out4, demultiplexer_5_out5, demultiplexer_5_out6, demultiplexer_5_out7;
  wire [31:0] register_1_q, register_2_q, register_3_q, register_4_q, register_5_q, register_6_q,
       register_7_q, register_8_q, register_9_q, register_10_q, register_11_q, register_12_q, register_13_q,
       register_14_q, register_15_q, register_16_q, register_17_q, register_18_q, register_19_q,
       register_20_q, register_21_q, register_22_q, register_23_q, register_24_q, register_25_q,
       register_26_q, register_27_q, register_28_q, register_29_q, register_30_q, register_31_q,
       register_32_q;

  Demultiplexer #(.select(2), .enable("false")) demultiplexer_1 (
    .out0(demultiplexer_1_out0), .out1(demultiplexer_1_out1), .out2(demultiplexer_1_out2),
    .out3(demultiplexer_1_out3), .in(Write_Enable), .sel(Write_Reg_num[4:3]));
  Demultiplexer #(.select(3), .enable("false")) demultiplexer_2 (
    .out0(demultiplexer_2_out0), .out1(demultiplexer_2_out1), .out2(demultiplexer_2_out2),
    .out3(demultiplexer_2_out3), .out4(demultiplexer_2_out4), .out5(demultiplexer_2_out5),
    .out6(demultiplexer_2_out6), .out7(demultiplexer_2_out7), .in(demultiplexer_1_out0),
    .sel(Write_Reg_num[2:0]));
  Register #(.width(32), .trigger("falling"), .Select("low")) register_1 (
    .D(Din), .en(and_1_out), .Q(register_1_q), .clk(Clock));  // open: clr
  and and_1 (and_1_out, Write_Enable, demultiplexer_2_out0);
  Register #(.width(32), .trigger("falling"), .Select("low")) register_2 (
    .D(Din), .en(and_2_out), .Q(register_2_q), .clk(Clock));  // open: clr
  and and_2 (and_2_out, Write_Enable, demultiplexer_2_out1);
  Register #(.width(32), .trigger("falling"), .Select("low")) register_3 (
    .D(Din), .en(and_3_out), .Q(register_3_q), .clk(Clock));  // open: clr
  and and_3 (and_3_out, Write_Enable, demultiplexer_2_out2);
  Register #(.width(32), .trigger("falling"), .Select("low")) register_4 (
    .D(Din), .en(and_4_out), .Q(register_4_q), .clk(Clock));  // open: clr
  and and_4 (and_4_out, Write_Enable, demultiplexer_2_out3);
  Register #(.width(32), .trigger("falling"), .Select("low")) register_5 (
    .D(Din), .en(and_5_out), .Q(register_5_q), .clk(Clock));  // open: clr
  and and_5 (and_5_out, Write_Enable, demultiplexer_2_out4);
  Register #(.width(32), .trigger("falling"), .Select("low")) register_6 (
    .D(Din), .en(and_6_out), .Q(register_6_q), .clk(Clock));  // open: clr
  and and_6 (and_6_out, Write_Enable, demultiplexer_2_out5);
  Register #(.width(32), .trigger("falling"), .Select("low")) register_7 (
    .D(Din), .en(and_7_out), .Q(register_7_q), .clk(Clock));  // open: clr
  and and_7 (and_7_out, Write_Enable, demultiplexer_2_out6);
  Register #(.width(32), .trigger("falling"), .Select("low")) register_8 (
    .D(Din), .en(and_8_out), .Q(register_8_q), .clk(Clock));  // open: clr
  and and_8 (and_8_out, Write_Enable, demultiplexer_2_out7);
  Demultiplexer #(.select(3), .enable("false")) demultiplexer_3 (
    .out0(demultiplexer_3_out0), .out1(demultiplexer_3_out1), .out2(demultiplexer_3_out2),
    .out3(demultiplexer_3_out3), .out4(demultiplexer_3_out4), .out5(demultiplexer_3_out5),
    .out6(demultiplexer_3_out6), .out7(demultiplexer_3_out7), .in(demultiplexer_1_out1),
    .sel(Write_Reg_num[2:0]));
  and and_9 (and_9_out, Write_Enable, demultiplexer_3_out0);
  and and_10 (and_10_out, Write_Enable, demultiplexer_3_out1);
  and and_11 (and_11_out, Write_Enable, demultiplexer_3_out2);
  and and_12 (and_12_out, Write_Enable, demultiplexer_3_out3);
  and and_13 (and_13_out, Write_Enable, demultiplexer_3_out4);
  and and_14 (and_14_out, Write_Enable, demultiplexer_3_out5);
  and and_15 (and_15_out, Write_Enable, demultiplexer_3_out6);
  and and_16 (and_16_out, Write_Enable, demultiplexer_3_out7);
  Demultiplexer #(.select(3), .enable("false")) demultiplexer_4 (
    .out0(demultiplexer_4_out0), .out1(demultiplexer_4_out1), .out2(demultiplexer_4_out2),
    .out3(demultiplexer_4_out3), .out4(demultiplexer_4_out4), .out5(demultiplexer_4_out5),
    .out6(demultiplexer_4_out6), .out7(demultiplexer_4_out7), .in(demultiplexer_1_out2),
    .sel(Write_Reg_num[2:0]));
  Register #(.width(32), .trigger("falling"), .Select("low")) register_9 (
    .D(Din), .en(and_9_out), .Q(register_9_q), .clk(Clock));  // open: clr
  Register #(.width(32), .trigger("falling"), .Select("low")) register_10 (
    .D(Din), .en(and_10_out), .Q(register_10_q), .clk(Clock));  // open: clr
  Register #(.width(32), .trigger("falling"), .Select("low")) register_11 (
    .D(Din), .en(and_11_out), .Q(register_11_q), .clk(Clock));  // open: clr
  Register #(.width(32), .trigger("falling"), .Select("low")) register_12 (
    .D(Din), .en(and_12_out), .Q(register_12_q), .clk(Clock));  // open: clr
  Register #(.width(32), .trigger("falling"), .Select("low")) register_13 (
    .D(Din), .en(and_13_out), .Q(register_13_q), .clk(Clock));  // open: clr
  Register #(.width(32), .trigger("falling"), .Select("low")) register_14 (
    .D(Din), .en(and_14_out), .Q(register_14_q), .clk(Clock));  // open: clr
  Register #(.width(32), .trigger("falling"), .Select("low")) register_15 (
    .D(Din), .en(and_15_out), .Q(register_15_q), .clk(Clock));  // open: clr
  Register #(.width(32), .trigger("falling"), .Select("low")) register_16 (
    .D(Din), .en(and_16_out), .Q(register_16_q), .clk(Clock));  // open: clr
  Register #(.width(32), .trigger("falling"), .Select("low")) register_17 (
    .D(Din), .en(and_17_out), .Q(register_17_q), .clk(Clock));  // open: clr
  and and_17 (and_17_out, Write_Enable, demultiplexer_4_out0);
  Register #(.width(32), .trigger("falling"), .Select("low")) register_18 (
    .D(Din), .en(and_18_out), .Q(register_18_q), .clk(Clock));  // open: clr
  and and_18 (and_18_out, Write_Enable, demultiplexer_4_out1);
  Register #(.width(32), .trigger("falling"), .Select("low")) register_19 (
    .D(Din), .en(and_19_out), .Q(register_19_q), .clk(Clock));  // open: clr
  and and_19 (and_19_out, Write_Enable, demultiplexer_4_out2);
  Register #(.width(32), .trigger("falling"), .Select("low")) register_20 (
    .D(Din), .en(and_20_out), .Q(register_20_q), .clk(Clock));  // open: clr
  and and_20 (and_20_out, Write_Enable, demultiplexer_4_out3);
  Register #(.width(32), .trigger("falling"), .Select("low")) register_21 (
    .D(Din), .en(and_21_out), .Q(register_21_q), .clk(Clock));  // open: clr
  and and_21 (and_21_out, Write_Enable, demultiplexer_4_out4);
  Register #(.width(32), .trigger("falling"), .Select("low")) register_22 (
    .D(Din), .en(and_22_out), .Q(register_22_q), .clk(Clock));  // open: clr
  and and_22 (and_22_out, Write_Enable, demultiplexer_4_out5);
  Register #(.width(32), .trigger("falling"), .Select("low")) register_23 (
    .D(Din), .en(and_23_out), .Q(register_23_q), .clk(Clock));  // open: clr
  and and_23 (and_23_out, Write_Enable, demultiplexer_4_out6);
  Register #(.width(32), .trigger("falling"), .Select("low")) register_24 (
    .D(Din), .en(and_24_out), .Q(register_24_q), .clk(Clock));  // open: clr
  and and_24 (and_24_out, Write_Enable, demultiplexer_4_out7);
  Demultiplexer #(.select(3), .enable("false")) demultiplexer_5 (
    .out0(demultiplexer_5_out0), .out1(demultiplexer_5_out1), .out2(demultiplexer_5_out2),
    .out3(demultiplexer_5_out3), .out4(demultiplexer_5_out4), .out5(demultiplexer_5_out5),
    .out6(demultiplexer_5_out6), .out7(demultiplexer_5_out7), .in(demultiplexer_1_out3),
    .sel(Write_Reg_num[2:0]));
  and and_25 (and_25_out, Write_Enable, demultiplexer_5_out0);
  and and_26 (and_26_out, Write_Enable, demultiplexer_5_out1);
  and and_27 (and_27_out, Write_Enable, demultiplexer_5_out2);
  and and_28 (and_28_out, Write_Enable, demultiplexer_5_out3);
  and and_29 (and_29_out, Write_Enable, demultiplexer_5_out4);
  and and_30 (and_30_out, Write_Enable, demultiplexer_5_out5);
  and and_31 (and_31_out, Write_Enable, demultiplexer_5_out6);
  and and_32 (and_32_out, Write_Enable, demultiplexer_5_out7);
  Register #(.width(32), .trigger("falling"), .Select("low")) register_25 (
    .D(Din), .en(and_25_out), .Q(register_25_q), .clk(Clock));  // open: clr
  Register #(.width(32), .trigger("falling"), .Select("low")) register_26 (
    .D(Din), .en(and_26_out), .Q(register_26_q), .clk(Clock));  // open: clr
  Register #(.width(32), .trigger("falling"), .Select("low")) register_27 (
    .D(Din), .en(and_27_out), .Q(register_27_q), .clk(Clock));  // open: clr
  Register #(.width(32), .trigger("falling"), .Select("low")) register_28 (
    .D(Din), .en(and_28_out), .Q(register_28_q), .clk(Clock));  // open: clr
  Register #(.width(32), .trigger("falling"), .Select("low")) register_29 (
    .D(Din), .en(and_29_out), .Q(register_29_q), .clk(Clock));  // open: clr
  Register #(.width(32), .trigger("falling"), .Select("low")) register_30 (
    .D(Din), .en(and_30_out), .Q(register_30_q), .clk(Clock));  // open: clr
  Register #(.width(32), .trigger("falling"), .Select("low")) register_31 (
    .D(Din), .en(and_31_out), .Q(register_31_q), .clk(Clock));  // open: clr
  Register #(.width(32), .trigger("falling"), .Select("low")) register_32 (
    .D(Din), .en(and_32_out), .Q(register_32_q), .clk(Clock));  // open: clr
  Multiplexer #(.select(5), .width(32), .enable("false")) multiplexer_1 (
    .in0(register_1_q), .in1(register_2_q), .in2(register_3_q), .in3(register_4_q), .in4(register_5_q),
    .in5(register_6_q), .in6(register_7_q), .in7(register_8_q), .in8(register_9_q), .in9(register_10_q),
    .in10(register_11_q), .in11(register_12_q), .in12(register_13_q), .in13(register_14_q),
    .in14(register_15_q), .in15(register_16_q), .in16(register_17_q), .in17(register_18_q),
    .in18(register_19_q), .in19(register_20_q), .in20(register_21_q), .in21(register_22_q),
    .in22(register_23_q), .in23(register_24_q), .in24(register_25_q), .in25(register_26_q),
    .in26(register_27_q), .in27(register_28_q), .in28(register_29_q), .in29(register_30_q),
    .in30(register_31_q), .in31(register_32_q), .out(Reg1Out), .sel(R1_num));
  Multiplexer #(.select(5), .width(32), .enable("false")) multiplexer_2 (
    .in0(register_1_q), .in1(register_2_q), .in2(register_3_q), .in3(register_4_q), .in4(register_5_q),
    .in5(register_6_q), .in6(register_7_q), .in7(register_8_q), .in8(register_9_q), .in9(register_10_q),
    .in10(register_11_q), .in11(register_12_q), .in12(register_13_q), .in13(register_14_q),
    .in14(register_15_q), .in15(register_16_q), .in16(register_17_q), .in17(register_18_q),
    .in18(register_19_q), .in19(register_20_q), .in20(register_21_q), .in21(register_22_q),
    .in22(register_23_q), .in23(register_24_q), .in24(register_25_q), .in25(register_26_q),
    .in26(register_27_q), .in27(register_28_q), .in28(register_29_q), .in29(register_30_q),
    .in30(register_31_q), .in31(register_32_q), .out(Reg2Out), .sel(R2_num));

  // Other names for the same wires on the sheet: CLK = Clock; RA[4:0] = R1_num; RB[4:0] = R2_num; RDA[31:0] = Reg1Out;
  //   RDB[31:0] = Reg2Out; RW[4:0] = Write_Reg_num; WE = Write_Enable

  // Notes on the sheet:
  //   000
  //   111
  //   输入引脚
  //   00
  //   电路功能：实现寄存器堆功能，实现0-31号寄存器。写使能有效且时钟边沿有效后写入数据，随时读出双口数据
  //   01
  //   输出引脚
  //   10
  //   11
endmodule

module \数据存储器  (
  input  [15:0] Addr,
  input  [31:0] Din,
  input  CLK,
  input  CLR,
  input  [2:0] MemOp,
  input  WE,
  input  SEL,
  output [31:0] DataOut
);

  wire and_1_out, and_2_out, and_3_out, and_4_out, and_5_out, and_6_out, and_7_out, or_1_out, or_2_out;
  wire [7:0] ram_1_data;
  wire [15:8] ram_2_data;
  wire [31:0] bit_extender_1_out, bit_extender_2_out, bit_extender_3_out, bit_extender_4_out;
  wire [31:16] ram_3_data;

  and and_1 (and_1_out, WE, or_1_out);
  or or_1 (or_1_out, and_2_out, and_3_out, and_4_out);
  and and_2 (and_2_out, ~MemOp[0], ~MemOp[1]);  // AND_Gate
  and and_3 (and_3_out, MemOp[0], ~MemOp[1]);  // AND_Gate
  and and_4 (and_4_out, ~MemOp[0], MemOp[1]);  // AND_Gate
  RAM #(.addrWidth(16), .bus("separate"), .Select("high"), .simpleMode("false")) ram_1 (
    .addr(Addr), .din(Din[7:0]), .data(ram_1_data), .str(and_1_out), .sel(SEL), .clk(CLK), .clr(CLR));  // open: ld
  assign bit_extender_1_out = {{16{1'b0}}, {ram_2_data, ram_1_data}};  // Bit_Extender bit_extender_1
  assign bit_extender_2_out = {{24{ram_1_data[7]}}, ram_1_data};  // Bit_Extender bit_extender_2
  and and_5 (and_5_out, WE, or_2_out);
  or or_2 (or_2_out, and_2_out, and_4_out);
  assign bit_extender_3_out = {{24{1'b0}}, ram_1_data};  // Bit_Extender bit_extender_3
  assign bit_extender_4_out = {{16{ram_2_data[15]}}, {ram_2_data, ram_1_data}};  // Bit_Extender bit_extender_4
  RAM #(.addrWidth(16), .bus("separate"), .Select("high"), .simpleMode("false")) ram_2 (
    .addr(Addr), .din(Din[15:8]), .data(ram_2_data), .str(and_5_out), .sel(SEL), .clk(CLK), .clr(CLR));  // open: ld
  and and_6 (and_6_out, WE, and_2_out);
  Multiplexer #(.select(3), .width(32), .enable("false")) multiplexer_1 (
    .in0({ram_3_data, ram_2_data, ram_1_data}), .in1(bit_extender_3_out), .in2(bit_extender_1_out),
    .in5(bit_extender_2_out), .in6(bit_extender_4_out), .out(DataOut), .sel(MemOp));  // open: in3, in4, in7
  RAM #(.addrWidth(16), .bus("separate"), .Select("high"), .simpleMode("false")) ram_3 (
    .addr(Addr), .din(Din[23:16]), .data(ram_3_data[23:16]), .str(and_6_out), .sel(SEL), .clk(CLK), .clr(CLR));  // open: ld
  and and_7 (and_7_out, WE, and_2_out);
  RAM #(.addrWidth(16), .bus("separate"), .Select("high"), .simpleMode("false")) ram_4 (
    .addr(Addr), .din(Din[31:24]), .data(ram_3_data[31:24]), .str(and_7_out), .sel(SEL), .clk(CLK), .clr(CLR));  // open: ld

  // Other names for the same wires on the sheet: Dout[31:0] = DataOut

  // Notes on the sheet:
  //   输入引脚区
  //   32位数据存储器，按字节分4片存储，可按照字节、半字和字进行存储；读取字节或半字时，支持0扩展和符号位扩展。
  //   为了后续实验中的引用，不要修改MemOp的编码定义，以及引脚名称和在布局图中位置。
  //   输出引脚区
endmodule

module DataPath (
  input  [2:0] ExtOp,
  input  [2:0] MemOp,
  input  RegWr,
  input  ALUASrc,
  input  MemWr,
  input  [1:0] ALUBSrc,
  input  [31:0] Initial_Address,
  input  [3:0] ALUctr,
  input  MemToReg,
  input  [2:0] Branch,
  input  Halt,
  output [6:0] OpCode,
  output [2:0] Funct3,
  output [6:0] Funct7
);

  wire alu_1_zero, branch_1_nxtasrc, branch_1_nxtbsrc, clk, RESET;
  wire [31:0] alu_1_s, idu_1_busa, idu_1_busb, idu_1_dataa, idu_1_datab, idu_1_imm, ifu_1_pc,
       multiplexer_1_out, \指令存储器_data , \数据存储器_1_dataout ;

  Clock clock_1 (.out(clk));
  Button u_Reset (.out(RESET));
  IFU ifu_1 (
    .PC(ifu_1_pc), .Initial_Address(Initial_Address), .BusA(idu_1_busa), .Halt(Halt),
    .NxtASrc(branch_1_nxtasrc), .NxtBSrc(branch_1_nxtbsrc), .Imm(idu_1_imm), .CLK(clk), .Reset(RESET));
  ROM #(.addrWidth(16), .dataWidth(32), .Select("high")) \u_指令存储器  (
    .addr(ifu_1_pc[17:2]), .data(\指令存储器_data ), .sel(1'b1));
  IDU idu_1 (
    .ExtOp(ExtOp), .RegWr(RegWr), .OpCode(OpCode), .ALUASrc(ALUASrc), .ALUBSrc(ALUBSrc), .Funct3(Funct3),
    .Funct7(Funct7), .IR(\指令存储器_data ), .BusW(multiplexer_1_out), .PC(ifu_1_pc), .DataA(idu_1_dataa),
    .BusB(idu_1_busb), .DataB(idu_1_datab), .Imm(idu_1_imm), .BusA(idu_1_busa));
  ALU alu_1 (.A(idu_1_dataa), .B(idu_1_datab), .S(alu_1_s), .ALUctr(ALUctr), .Zero(alu_1_zero));
  Branch branch_1 (
    .Branch(Branch), .NxtASrc(branch_1_nxtasrc), .Zero(alu_1_zero), .NxtBSrc(branch_1_nxtbsrc),
    .Result0(alu_1_s[0]));
  \数据存储器  \u_数据存储器_1  (
    .Addr(alu_1_s[17:2]), .Din(idu_1_busb), .DataOut(\数据存储器_1_dataout ), .CLK(clk), .CLR(1'b0),
    .MemOp(MemOp), .WE(MemWr), .SEL(1'b1));
  Multiplexer #(.width(32), .enable("false")) multiplexer_1 (
    .in0(alu_1_s), .in1(\数据存储器_1_dataout ), .out(multiplexer_1_out), .sel(MemToReg));

  // Other names for the same wires on the sheet: Init_Addr[31:0] = Initial_Address; op[6:0] = OpCode

  // Notes on the sheet:
  //   ALUASrc: pull=down
  //   Branch: pull=down
  //   ExtOp: pull=down
  //   Halt: pull=down
  //   ALUBSrc: pull=down
  //   ALUctr: pull=down
  //   RegWr: pull=down
  //   contents of 指令存储器 (hex, n*v repeats v):
  //   fffff2b7 6428293 502023 4032d313 602223 401383 fff3c413 802423 7424b3 902623 fc049ce3 3000567 a02823
  //   64597
  //   输入信号
  //   数据通路设计，提示指令存储器和数据存储器数据位32位，编址以字为单位，地址信号低2位舍弃。
  //   输出信号
endmodule

module Branch (
  input  [2:0] Branch,
  input  Zero,
  input  Result0,
  output NxtASrc,
  output NxtBSrc
);

  wire not_1_out, or_1_out;

  not not_1 (not_1_out, Zero);
  or or_1 (or_1_out, Zero, ~Result0);  // OR_Gate
  Multiplexer #(.select(3), .enable("false")) multiplexer_1 (
    .in0(1'b0), .in1(1'b0), .in2(1'b1), .in3(1'b0), .in4(1'b0), .in5(1'b0), .in6(1'b0), .in7(1'b0),
    .out(NxtASrc), .sel(Branch));
  Multiplexer #(.select(3), .enable("false")) multiplexer_2 (
    .in0(1'b0), .in1(1'b1), .in2(1'b1), .in3(1'b0), .in4(Zero), .in5(not_1_out), .in6(Result0),
    .in7(or_1_out), .out(NxtBSrc), .sel(Branch));

  // Notes on the sheet:
  //   Branch: pull=down
  //   Zero: pull=down
  //   输入信号
  //   输出信号
endmodule
