// Logisim project lab6（txy）.circ as structural Verilog: 2 circuits, main circuit 单周期CPU
module \单周期CPU  (
  input  [31:0] Initial_Address,
  output halt
);

  wire alu_1_zero, branch_1_nxtasrc, branch_1_nxtbsrc, clk, clock_2_out, Halt0, not_1_out, not_2_out,
       not_3_out, or_1_out, RESET, \控制器_1_aluasrc , \控制器_1_memtoreg , \控制器_1_memwr , \控制器_1_regwr ;
  wire [1:0] \控制器_1_alubsrc ;
  wire [2:0] idu_1_funct3, \控制器_1_branch , \控制器_1_extop , \控制器_1_memop ;
  wire [3:0] \控制器_1_aluctr ;
  wire [6:0] idu_1_funct7, idu_1_opcode;
  wire [15:0] alu_1_s_2, counter_1_q;
  wire [31:0] alu_1_s, idu_1_busa, idu_1_busb, idu_1_dataa, idu_1_datab, idu_1_imm, ifu_1_pc, IR,
       multiplexer_1_out, \数据存储器_1_dataout ;

  IFU ifu_1 (
    .PC(ifu_1_pc), .Initial_Address(Initial_Address), .BusA(idu_1_busa), .Halt(halt),
    .NxtASrc(branch_1_nxtasrc), .NxtBSrc(branch_1_nxtbsrc), .Imm(idu_1_imm), .CLK(clk), .Reset(RESET));
  not not_1 (not_1_out, RESET);
  Clock clock_1 (.out(clk));
  Button u_Reset (.out(RESET));
  ROM #(.addrWidth(16), .dataWidth(32), .Select("high")) \u_指令存储器  (.addr(ifu_1_pc[17:2]), .data(IR), .sel(not_1_out));
  \控制器  \u_控制器_1  (
    .funct3(idu_1_funct3), .opcode(idu_1_opcode), .Branch(\控制器_1_branch ), .MemOp(\控制器_1_memop ),
    .ALUASrc(\控制器_1_aluasrc ), .ALUBSrc(\控制器_1_alubsrc ), .ALUctr(\控制器_1_aluctr ),
    .MemtoReg(\控制器_1_memtoreg ), .RegWr(\控制器_1_regwr ), .MemWr(\控制器_1_memwr ), .ExtOp(\控制器_1_extop ),
    .funct7(idu_1_funct7), .halt(halt));
  IDU idu_1 (
    .ExtOp(\控制器_1_extop ), .RegWr(\控制器_1_regwr ), .OpCode(idu_1_opcode), .ALUASrc(\控制器_1_aluasrc ),
    .ALUBSrc(\控制器_1_alubsrc ), .Funct3(idu_1_funct3), .Funct7(idu_1_funct7), .IR(IR),
    .BusW(multiplexer_1_out), .PC(ifu_1_pc), .DataA(idu_1_dataa), .BusB(idu_1_busb), .DataB(idu_1_datab),
    .Imm(idu_1_imm), .BusA(idu_1_busa));
  ALU alu_1 (
    .A(idu_1_dataa), .B(idu_1_datab), .S({alu_1_s[31:18], alu_1_s_2, alu_1_s[1:0]}), .ALUctr(\控制器_1_aluctr ),
    .Zero(alu_1_zero));
  not not_2 (not_2_out, RESET);
  or or_1 (or_1_out, halt, Halt0);
  Comparator #(.width(32)) comparator_1 (.a(IR), .b(32'h6f), .eq(Halt0));  // open: gt, lt
  Counter #(.width(16), .max('hffff), .behavior("old")) counter_1 (
    .count(not_3_out), .Q(counter_1_q), .clk(clock_2_out), .clr(RESET));  // open: load, D, carry, preset
  // Probe on counter_1_q
  not not_3 (not_3_out, or_1_out);
  Clock clock_2 (.out(clock_2_out));
  Branch branch_1 (
    .Branch(\控制器_1_branch ), .NxtASrc(branch_1_nxtasrc), .Zero(alu_1_zero), .NxtBSrc(branch_1_nxtbsrc),
    .Result0(alu_1_s[0]));
  \数据存储器  \u_数据存储器_1  (
    .Addr(alu_1_s_2), .Din(idu_1_busb), .DataOut(\数据存储器_1_dataout ), .CLK(clk), .CLR(RESET),
    .MemOp(\控制器_1_memop ), .WE(\控制器_1_memwr ), .SEL(not_2_out));
  Multiplexer #(.width(32), .enable("false")) multiplexer_1 (
    .in0({alu_1_s[31:18], alu_1_s_2, alu_1_s[1:0]}), .in1(\数据存储器_1_dataout ), .out(multiplexer_1_out),
    .sel(\控制器_1_memtoreg ));

  // Other names for the same wires on the sheet: Init_Addr[31:0] = Initial_Address

  // Notes on the sheet:
  //   取指令部件
  //   输入信号
  //   RV32I单周期CPU设计
  //   contents of 指令存储器 (hex, n*v repeats v):
  //   2503 100593 50633 586b3 269713 72803 472883 108f663 1172023 1072223 b686b3 fec6e2e3 40b60633
  //   fcb61ce3 6f
  //   输出信号
  //   数据通路
  //   ALU
  //   数据存储器
  //   程序执行周期数
endmodule

module \控制器  (
  input  [6:0] opcode,
  input  [2:0] funct3,
  input  [6:0] funct7,
  output [2:0] ExtOp,
  output RegWr,
  output ALUASrc,
  output [1:0] ALUBSrc,
  output [3:0] ALUctr,
  output [2:0] Branch,
  output MemtoReg,
  output [2:0] MemOp,
  output MemWr,
  output halt
);

  wire and_1_out, and_2_out, and_3_out, and_4_out, and_5_out, and_6_out, and_7_out, B_Instr, comparator_3_eq,
       comparator_4_eq, I_Arith, J_jalr, or_1_out, or_6_out, or_9_out, R_Arith, U_auipc, U_lui;
  wire [2:0] multiplexer_1_out;

  Comparator #(.width(7)) comparator_1 (.a(opcode), .b(7'b0110111), .eq(U_lui));  // open: gt, lt
  Comparator #(.width(7)) comparator_2 (.a(opcode), .b(7'b1100111), .eq(J_jalr));  // open: gt, lt
  Comparator #(.width(3)) comparator_3 (.a(funct3), .b(3'b000), .eq(comparator_3_eq));  // open: gt, lt
  Comparator #(.width(3)) comparator_4 (.a(funct3), .b(3'b101), .eq(comparator_4_eq));  // open: gt, lt
  Comparator #(.width(7)) comparator_5 (.a(opcode), .b(7'b0010111), .eq(U_auipc));  // open: gt, lt
  Comparator #(.width(7)) comparator_6 (.a(opcode), .b(7'b1100011), .eq(B_Instr));  // open: gt, lt
  or or_1 (or_1_out, comparator_3_eq, comparator_4_eq);
  and and_1 (and_1_out, comparator_4_eq, I_Arith);
  Multiplexer #(.select(3), .width(3), .enable("false")) multiplexer_1 (
    .in0(3'b100), .in1(3'b101), .in4(3'b110), .in5(3'b111), .in6(3'b110), .in7(3'b111),
    .out(multiplexer_1_out), .sel(funct3));  // open: in2, in3
  Comparator #(.width(7)) comparator_7 (.a(opcode), .b(7'b0010011), .eq(I_Arith));  // open: gt, lt
  Comparator #(.width(7)) comparator_8 (.a(opcode), .b(7'b0000011), .eq(MemtoReg));  // open: gt, lt
  Comparator #(.width(7)) comparator_9 (.a(opcode), .b(7'b0110011), .eq(R_Arith));  // open: gt, lt
  Comparator #(.width(7)) comparator_10 (.a(opcode), .b(7'b0100011), .eq(MemWr));  // open: gt, lt
  or or_2 (ALUBSrc[1], U_lui, U_auipc, I_Arith, MemtoReg, MemWr);
  or or_3 (ALUBSrc[0], ExtOp[2], J_jalr);
  or or_4 (ExtOp[0], U_lui, U_auipc, B_Instr);
  or or_5 (ExtOp[1], B_Instr, MemWr);
  and and_2 (and_2_out, or_1_out, R_Arith);
  or or_6 (or_6_out, I_Arith, R_Arith);
  or or_7 (RegWr, U_lui, U_auipc, ExtOp[2], J_jalr, I_Arith, R_Arith, MemtoReg);
  or or_8 (ALUASrc, U_auipc, ExtOp[2], J_jalr);
  Multiplexer #(.width(3), .enable("false")) multiplexer_2 (
    .in0({1'b0, J_jalr, ExtOp[2]}), .in1(multiplexer_1_out), .out(Branch), .sel(B_Instr));
  or or_9 (or_9_out, and_2_out, and_1_out);
  and and_3 (and_3_out, or_6_out, funct3[2]);
  and and_4 (and_4_out, or_6_out, funct3[1]);
  and and_5 (and_5_out, or_6_out, funct3[0]);
  and and_6 (and_6_out, B_Instr, funct3[1], funct3[2]);
  Comparator #(.width(7)) comparator_11 (.a(opcode), .b(7'b1101111), .eq(ExtOp[2]));  // open: gt, lt
  Comparator #(.width(7)) comparator_12 (.a(opcode), .b({7{1'b0}}), .eq(halt));  // open: gt, lt
  or or_10 (ALUctr[3], U_lui, and_7_out);
  and and_7 (and_7_out, funct7[5], or_9_out);
  or or_11 (ALUctr[2], U_lui, and_3_out);
  or or_12 (ALUctr[1], U_lui, B_Instr, and_4_out);
  or or_13 (ALUctr[0], U_lui, and_5_out, and_6_out);
  Multiplexer #(.select(3), .width(3), .enable("false")) multiplexer_3 (
    .in0(3'b101), .in1(3'b110), .in2(3'b000), .in4(3'b001), .in5(3'b010), .out(MemOp), .sel(funct3));  // open: in3, in6, in7

  // Other names for the same wires on the sheet: J_jal = ExtOp[2]; I_load = MemtoReg; S_Instr = MemWr

  // Notes on the sheet:
  //   输入信号
  //   提示：根据指令种类和代码，把7位指令code用一位标志位来表示。
  //   输出信号
endmodule
