// Logisim project lab6.circ as structural Verilog: 2 circuits, main circuit 单周期CPU
module \单周期CPU  (
  input  [31:0] Initial_Address,
  output halt
);

  wire ALU_zero, ALUASrc, bit_extender_1_out, Branch_nxtasrc, Branch_nxtbsrc, clk, clock_2_out, Halt0,
       MemToReg, MemWr, not_1_out, not_2_out, or_1_out, RegWr, RESET;
  wire [1:0] ALUBSrc;
  wire [2:0] Branch, ExtOp, funct3, MemOp;
  wire [3:0] ALUctr;
  wire [6:0] funct7, op;
  wire [15:0] ALU_s_2, counter_1_q;
  wire [31:0] ALU_s, idu_1_busa, idu_1_busb, idu_1_dataa, idu_1_datab, idu_1_imm, ifu_1_pc, IR,
       multiplexer_1_out, \数据存储器_dataout ;

  IFU ifu_1 (
    .PC(ifu_1_pc), .Initial_Address(Initial_Address), .BusA(idu_1_busa), .Halt(halt),
    .NxtASrc(Branch_nxtasrc), .NxtBSrc(Branch_nxtbsrc), .Imm(idu_1_imm), .CLK(clk), .Reset(RESET));
  not not_1 (not_1_out, RESET);
  Clock clock_1 (.out(clk));
  Button u_Reset (.out(RESET));
  // Probe on ifu_1_pc
  ROM #(.addrWidth(16), .dataWidth(32), .Select("high")) \u_指令存储器  (.addr(ifu_1_pc[17:2]), .data(IR), .sel(not_1_out));
  \控制器  \u_控制器_1  (
    .funct3(funct3), .opcode(op), .Branch(Branch), .MemOp(MemOp), .ALUASrc(ALUASrc), .ALUBSrc(ALUBSrc),
    .ALUctr(ALUctr), .MemtoReg(MemToReg), .RegWr(RegWr), .MemWr(MemWr), .ExtOp(ExtOp), .funct7(funct7),
    .halt(halt));
  // Probe on multiplexer_1_out
  IDU idu_1 (
    .ExtOp(ExtOp), .RegWr(RegWr), .OpCode(op), .ALUASrc(ALUASrc), .ALUBSrc(ALUBSrc), .Funct3(funct3),
    .Funct7(funct7), .IR(IR), .BusW(multiplexer_1_out), .PC(ifu_1_pc), .DataA(idu_1_dataa),
    .BusB(idu_1_busb), .DataB(idu_1_datab), .Imm(idu_1_imm), .BusA(idu_1_busa), .CLK(clk));
  or or_1 (or_1_out, halt, Halt0);
  // Probe on idu_1_imm
  // Probe on idu_1_busb
  Comparator #(.width(32)) comparator_1 (.a(IR), .b(32'h6f), .eq(Halt0));  // open: gt, lt
  Counter #(.width(16), .max('hffff), .behavior("old")) counter_1 (
    .count(not_2_out), .Q(counter_1_q), .clk(clock_2_out), .clr(RESET));  // open: load, D, carry, preset
  // Probe on counter_1_q
  not not_2 (not_2_out, or_1_out);
  Clock clock_2 (.out(clock_2_out));
  ALU ALU (.A(idu_1_dataa), .B(idu_1_datab), .S({ALU_s[31:18], ALU_s_2, ALU_s[1:0]}), .ALUctr(ALUctr), .Zero(ALU_zero));
  Branch u_Branch (
    .Branch(Branch), .NxtASrc(Branch_nxtasrc), .Zero(ALU_zero), .NxtBSrc(Branch_nxtbsrc),
    .Result0(bit_extender_1_out));
  Multiplexer #(.width(32), .enable("false")) multiplexer_1 (
    .in0({ALU_s[31:18], ALU_s_2, ALU_s[1:0]}), .in1(\数据存储器_dataout ), .out(multiplexer_1_out), .sel(MemToReg));
  \数据存储器  \u_数据存储器  (
    .Addr(ALU_s_2), .Din(idu_1_busb), .DataOut(\数据存储器_dataout ), .CLK(clk), .CLR(RESET), .MemOp(MemOp),
    .WE(MemWr), .SEL(not_1_out));
  Bit_Extender #(.in_width(32), .out_width(1), .\type ("sign")) bit_extender_1 (
    .in({ALU_s[31:18], ALU_s_2, ALU_s[1:0]}), .out(bit_extender_1_out));

  // Other names for the same wires on the sheet: Init_Addr[31:0] = Initial_Address

  // Notes on the sheet:
  //   输入信号
  //   RV32I单周期CPU设计
  //   contents of 指令存储器 (hex, n*v repeats v):
  //   2503 100613 6b3 c686b3 a60663 160613 ff5ff06f d02423 6f
  //   输出信号
  //   程序执行周期数
endmodule

module \控制器  (
  input  [6:0] opcode,
  input  [2:0] funct3,
  input  [6:0] funct7,
  output [2:0] ExtOp,
  output RegWr,
  output ALUASrc,
  output [1:0] ALUBSrc,
  output [3:0] ALUctr,
  output [2:0] Branch,
  output MemtoReg,
  output [2:0] MemOp,
  output MemWr,
  output halt
);

  wire and_1_out, and_2_out, and_3_out, and_4_out, and_5_out, and_6_out, and_7_out, and_8_out, and_9_out,
       and_10_out, and_11_out, and_12_out, and_13_out, and_17_out, and_18_out, I_Arith, J_jalr, or_1_out,
       or_7_out, or_8_out, or_9_out, R_Arith, U_auipc, U_lui, xnor_1_out;

  Comparator #(.width(7)) comparator_1 (.a(opcode), .b(7'b0110111), .eq(U_lui));  // open: gt, lt
  Comparator #(.width(7)) comparator_2 (.a(opcode), .b(7'b1100111), .eq(J_jalr));  // open: gt, lt
  and and_1 (and_1_out, Branch[2], funct3[0], ~funct3[1], ~funct3[2]);  // AND_Gate
  or or_1 (or_1_out, MemtoReg, MemWr);
  and and_2 (and_2_out, R_Arith, funct7[4]);
  xnor xnor_1 (xnor_1_out, funct3[0], funct3[1]);
  and and_3 (and_3_out, funct3[0], ~funct3[1]);  // AND_Gate
  and and_4 (and_4_out, ~funct3[1], ~funct3[2]);  // AND_Gate
  Comparator #(.width(7)) comparator_3 (.a(opcode), .b(7'b0010111), .eq(U_auipc));  // open: gt, lt
  Comparator #(.width(7)) comparator_4 (.a(opcode), .b(7'b1100011), .eq(Branch[2]));  // open: gt, lt
  and and_5 (and_5_out, Branch[2], funct3[0], ~funct3[1], funct3[2]);  // AND_Gate
  and and_6 (and_6_out, I_Arith, funct3[0]);
  and and_7 (and_7_out, R_Arith, funct3[0]);
  and and_8 (and_8_out, Branch[2], funct3[1]);
  and and_9 (and_9_out, I_Arith, funct3[1]);
  and and_10 (and_10_out, R_Arith, funct3[1]);
  and and_11 (and_11_out, I_Arith, funct3[2]);
  and and_12 (and_12_out, R_Arith, funct3[2]);
  and and_13 (and_13_out, I_Arith, funct3[0], ~funct3[1], funct3[2], funct7[4]);  // AND_Gate
  and and_14 (MemOp[0], or_1_out, xnor_1_out);
  and and_15 (MemOp[1], or_1_out, and_3_out);
  and and_16 (MemOp[2], or_1_out, and_4_out);
  Comparator #(.width(7)) comparator_5 (.a(opcode), .b(7'b0010011), .eq(I_Arith));  // open: gt, lt
  Comparator #(.width(7)) comparator_6 (.a(opcode), .b(7'b0000011), .eq(MemtoReg));  // open: gt, lt
  and and_17 (and_17_out, Branch[2], funct3[0], funct3[1], funct3[2]);
  and and_18 (and_18_out, funct3[2], Branch[2]);
  or or_2 (ALUctr[0], U_lui, and_6_out, and_7_out, and_8_out);
  or or_3 (ALUctr[1], U_lui, and_9_out, and_10_out, Branch[2]);
  or or_4 (ALUctr[2], U_lui, and_11_out, and_12_out);
  or or_5 (ALUctr[3], U_lui, and_13_out, and_2_out);
  Comparator #(.width(7)) comparator_7 (.a(opcode), .b(7'b0110011), .eq(R_Arith));  // open: gt, lt
  Comparator #(.width(7)) comparator_8 (.a(opcode), .b(7'b0100011), .eq(MemWr));  // open: gt, lt
  or or_6 (Branch[1], J_jalr, and_18_out);
  or or_7 (or_7_out, U_lui, U_auipc);
  or or_8 (or_8_out, ExtOp[2], J_jalr);
  or or_9 (or_9_out, I_Arith, R_Arith);
  or or_10 (ALUASrc, U_auipc, ExtOp[2], J_jalr);
  or or_11 (ALUBSrc[0], ExtOp[2], J_jalr);
  or or_12 (ALUBSrc[1], U_lui, U_auipc, I_Arith, MemWr, MemtoReg);
  or or_13 (ExtOp[0], U_lui, U_auipc, Branch[2]);
  or or_14 (ExtOp[1], Branch[2], MemWr);
  or or_15 (Branch[0], ExtOp[2], and_17_out, and_5_out, and_1_out);
  Comparator #(.width(7)) comparator_9 (.a(opcode), .b(7'b1101111), .eq(ExtOp[2]));  // open: gt, lt
  Comparator #(.width(7)) comparator_10 (.a(opcode), .b({7{1'b0}}), .eq(halt));  // open: gt, lt
  or or_16 (RegWr, or_7_out, or_8_out, or_9_out, MemtoReg);

  // Other names for the same wires on the sheet: B_Instr = Branch[2]; J_jal = ExtOp[2]; I_load = MemtoReg;
  //   S_Instr = MemWr

  // Notes on the sheet:
  //   输入信号
  //   提示：根据指令种类和代码，把7位指令code用一位标志位来表示。
  //   输出信号
endmodule
